// Logisim project cpu21-riscv.circ as structural Verilog: 24 circuits, main circuit ◇单周期RISC-V
module \单周期RISC_V  (
  input  IR1,
  input  IR2,
  input  IR3,
  output RegWrite,
  output MemWrite,
  output [31:0] PC,
  output [31:0] IR,
  output [31:0] RDin,
  output [31:0] MDin,
  output [31:0] LedData
);

  wire alu_1_equal, alu_1_out_4, and_1_out, and_3_out, and_4_out, and_5_out, B, CLK, clock_1_out,
       comparator_1_eq, comparator_2_eq, comparator_2_lt, d_ff_1_q, ecall, Go, halt, IR1_t, IR2_t, IR3_t,
       IRA, IRB, IRC, jmp, nand_1_out, not_1_out, not_2_out, not_3_out, not_4_out, or_1_out,
       riscv_probe_1_p2, RST, sb, W1, W2, W3, \单周期硬布线控制器_1_alu_src , \单周期硬布线控制器_1_beq , \单周期硬布线控制器_1_bgeu ,
       \单周期硬布线控制器_1_bne , \单周期硬布线控制器_1_jal , \单周期硬布线控制器_1_jalr , \单周期硬布线控制器_1_lui , \单周期硬布线控制器_1_memtoreg ,
       \单周期硬布线控制器_1_s_type ;
  wire [0:0] adder_2_out;
  wire [1:0] priority_encoder_1_out, priority_encoder_2_out;
  wire [3:0] decoder_1_out0, multiplexer_7_out, \单周期硬布线控制器_1_alu_op ;
  wire [4:0] multiplexer_2_out, multiplexer_3_out;
  wire [11:0] multiplexer_4_out;
  wire [12:0] CNT_num;
  wire [15:0] \总周期数 ;
  wire [31:0] ALUout, B_dest, bit_extender_1_out, bit_extender_2_out, bit_extender_3_out, bit_extender_4_out,
       bit_extender_5_out, J_dest, mips_ram_1_p7, multiplexer_1_out, multiplexer_5_out, PC_4, R1, R2, sbdata,
       shifter_1_out, shifter_2_out, shifter_4_out, shifter_5_out, shifter_6_out, ui;
  wire [31:1] I_dest;

  Button \u_继续运行  (.out(Go));
  Button _1 (.out(IRA));
  Button _2 (.out(IRB));
  Button _3 (.out(IRC));
  not not_1 (not_1_out, halt);
  LED #(.active("true")) led_1 (.in(W1));
  LED #(.active("true")) led_2 (.in(W2));
  LED #(.active("true")) led_3 (.in(W3));
  Priority_Encoder #(.select(2), .disabled("Z")) priority_encoder_1 (
    .in0(1'b1), .in1(\单周期硬布线控制器_1_jal ), .in2(\单周期硬布线控制器_1_jalr ), .in3(B), .out(priority_encoder_1_out));  // open: gs, en_out, en_in
  Multiplexer #(.select(2), .width(32), .disabled("Z"), .enable("false")) multiplexer_1 (
    .in0(PC_4), .in1(J_dest), .in2({I_dest, 1'b0}), .in3(B_dest), .out(multiplexer_1_out),
    .sel(priority_encoder_1_out));
  or or_1 (or_1_out, Go, not_1_out);
  Hex_Digit_Display hex_digit_display_1 (.value(LedData[31:28]));  // open: dp
  or or_2 (jmp, \单周期硬布线控制器_1_jalr , \单周期硬布线控制器_1_jal );
  Register #(.width(32), .trigger("rising"), .Select("low")) u_PC (
    .D(multiplexer_1_out), .en(or_1_out), .Q(PC), .clk(CLK), .clr(RST));
  not not_2 (not_2_out, comparator_1_eq);
  Comparator #(.width(32), .mode("unsigned")) comparator_1 (.a(R2), .b(32'h22), .eq(comparator_1_eq));  // open: gt, lt
  Hex_Digit_Display hex_digit_display_2 (.value(LedData[27:24]));  // open: dp
  Hex_Digit_Display hex_digit_display_3 (.value(LedData[23:20]));  // open: dp
  Adder #(.width(32)) adder_1 (.a(PC), .b(32'h4), .out(PC_4));  // open: cin, cout
  and and_1 (and_1_out, ecall, comparator_1_eq);
  and and_2 (halt, ecall, not_2_out);
  not not_3 (not_3_out, halt);
  Counter #(.width(16), .max('hffff), .ongoal("wrap"), .trigger("rising"), .behavior("new")) counter_1 (
    .count(not_3_out), .Q(\总周期数 ), .clk(CLK));  // open: load, D, carry, clr, preset, down
  Hex_Digit_Display hex_digit_display_4 (.value(LedData[15:12]));  // open: dp
  Hex_Digit_Display hex_digit_display_5 (.value(LedData[19:16]));  // open: dp
  // RiscV_Probe riscv_probe_1: pin names not known; wires that end beside it: IR, riscv_probe_1_p2
  Register #(.width(32), .trigger("rising"), .Select("low")) register_1 (
    .D(R1), .en(and_1_out), .Q(LedData), .clk(CLK));  // open: clr
  Hex_Digit_Display hex_digit_display_6 (.value(LedData[11:8]));  // open: dp
  Hex_Digit_Display hex_digit_display_7 (.value(LedData[7:4]));  // open: dp
  // Probe on \总周期数 
  ROM #(.addrWidth(10), .dataWidth(32), .Select("high")) rom_1 (.addr(PC[11:2]), .data(IR));
  Hex_Digit_Display hex_digit_display_8 (.value(LedData[3:0]));  // open: dp
  \单周期硬布线控制器  \u_单周期硬布线控制器_1  (
    .Funct({IR[30], IR[25], IR[14:12]}), .OP(IR[6:2]), .ALU_OP(\单周期硬布线控制器_1_alu_op ),
    .MemToReg(\单周期硬布线控制器_1_memtoreg ), .MemWrite(MemWrite), .ALU_SRC(\单周期硬布线控制器_1_alu_src ),
    .RegWrite(RegWrite), .ecall(ecall), .S_type(\单周期硬布线控制器_1_s_type ), .Beq(\单周期硬布线控制器_1_beq ),
    .JAL(\单周期硬布线控制器_1_jal ), .Bne(\单周期硬布线控制器_1_bne ), .in_3(IR[21]), .uret(riscv_probe_1_p2),
    .Jalr(\单周期硬布线控制器_1_jalr ), .LUI(\单周期硬布线控制器_1_lui ), .SB(sb), .BGEU(\单周期硬布线控制器_1_bgeu ));  // open: CSRRSI, CSRRCI
  Multiplexer #(.select(1), .width(5), .disabled("Z"), .enable("false")) multiplexer_2 (
    .in0(IR[19:15]), .in1(5'b01010), .out(multiplexer_2_out), .sel(ecall));
  Multiplexer #(.select(1), .width(5), .disabled("Z"), .enable("false")) multiplexer_3 (
    .in0(IR[24:20]), .in1(5'b10001), .out(multiplexer_3_out), .sel(ecall));
  or or_3 (IR1_t, IR1, IRA);
  Multiplexer #(.select(1), .width(12), .disabled("Z"), .enable("false")) multiplexer_4 (
    .in0(IR[31:20]), .in1({IR[31:25], IR[11:7]}), .out(multiplexer_4_out), .sel(\单周期硬布线控制器_1_s_type ));
  assign bit_extender_1_out = {{20{IR[31]}}, {IR[31], IR[7], IR[30:25], IR[11:8]}};  // Bit_Extender bit_extender_1
  assign bit_extender_2_out = {{12{IR[31]}}, {IR[31], IR[19:12], IR[20], IR[30:21]}};  // Bit_Extender bit_extender_2
  assign bit_extender_3_out = {{12{IR[31]}}, IR[31:12]};  // Bit_Extender bit_extender_3
  or or_4 (IR2_t, IR2, IRB);
  Regifile regifile_1 (
    .Din(RDin), .Clk(CLK), .R1(R1), .R2(R2), .WE(RegWrite), .W_num(IR[11:7]), .R1_num(multiplexer_2_out),
    .R2_num(multiplexer_3_out));
  assign bit_extender_4_out = {{20{multiplexer_4_out[11]}}, multiplexer_4_out};  // Bit_Extender bit_extender_4
  Shifter #(.width(32), .shift("ll")) shifter_1 (.in(bit_extender_1_out), .\dist (5'b00001), .out(shifter_1_out));
  Shifter #(.width(32), .shift("ll")) shifter_2 (.in(bit_extender_2_out), .\dist (5'b00001), .out(shifter_2_out));
  Shifter #(.width(32), .shift("ll")) shifter_3 (.in(bit_extender_3_out), .\dist (5'b01100), .out(ui));
  Adder #(.width(32)) adder_2 (.a(bit_extender_4_out), .b(R1), .out({I_dest, adder_2_out[0]}));  // open: cin, cout
  Adder #(.width(32)) adder_3 (.a(shifter_1_out), .b(PC), .out(B_dest));  // open: cin, cout
  Adder #(.width(32)) adder_4 (.a(shifter_2_out), .b(PC), .out(J_dest));  // open: cin, cout
  or or_5 (IR3_t, IR3, IRC);
  Multiplexer #(.select(1), .width(32), .disabled("Z"), .enable("false")) multiplexer_5 (
    .in0(R2), .in1(bit_extender_4_out), .out(multiplexer_5_out), .sel(\单周期硬布线控制器_1_alu_src ));
  and and_3 (and_3_out, \单周期硬布线控制器_1_beq , alu_1_equal);
  and and_4 (and_4_out, \单周期硬布线控制器_1_bne , not_4_out);
  not not_4 (not_4_out, alu_1_equal);
  and and_5 (and_5_out, \单周期硬布线控制器_1_bgeu , alu_1_out_4);
  ALU alu_1 (
    .X(R1), .Y(multiplexer_5_out), .AluOP(\单周期硬布线控制器_1_alu_op ), .Equal(alu_1_equal), .Result(ALUout),
    .out_4(alu_1_out_4));  // open: Result_2, out_6
  Multiplexer #(.select(1), .width(32), .disabled("Z"), .enable("false")) multiplexer_6 (
    .in0(R2), .in1(sbdata), .out(MDin), .sel(sb));
  or or_6 (B, and_3_out, and_4_out, and_5_out);
  Decoder #(.select(2), .tristate("false"), .disabled("Z"), .enable("false")) decoder_1 (
    .out0(decoder_1_out0[0]), .out1(decoder_1_out0[1]), .out2(decoder_1_out0[2]), .out3(decoder_1_out0[3]),
    .sel(ALUout[1:0]));
  assign bit_extender_5_out = {{24{1'b0}}, R2[7:0]};  // Bit_Extender bit_extender_5
  Multiplexer #(.select(1), .width(4), .disabled("Z"), .enable("false")) multiplexer_7 (
    .in0(4'b1111), .in1(decoder_1_out0), .out(multiplexer_7_out), .sel(sb));
  Shifter #(.width(32), .shift("ll")) shifter_4 (.in(bit_extender_5_out), .\dist (5'b01000), .out(shifter_4_out));
  Shifter #(.width(32), .shift("ll")) shifter_5 (.in(bit_extender_5_out), .\dist (5'b10000), .out(shifter_5_out));
  Shifter #(.width(32), .shift("ll")) shifter_6 (.in(bit_extender_5_out), .\dist (5'b11000), .out(shifter_6_out));
  // MIPS_RAM mips_ram_1: pin names not known; wires that end beside it: ALUout[11:2], MDin, MemWrite, multiplexer_7_out, CLK, 1'b1, mips_ram_1_p7
  Multiplexer #(.select(2), .width(32), .disabled("Z"), .enable("false")) multiplexer_8 (
    .in0(bit_extender_5_out), .in1(shifter_4_out), .in2(shifter_5_out), .in3(shifter_6_out), .out(sbdata),
    .sel(ALUout[1:0]));
  D_Flip_Flop #(.trigger("high"), .Pre_Clr_Positions("LEGACY"), .NegatePresetClear("false"), .enable("true"), .NewFFLayout("false")) d_ff_1 (.Q(d_ff_1_q));  // open: clk, D, Qn, preset, en, reset
  // Probe on 13'hc
  Priority_Encoder #(.select(2), .disabled("Z")) priority_encoder_2 (
    .in0(1'b1), .in1(\单周期硬布线控制器_1_memtoreg ), .in2(jmp), .in3(\单周期硬布线控制器_1_lui ), .out(priority_encoder_2_out));  // open: gs, en_out, en_in
  Multiplexer #(.select(2), .width(32), .disabled("Z"), .enable("false")) multiplexer_9 (
    .in0(ALUout), .in1(mips_ram_1_p7), .in2(PC_4), .in3(ui), .out(RDin), .sel(priority_encoder_2_out));
  Comparator #(.width(13), .mode("twosComplement")) comparator_2 (
    .a(CNT_num), .b(13'hc), .eq(comparator_2_eq), .lt(comparator_2_lt));  // open: gt
  Clock #(.highDuration(1), .lowDuration(1)) clock_1 (.out(clock_1_out));
  Counter #(.width(13), .max('h1fff), .ongoal("stay"), .trigger("rising"), .behavior("old")) counter_2 (
    .count(comparator_2_lt), .Q(CNT_num), .clk(clock_1_out));  // open: load, D, carry, clr, preset
  nand nand_1 (nand_1_out, d_ff_1_q, comparator_2_eq);
  assign CLK = nand_1_out ? clock_1_out : 1'bz;  // Controlled_Buffer controlled_buffer_1
  Pull_Resistor #(.pull(1)) pull_resistor_1 (.node(CLK));

  // Other names for the same wires on the sheet: byte[1:0] = ALUout[1:0]

  // Notes on the sheet:
  //   中断源
  //   中断等待指示
  //   数码管输出应该用寄存器锁存，否则显示数据只能一闪而过
  //   数码管输出
  //   指令探针
  //   指令存储器
  //   指令字
  //   contents of rom_1 (hex, n*v repeats v):
  //   100493 100006f 100493 200913 300993 100006f 100493 200913 300993 100006f 100493 200913 300993
  //   100006f 100493 200913 300993 3bc000ef 100413 100493 1f49493 900533 2200893 73 24d493 48463 fedff06f
  //   900533 2200893 73 100493 249493 900533 2200893 73 48463 fedff06f 100493 1f49493 900533 2200893 73
  //   4034d493 900533 2200893 73 4044d493 900533 2200893 73 4044d493 900533 2200893 73 4044d493 900533
  //   2200893 73 4044d493 900533 2200893 73 4044d493 900533 2200893 73 4044d493 900533 2200893 73 4044d493
  //   900533 2200893 73 100413 1f41993 41f9d993 433 c00913 300b13 140413 f47413 800293 100313 499993
  //   89e9b3 1300533 2200893 73 406282b3 fe0294e3 140413 f00f93 1f47433 1c41413 800293 100313 49d993
  //   89e9b3 1300533 2200893 73 406282b3 fe0294e3 1c45413 406b0b33 b0463 f95ff06f 2b3 fff2c293 829293
  //   ff2e293 500533 2200893 73 fff00413 493 84a023 140413 448493 84a023 140413 448493 84a023 140413
  //   448493 84a023 140413 448493 84a023 140413 448493 84a023 140413 448493 84a023 140413 448493 84a023
  //   140413 448493 84a023 140413 448493 84a023 140413 448493 84a023 140413 448493 84a023 140413 448493
  //   84a023 140413 448493 84a023 140413 448493 84a023 140413 448493 84a023 140413 448493 140413 433
  //   3c00493 42983 4aa03 149a2b3 28663 134a023 1442023 ffc48493 fe9412e3 800533 2200893 73 440413 3c00493
  //   fc9416e3 3200893 73 fff00293 7700493 849493 7748493 900533 2200893 73 1000e13 54c4b3 900533 2200893
  //   73 fffe0e13 fe0e16e3 a00893 73 800e13 fedc04b7 fff00413 1045413 84e4b3 900533 2200893 73 ba984b7
  //   900533 73 76544b7 900533 73 32104b7 900533 73 fffe0e13 fa0e1ee3 a00893 73 313 2000e13 493 100913
  //   930023 900533 2200893 73 12484b3 130313 fffe0e13 fe0e12e3 800e13 313 32483 900533 2200893 73 430313
  //   fffe0e13 fe0e14e3 a00893 73 f00493 100913 409909b3 900533 2200893 73 fff48493 ff29f6e3 a00893 73
  //   a00893 73 413 140413 800533 2200893 73 240413 800533 2200893 73 340413 800533 2200893 73 440413
  //   800533 2200893 73 540413 800533 2200893 73 640413 800533 2200893 73 740413 800533 2200893 73 840413
  //   800533 2200893 2200893 73 8067
  //   JAL
  //   JALR
  //   URET
  //   I
  //   S
  //   Beq
  //   Bne
  //   Bgeu
  //   MemToReg
  //   MemWrite
  //   AluOP
  //   AluSrcB
  //   RegWrite
  //   LUI
  //   Sb
  //   B
  //   J
  //   为方便自动评测，需要输出PC，IR，寄存器堆写如数据RDin
  //   RAM写使能MemWrite、RAM写入数据MDin等信号
  //   数据存储器
  //   控制位
  //   暂停节拍，不能为0
  //   戳工具置1进入计数暂停模式，ctrl+k时钟自动运行到对应节拍暂停
  //   ctrl+k关闭时钟连续运行，将控制位置零，进入单步调试模式调试
  //   用这个时钟源需要去掉电路中的其他时钟源
  //   可计数暂停的时钟源
endmodule

// 单周期硬布线控制器
module \单周期硬布线控制器  (
  input  [4:0] OP,
  input  [4:0] Funct,
  input  in_3,
  output [3:0] ALU_OP,
  output uret,
  output MemToReg,
  output ecall,
  output MemWrite,
  output ALU_SRC,
  output RegWrite,
  output S_type,
  output Beq,
  output Bne,
  output JAL,
  output Jalr,
  output LUI,
  output SB,
  output BGEU,
  output CSRRSI,
  output CSRRCI
);

  wire \控制信号自动生成_1_ecall ;

  \运算控制器自动生成  \u_运算控制器自动生成_1  (
    .OP2(OP[0]), .OP3(OP[1]), .OP4(OP[2]), .OP5(OP[3]), .OP6(OP[4]), .F12(Funct[0]), .F13(Funct[1]),
    .F14(Funct[2]), .F25(Funct[3]), .F30(Funct[4]), .S0(ALU_OP[0]), .S1(ALU_OP[1]), .S2(ALU_OP[2]),
    .S3(ALU_OP[3]));
  \控制信号自动生成  \u_控制信号自动生成_1  (
    .OP2(OP[0]), .OP3(OP[1]), .MemToReg(MemToReg), .OP4(OP[2]), .OP5(OP[3]), .OP6(OP[4]), .F12(Funct[0]),
    .F13(Funct[1]), .F14(Funct[2]), .MemWrite(MemWrite), .F25(Funct[3]), .F30(Funct[4]), .ALU_Src(ALU_SRC),
    .RegWrite(RegWrite), .ecall(\控制信号自动生成_1_ecall ), .S_Type(S_type), .BEQ(Beq), .BNE(Bne), .Jal(JAL),
    .jalr(Jalr), .LUI(LUI), .SB(SB), .BGEU(BGEU), .CSRRSI(CSRRSI), .CSRRCI(CSRRCI));  // open: URET
  and and_1 (uret, in_3, \控制信号自动生成_1_ecall );
  and and_2 (ecall, ~in_3, \控制信号自动生成_1_ecall );  // AND_Gate

  // Other names for the same wires on the sheet: IR21 = in_3; OP_CODE[4:0] = OP

  // Notes on the sheet:
  //   运算器控制器，根据指令生成运算器功能选择信号
  //   控制信号生成，产生数据通路需要的其他控制信号
endmodule

// 运算器控制器
module \运算控制器自动生成  (
  input  OP2,
  input  OP3,
  input  OP4,
  input  OP5,
  input  OP6,
  input  F12,
  input  F13,
  input  F14,
  input  F25,
  input  F30,
  output S0,
  output S1,
  output S2,
  output S3
);

  wire and_1_out, and_2_out, and_3_out, and_4_out, and_5_out, and_6_out, and_7_out, and_8_out, and_9_out,
       and_10_out, and_11_out, and_12_out, and_13_out, and_14_out, and_15_out, and_16_out, and_17_out,
       and_18_out, and_19_out, and_20_out, and_21_out, and_22_out, and_23_out, and_24_out, and_25_out,
       and_26_out, and_27_out, and_28_out, and_29_out, and_30_out, and_31_out, and_32_out, and_33_out,
       and_34_out, and_35_out, and_36_out, and_37_out, and_38_out, not_1_out, not_2_out, not_3_out,
       not_4_out, not_5_out, not_6_out, not_7_out, not_8_out, not_9_out, not_10_out, not_11_out, not_12_out,
       not_13_out, not_14_out, not_15_out, not_16_out, not_17_out, not_18_out, not_19_out, not_20_out,
       not_21_out, not_22_out, not_23_out, not_24_out, not_25_out, not_26_out, not_27_out, not_28_out,
       not_29_out, not_30_out, not_31_out, not_32_out, not_33_out, not_34_out, not_35_out, not_36_out,
       not_37_out, not_38_out, not_39_out, not_40_out, not_41_out, not_42_out, not_43_out, not_44_out,
       not_45_out, not_46_out, not_47_out, not_48_out, not_49_out, not_50_out, not_51_out, not_52_out,
       not_53_out, not_54_out, not_55_out, not_56_out, not_57_out, not_58_out, not_59_out, not_60_out,
       not_61_out, not_62_out, not_63_out, not_64_out, not_65_out, not_66_out, not_67_out, not_68_out,
       not_69_out, not_70_out, not_71_out, not_72_out, not_73_out, not_74_out, not_75_out, not_76_out,
       not_77_out, not_78_out, not_79_out, not_80_out, not_81_out, not_82_out, not_83_out, not_84_out,
       not_85_out, not_86_out, not_87_out, not_88_out, not_89_out, not_90_out, not_91_out, not_92_out,
       not_93_out, not_94_out, not_95_out, not_96_out, not_97_out, not_98_out, not_99_out, not_100_out,
       not_101_out, not_102_out, not_103_out, not_104_out, not_105_out, not_106_out, not_107_out,
       not_108_out, not_109_out, not_110_out, not_111_out, not_112_out, not_113_out, not_114_out,
       not_115_out, not_116_out, not_117_out, not_118_out, not_119_out, not_120_out, not_121_out,
       not_122_out, not_123_out, not_124_out, not_125_out, not_126_out, not_127_out, not_128_out,
       not_129_out, not_130_out, not_131_out, not_132_out, not_133_out, not_134_out, not_135_out,
       not_136_out, not_137_out, not_138_out, not_139_out, not_140_out, not_141_out, not_142_out,
       not_143_out, not_144_out, not_145_out, not_146_out, not_147_out, not_148_out, not_149_out,
       not_150_out, not_151_out, not_152_out, not_153_out, not_154_out, not_155_out, not_156_out,
       not_157_out, not_158_out, not_159_out, not_160_out, not_161_out, not_162_out, not_163_out,
       not_164_out, not_165_out, not_166_out, not_167_out, not_168_out, not_169_out, not_170_out,
       not_171_out, not_172_out, not_173_out, not_174_out, not_175_out, not_176_out, not_177_out,
       not_178_out, not_179_out, not_180_out, not_181_out, not_182_out, not_183_out, not_184_out,
       not_185_out, not_186_out, not_187_out, not_188_out, not_189_out, not_190_out, not_191_out,
       not_192_out, not_193_out, not_194_out, not_195_out, not_196_out, not_197_out, not_198_out,
       not_199_out, not_200_out, not_201_out, not_202_out, not_203_out, not_204_out, not_205_out,
       not_206_out, not_207_out, not_208_out, not_209_out, not_210_out, not_211_out, not_212_out,
       not_213_out, not_214_out, not_215_out, not_216_out, not_217_out, not_218_out, not_219_out,
       not_220_out, not_221_out;

  not not_1 (not_1_out, F30);
  not not_2 (not_2_out, F25);
  not not_3 (not_3_out, F14);
  not not_4 (not_4_out, F13);
  not not_5 (not_5_out, F12);
  not not_6 (not_6_out, OP6);
  not not_7 (not_7_out, OP3);
  not not_8 (not_8_out, OP2);
  not not_9 (not_9_out, F30);
  not not_10 (not_10_out, F25);
  not not_11 (not_11_out, OP6);
  not not_12 (not_12_out, OP3);
  not not_13 (not_13_out, OP2);
  not not_14 (not_14_out, F30);
  not not_15 (not_15_out, F25);
  not not_16 (not_16_out, F14);
  not not_17 (not_17_out, F12);
  not not_18 (not_18_out, OP6);
  not not_19 (not_19_out, OP3);
  not not_20 (not_20_out, OP2);
  not not_21 (not_21_out, F14);
  not not_22 (not_22_out, F13);
  not not_23 (not_23_out, F12);
  not not_24 (not_24_out, OP6);
  not not_25 (not_25_out, OP5);
  not not_26 (not_26_out, OP3);
  not not_27 (not_27_out, OP2);
  not not_28 (not_28_out, OP6);
  not not_29 (not_29_out, OP5);
  not not_30 (not_30_out, OP3);
  not not_31 (not_31_out, OP2);
  not not_32 (not_32_out, F13);
  not not_33 (not_33_out, F12);
  not not_34 (not_34_out, OP6);
  not not_35 (not_35_out, OP5);
  not not_36 (not_36_out, OP3);
  not not_37 (not_37_out, OP2);
  not not_38 (not_38_out, F14);
  not not_39 (not_39_out, F12);
  not not_40 (not_40_out, OP6);
  not not_41 (not_41_out, OP5);
  not not_42 (not_42_out, OP3);
  not not_43 (not_43_out, OP2);
  not not_44 (not_44_out, F25);
  not not_45 (not_45_out, F13);
  not not_46 (not_46_out, OP6);
  not not_47 (not_47_out, OP5);
  not not_48 (not_48_out, OP3);
  not not_49 (not_49_out, OP2);
  not not_50 (not_50_out, F14);
  not not_51 (not_51_out, F12);
  not not_52 (not_52_out, OP6);
  not not_53 (not_53_out, OP5);
  not not_54 (not_54_out, OP4);
  not not_55 (not_55_out, OP3);
  not not_56 (not_56_out, OP2);
  not not_57 (not_57_out, F14);
  not not_58 (not_58_out, F12);
  not not_59 (not_59_out, OP6);
  not not_60 (not_60_out, OP4);
  not not_61 (not_61_out, OP3);
  not not_62 (not_62_out, OP2);
  not not_63 (not_63_out, OP3);
  not not_64 (not_64_out, OP2);
  not not_65 (not_65_out, F30);
  not not_66 (not_66_out, F25);
  not not_67 (not_67_out, F13);
  not not_68 (not_68_out, F12);
  not not_69 (not_69_out, OP6);
  not not_70 (not_70_out, OP3);
  not not_71 (not_71_out, OP2);
  not not_72 (not_72_out, F14);
  not not_73 (not_73_out, F13);
  not not_74 (not_74_out, F12);
  not not_75 (not_75_out, OP6);
  not not_76 (not_76_out, OP4);
  not not_77 (not_77_out, OP3);
  not not_78 (not_78_out, OP2);
  not not_79 (not_79_out, F25);
  not not_80 (not_80_out, F14);
  not not_81 (not_81_out, F13);
  not not_82 (not_82_out, F12);
  not not_83 (not_83_out, OP6);
  not not_84 (not_84_out, OP3);
  not not_85 (not_85_out, OP2);
  not not_86 (not_86_out, F30);
  not not_87 (not_87_out, F25);
  not not_88 (not_88_out, OP6);
  not not_89 (not_89_out, OP3);
  not not_90 (not_90_out, OP2);
  not not_91 (not_91_out, F30);
  not not_92 (not_92_out, F25);
  not not_93 (not_93_out, F14);
  not not_94 (not_94_out, F12);
  not not_95 (not_95_out, OP6);
  not not_96 (not_96_out, OP3);
  not not_97 (not_97_out, OP2);
  not not_98 (not_98_out, OP6);
  not not_99 (not_99_out, OP5);
  not not_100 (not_100_out, OP3);
  not not_101 (not_101_out, OP2);
  not not_102 (not_102_out, F14);
  not not_103 (not_103_out, F12);
  not not_104 (not_104_out, OP6);
  not not_105 (not_105_out, OP5);
  not not_106 (not_106_out, OP3);
  not not_107 (not_107_out, OP2);
  not not_108 (not_108_out, F30);
  not not_109 (not_109_out, F25);
  not not_110 (not_110_out, F13);
  not not_111 (not_111_out, OP6);
  not not_112 (not_112_out, OP5);
  not not_113 (not_113_out, OP3);
  not not_114 (not_114_out, OP2);
  not not_115 (not_115_out, OP3);
  not not_116 (not_116_out, OP2);
  not not_117 (not_117_out, F30);
  not not_118 (not_118_out, F25);
  not not_119 (not_119_out, F14);
  not not_120 (not_120_out, F13);
  not not_121 (not_121_out, F12);
  not not_122 (not_122_out, OP6);
  not not_123 (not_123_out, OP3);
  not not_124 (not_124_out, OP2);
  not not_125 (not_125_out, F25);
  not not_126 (not_126_out, F14);
  not not_127 (not_127_out, F13);
  not not_128 (not_128_out, F12);
  not not_129 (not_129_out, OP6);
  not not_130 (not_130_out, OP3);
  not not_131 (not_131_out, OP2);
  not not_132 (not_132_out, F30);
  not not_133 (not_133_out, F25);
  not not_134 (not_134_out, OP6);
  not not_135 (not_135_out, OP3);
  not not_136 (not_136_out, OP2);
  not not_137 (not_137_out, F30);
  not not_138 (not_138_out, F25);
  not not_139 (not_139_out, F14);
  not not_140 (not_140_out, OP6);
  not not_141 (not_141_out, OP3);
  not not_142 (not_142_out, OP2);
  not not_143 (not_143_out, F14);
  not not_144 (not_144_out, F13);
  not not_145 (not_145_out, F12);
  not not_146 (not_146_out, OP6);
  not not_147 (not_147_out, OP5);
  not not_148 (not_148_out, OP3);
  not not_149 (not_149_out, OP2);
  not not_150 (not_150_out, OP6);
  not not_151 (not_151_out, OP5);
  not not_152 (not_152_out, OP3);
  not not_153 (not_153_out, OP2);
  not not_154 (not_154_out, F14);
  not not_155 (not_155_out, F12);
  not not_156 (not_156_out, OP6);
  not not_157 (not_157_out, OP5);
  not not_158 (not_158_out, OP4);
  not not_159 (not_159_out, OP3);
  not not_160 (not_160_out, OP2);
  not not_161 (not_161_out, F14);
  not not_162 (not_162_out, F12);
  not not_163 (not_163_out, OP6);
  not not_164 (not_164_out, OP4);
  not not_165 (not_165_out, OP3);
  not not_166 (not_166_out, OP2);
  not not_167 (not_167_out, OP3);
  not not_168 (not_168_out, OP2);
  not not_169 (not_169_out, F14);
  not not_170 (not_170_out, F13);
  not not_171 (not_171_out, F12);
  not not_172 (not_172_out, OP6);
  not not_173 (not_173_out, OP4);
  not not_174 (not_174_out, OP3);
  not not_175 (not_175_out, OP2);
  not not_176 (not_176_out, F30);
  not not_177 (not_177_out, F25);
  not not_178 (not_178_out, F12);
  not not_179 (not_179_out, OP6);
  not not_180 (not_180_out, OP3);
  not not_181 (not_181_out, OP2);
  not not_182 (not_182_out, F30);
  not not_183 (not_183_out, F25);
  not not_184 (not_184_out, F14);
  not not_185 (not_185_out, F12);
  not not_186 (not_186_out, OP6);
  not not_187 (not_187_out, OP3);
  not not_188 (not_188_out, OP2);
  not not_189 (not_189_out, F30);
  not not_190 (not_190_out, F25);
  not not_191 (not_191_out, F14);
  not not_192 (not_192_out, OP6);
  not not_193 (not_193_out, OP3);
  not not_194 (not_194_out, OP2);
  not not_195 (not_195_out, F12);
  not not_196 (not_196_out, OP6);
  not not_197 (not_197_out, OP5);
  not not_198 (not_198_out, OP3);
  not not_199 (not_199_out, OP2);
  not not_200 (not_200_out, F13);
  not not_201 (not_201_out, F12);
  not not_202 (not_202_out, OP6);
  not not_203 (not_203_out, OP5);
  not not_204 (not_204_out, OP3);
  not not_205 (not_205_out, OP2);
  not not_206 (not_206_out, F14);
  not not_207 (not_207_out, F12);
  not not_208 (not_208_out, OP6);
  not not_209 (not_209_out, OP5);
  not not_210 (not_210_out, OP3);
  not not_211 (not_211_out, OP2);
  not not_212 (not_212_out, F12);
  not not_213 (not_213_out, OP3);
  not not_214 (not_214_out, OP2);
  not not_215 (not_215_out, F30);
  not not_216 (not_216_out, F25);
  not not_217 (not_217_out, F13);
  not not_218 (not_218_out, F12);
  not not_219 (not_219_out, OP6);
  not not_220 (not_220_out, OP3);
  not not_221 (not_221_out, OP2);
  and and_1 (and_1_out, not_1_out, not_2_out, not_3_out, not_4_out, not_5_out, not_6_out, OP5, OP4, not_7_out, not_8_out);
  and and_2 (and_2_out, not_9_out, not_10_out, F14, F13, F12, not_11_out, OP5, OP4, not_12_out, not_13_out);
  and and_3 (and_3_out, not_14_out, not_15_out, not_16_out, F13, not_17_out, not_18_out, OP5, OP4, not_19_out, not_20_out);
  and and_4 (and_4_out, not_21_out, not_22_out, not_23_out, not_24_out, not_25_out, OP4, not_26_out, not_27_out);
  and and_5 (and_5_out, F14, F13, F12, not_28_out, not_29_out, OP4, not_30_out, not_31_out);
  and and_6 (and_6_out, F14, not_32_out, not_33_out, not_34_out, not_35_out, OP4, not_36_out, not_37_out);
  and and_7 (and_7_out, not_38_out, F13, not_39_out, not_40_out, not_41_out, OP4, not_42_out, not_43_out);
  and and_8 (and_8_out, F30, not_44_out, F14, not_45_out, F12, not_46_out, not_47_out, OP4, not_48_out, not_49_out);
  and and_9 (and_9_out, not_50_out, F13, not_51_out, not_52_out, not_53_out, not_54_out, not_55_out, not_56_out);
  and and_10 (and_10_out, not_57_out, F13, not_58_out, not_59_out, OP5, not_60_out, not_61_out, not_62_out);
  and and_11 (and_11_out, F14, F13, F12, OP6, OP5, OP4, not_63_out, not_64_out);
  and and_12 (and_12_out, not_65_out, not_66_out, F14, not_67_out, not_68_out, not_69_out, OP5, OP4, not_70_out, not_71_out);
  and and_13 (and_13_out, not_72_out, not_73_out, not_74_out, not_75_out, OP5, not_76_out, not_77_out, not_78_out);
  and and_14 (and_14_out, F30, not_79_out, not_80_out, not_81_out, not_82_out, not_83_out, OP5, OP4, not_84_out, not_85_out);
  and and_15 (and_15_out, not_86_out, not_87_out, F14, F13, F12, not_88_out, OP5, OP4, not_89_out, not_90_out);
  and and_16 (and_16_out, not_91_out, not_92_out, not_93_out, F13, not_94_out, not_95_out, OP5, OP4, not_96_out, not_97_out);
  and and_17 (and_17_out, F14, F13, F12, not_98_out, not_99_out, OP4, not_100_out, not_101_out);
  and and_18 (and_18_out, not_102_out, F13, not_103_out, not_104_out, not_105_out, OP4, not_106_out, not_107_out);
  and and_19 (and_19_out, not_108_out, not_109_out, F14, not_110_out, F12, not_111_out, not_112_out, OP4, not_113_out, not_114_out);
  and and_20 (and_20_out, F14, F13, F12, OP6, OP5, OP4, not_115_out, not_116_out);
  and and_21 (and_21_out, not_117_out, not_118_out, not_119_out, not_120_out, not_121_out, not_122_out, OP5, OP4, not_123_out, not_124_out);
  and and_22 (and_22_out, F30, not_125_out, not_126_out, not_127_out, not_128_out, not_129_out, OP5, OP4, not_130_out, not_131_out);
  and and_23 (and_23_out, not_132_out, not_133_out, F14, F13, F12, not_134_out, OP5, OP4, not_135_out, not_136_out);
  and and_24 (and_24_out, not_137_out, not_138_out, not_139_out, F13, F12, not_140_out, OP5, OP4, not_141_out, not_142_out);
  and and_25 (and_25_out, not_143_out, not_144_out, not_145_out, not_146_out, not_147_out, OP4, not_148_out, not_149_out);
  and and_26 (and_26_out, F14, F13, F12, not_150_out, not_151_out, OP4, not_152_out, not_153_out);
  and and_27 (and_27_out, not_154_out, F13, not_155_out, not_156_out, not_157_out, not_158_out, not_159_out, not_160_out);
  and and_28 (and_28_out, not_161_out, F13, not_162_out, not_163_out, OP5, not_164_out, not_165_out, not_166_out);
  and and_29 (and_29_out, F14, F13, F12, OP6, OP5, OP4, not_167_out, not_168_out);
  and and_30 (and_30_out, not_169_out, not_170_out, not_171_out, not_172_out, OP5, not_173_out, not_174_out, not_175_out);
  and and_31 (and_31_out, not_176_out, not_177_out, F14, F13, not_178_out, not_179_out, OP5, OP4, not_180_out, not_181_out);
  and and_32 (and_32_out, not_182_out, not_183_out, not_184_out, F13, not_185_out, not_186_out, OP5, OP4, not_187_out, not_188_out);
  and and_33 (and_33_out, not_189_out, not_190_out, not_191_out, F13, F12, not_192_out, OP5, OP4, not_193_out, not_194_out);
  and and_34 (and_34_out, F14, F13, not_195_out, not_196_out, not_197_out, OP4, not_198_out, not_199_out);
  and and_35 (and_35_out, F14, not_200_out, not_201_out, not_202_out, not_203_out, OP4, not_204_out, not_205_out);
  and and_36 (and_36_out, not_206_out, F13, not_207_out, not_208_out, not_209_out, OP4, not_210_out, not_211_out);
  and and_37 (and_37_out, F14, F13, not_212_out, OP6, OP5, OP4, not_213_out, not_214_out);
  and and_38 (and_38_out, not_215_out, not_216_out, F14, not_217_out, not_218_out, not_219_out, OP5, OP4, not_220_out, not_221_out);
  or or_1 (S0, and_1_out, and_2_out, and_3_out, and_4_out, and_5_out, and_6_out, and_7_out, and_8_out, and_9_out, and_10_out, and_11_out, and_12_out, and_13_out);
  or or_2 (S1, and_14_out, and_15_out, and_16_out, and_17_out, and_18_out, and_19_out, and_20_out);
  or or_3 (S2, and_21_out, and_22_out, and_23_out, and_24_out, and_25_out, and_26_out, and_27_out, and_28_out, and_29_out, and_30_out);
  or or_4 (S3, and_31_out, and_32_out, and_33_out, and_34_out, and_35_out, and_36_out, and_37_out, and_38_out);
endmodule

// 控制信号生成
module \控制信号自动生成  (
  input  OP2,
  input  OP3,
  input  OP4,
  input  OP5,
  input  OP6,
  input  F12,
  input  F13,
  input  F14,
  input  F25,
  input  F30,
  output MemToReg,
  output MemWrite,
  output ALU_Src,
  output RegWrite,
  output ecall,
  output S_Type,
  output BEQ,
  output BNE,
  output Jal,
  output jalr,
  output URET,
  output LUI,
  output SB,
  output BGEU,
  output CSRRSI,
  output CSRRCI
);

  wire and_2_out, and_3_out, and_4_out, and_5_out, and_6_out, and_7_out, and_8_out, and_9_out, and_10_out,
       and_11_out, and_12_out, and_13_out, and_14_out, and_15_out, and_16_out, and_17_out, and_18_out,
       and_19_out, and_20_out, and_21_out, and_22_out, and_23_out, and_24_out, and_25_out, and_26_out,
       and_27_out, and_28_out, and_29_out, and_30_out, and_31_out, and_32_out, and_33_out, and_35_out,
       and_36_out, not_1_out, not_2_out, not_3_out, not_4_out, not_5_out, not_6_out, not_7_out, not_8_out,
       not_9_out, not_10_out, not_11_out, not_12_out, not_13_out, not_14_out, not_15_out, not_16_out,
       not_17_out, not_18_out, not_19_out, not_20_out, not_21_out, not_22_out, not_23_out, not_24_out,
       not_25_out, not_26_out, not_27_out, not_28_out, not_29_out, not_30_out, not_31_out, not_32_out,
       not_33_out, not_34_out, not_35_out, not_36_out, not_37_out, not_38_out, not_39_out, not_40_out,
       not_41_out, not_42_out, not_43_out, not_44_out, not_45_out, not_46_out, not_47_out, not_48_out,
       not_49_out, not_50_out, not_51_out, not_52_out, not_53_out, not_54_out, not_55_out, not_56_out,
       not_57_out, not_58_out, not_59_out, not_60_out, not_61_out, not_62_out, not_63_out, not_64_out,
       not_65_out, not_66_out, not_67_out, not_68_out, not_69_out, not_70_out, not_71_out, not_72_out,
       not_73_out, not_74_out, not_75_out, not_76_out, not_77_out, not_78_out, not_79_out, not_80_out,
       not_81_out, not_82_out, not_83_out, not_84_out, not_85_out, not_86_out, not_87_out, not_88_out,
       not_89_out, not_90_out, not_91_out, not_92_out, not_93_out, not_94_out, not_95_out, not_96_out,
       not_97_out, not_98_out, not_99_out, not_100_out, not_101_out, not_102_out, not_103_out, not_104_out,
       not_105_out, not_106_out, not_107_out, not_108_out, not_109_out, not_110_out, not_111_out,
       not_112_out, not_113_out, not_114_out, not_115_out, not_116_out, not_117_out, not_118_out,
       not_119_out, not_120_out, not_121_out, not_122_out, not_123_out, not_124_out, not_125_out,
       not_126_out, not_127_out, not_128_out, not_129_out, not_130_out, not_131_out, not_132_out,
       not_133_out, not_134_out, not_135_out, not_136_out, not_137_out, not_138_out, not_139_out,
       not_140_out, not_141_out, not_142_out, not_143_out, not_144_out, not_145_out, not_146_out,
       not_147_out, not_148_out, not_149_out, not_150_out, not_151_out, not_152_out, not_153_out,
       not_154_out, not_155_out, not_156_out, not_157_out, not_158_out, not_159_out, not_160_out,
       not_161_out, not_162_out, not_163_out, not_164_out, not_165_out, not_166_out, not_167_out,
       not_168_out, not_169_out, not_170_out, not_171_out, not_172_out, not_173_out, not_174_out,
       not_175_out, not_176_out, not_177_out, not_178_out, not_179_out, not_180_out, not_181_out,
       not_182_out, not_183_out, not_184_out, not_185_out, not_186_out, not_187_out, not_188_out,
       not_189_out, not_190_out, not_191_out, not_192_out, not_193_out, not_194_out, not_195_out,
       not_196_out, not_197_out, not_198_out, not_199_out, not_200_out, not_201_out, not_202_out,
       not_203_out, not_204_out, not_205_out, not_206_out, not_207_out, not_208_out, not_209_out,
       not_210_out, not_211_out, not_212_out, not_213_out, not_214_out, not_215_out, not_216_out,
       not_217_out, not_218_out, not_219_out, not_220_out, not_221_out, not_222_out, not_223_out,
       not_224_out, not_225_out, not_226_out, not_227_out, not_228_out, not_229_out, not_230_out,
       not_231_out, not_232_out, not_233_out, not_234_out, not_235_out, not_236_out, not_237_out,
       not_238_out, not_239_out, not_240_out, not_241_out, not_242_out, not_243_out, not_244_out,
       not_245_out, not_246_out, not_247_out, not_248_out, not_249_out, not_250_out, not_251_out,
       not_252_out, not_253_out, not_254_out, not_255_out, not_256_out;

  not not_1 (not_1_out, F14);
  not not_2 (not_2_out, F12);
  not not_3 (not_3_out, OP6);
  not not_4 (not_4_out, OP5);
  not not_5 (not_5_out, OP4);
  not not_6 (not_6_out, OP3);
  not not_7 (not_7_out, OP2);
  not not_8 (not_8_out, F14);
  not not_9 (not_9_out, F12);
  not not_10 (not_10_out, OP6);
  not not_11 (not_11_out, OP4);
  not not_12 (not_12_out, OP3);
  not not_13 (not_13_out, OP2);
  not not_14 (not_14_out, F14);
  not not_15 (not_15_out, F13);
  not not_16 (not_16_out, F12);
  not not_17 (not_17_out, OP6);
  not not_18 (not_18_out, OP4);
  not not_19 (not_19_out, OP3);
  not not_20 (not_20_out, OP2);
  not not_21 (not_21_out, F14);
  not not_22 (not_22_out, F13);
  not not_23 (not_23_out, F12);
  not not_24 (not_24_out, OP6);
  not not_25 (not_25_out, OP5);
  not not_26 (not_26_out, OP3);
  not not_27 (not_27_out, OP2);
  not not_28 (not_28_out, OP6);
  not not_29 (not_29_out, OP5);
  not not_30 (not_30_out, OP3);
  not not_31 (not_31_out, OP2);
  not not_32 (not_32_out, F12);
  not not_33 (not_33_out, OP6);
  not not_34 (not_34_out, OP5);
  not not_35 (not_35_out, OP3);
  not not_36 (not_36_out, OP2);
  not not_37 (not_37_out, F13);
  not not_38 (not_38_out, F12);
  not not_39 (not_39_out, OP6);
  not not_40 (not_40_out, OP5);
  not not_41 (not_41_out, OP3);
  not not_42 (not_42_out, OP2);
  not not_43 (not_43_out, F14);
  not not_44 (not_44_out, F12);
  not not_45 (not_45_out, OP6);
  not not_46 (not_46_out, OP5);
  not not_47 (not_47_out, OP3);
  not not_48 (not_48_out, OP2);
  not not_49 (not_49_out, F30);
  not not_50 (not_50_out, F25);
  not not_51 (not_51_out, F14);
  not not_52 (not_52_out, F13);
  not not_53 (not_53_out, OP6);
  not not_54 (not_54_out, OP5);
  not not_55 (not_55_out, OP3);
  not not_56 (not_56_out, OP2);
  not not_57 (not_57_out, F30);
  not not_58 (not_58_out, F25);
  not not_59 (not_59_out, F13);
  not not_60 (not_60_out, OP6);
  not not_61 (not_61_out, OP5);
  not not_62 (not_62_out, OP3);
  not not_63 (not_63_out, OP2);
  not not_64 (not_64_out, F25);
  not not_65 (not_65_out, F13);
  not not_66 (not_66_out, OP6);
  not not_67 (not_67_out, OP5);
  not not_68 (not_68_out, OP3);
  not not_69 (not_69_out, OP2);
  not not_70 (not_70_out, F14);
  not not_71 (not_71_out, F12);
  not not_72 (not_72_out, OP6);
  not not_73 (not_73_out, OP5);
  not not_74 (not_74_out, OP4);
  not not_75 (not_75_out, OP3);
  not not_76 (not_76_out, OP2);
  not not_77 (not_77_out, F14);
  not not_78 (not_78_out, F12);
  not not_79 (not_79_out, OP6);
  not not_80 (not_80_out, OP4);
  not not_81 (not_81_out, OP3);
  not not_82 (not_82_out, OP2);
  not not_83 (not_83_out, F14);
  not not_84 (not_84_out, F13);
  not not_85 (not_85_out, F12);
  not not_86 (not_86_out, OP6);
  not not_87 (not_87_out, OP4);
  not not_88 (not_88_out, OP3);
  not not_89 (not_89_out, OP2);
  not not_90 (not_90_out, F30);
  not not_91 (not_91_out, F25);
  not not_92 (not_92_out, F14);
  not not_93 (not_93_out, F13);
  not not_94 (not_94_out, F12);
  not not_95 (not_95_out, OP6);
  not not_96 (not_96_out, OP3);
  not not_97 (not_97_out, OP2);
  not not_98 (not_98_out, F25);
  not not_99 (not_99_out, F14);
  not not_100 (not_100_out, F13);
  not not_101 (not_101_out, F12);
  not not_102 (not_102_out, OP6);
  not not_103 (not_103_out, OP3);
  not not_104 (not_104_out, OP2);
  not not_105 (not_105_out, F30);
  not not_106 (not_106_out, F25);
  not not_107 (not_107_out, OP6);
  not not_108 (not_108_out, OP3);
  not not_109 (not_109_out, OP2);
  not not_110 (not_110_out, F30);
  not not_111 (not_111_out, F25);
  not not_112 (not_112_out, F12);
  not not_113 (not_113_out, OP6);
  not not_114 (not_114_out, OP3);
  not not_115 (not_115_out, OP2);
  not not_116 (not_116_out, F30);
  not not_117 (not_117_out, F25);
  not not_118 (not_118_out, F14);
  not not_119 (not_119_out, F12);
  not not_120 (not_120_out, OP6);
  not not_121 (not_121_out, OP3);
  not not_122 (not_122_out, OP2);
  not not_123 (not_123_out, F30);
  not not_124 (not_124_out, F25);
  not not_125 (not_125_out, F14);
  not not_126 (not_126_out, OP6);
  not not_127 (not_127_out, OP3);
  not not_128 (not_128_out, OP2);
  not not_129 (not_129_out, F14);
  not not_130 (not_130_out, F13);
  not not_131 (not_131_out, F12);
  not not_132 (not_132_out, OP6);
  not not_133 (not_133_out, OP5);
  not not_134 (not_134_out, OP3);
  not not_135 (not_135_out, OP2);
  not not_136 (not_136_out, OP6);
  not not_137 (not_137_out, OP5);
  not not_138 (not_138_out, OP3);
  not not_139 (not_139_out, OP2);
  not not_140 (not_140_out, F12);
  not not_141 (not_141_out, OP6);
  not not_142 (not_142_out, OP5);
  not not_143 (not_143_out, OP3);
  not not_144 (not_144_out, OP2);
  not not_145 (not_145_out, F13);
  not not_146 (not_146_out, F12);
  not not_147 (not_147_out, OP6);
  not not_148 (not_148_out, OP5);
  not not_149 (not_149_out, OP3);
  not not_150 (not_150_out, OP2);
  not not_151 (not_151_out, F14);
  not not_152 (not_152_out, F12);
  not not_153 (not_153_out, OP6);
  not not_154 (not_154_out, OP5);
  not not_155 (not_155_out, OP3);
  not not_156 (not_156_out, OP2);
  not not_157 (not_157_out, F30);
  not not_158 (not_158_out, F25);
  not not_159 (not_159_out, F14);
  not not_160 (not_160_out, F13);
  not not_161 (not_161_out, OP6);
  not not_162 (not_162_out, OP5);
  not not_163 (not_163_out, OP3);
  not not_164 (not_164_out, OP2);
  not not_165 (not_165_out, F30);
  not not_166 (not_166_out, F25);
  not not_167 (not_167_out, F13);
  not not_168 (not_168_out, OP6);
  not not_169 (not_169_out, OP5);
  not not_170 (not_170_out, OP3);
  not not_171 (not_171_out, OP2);
  not not_172 (not_172_out, F25);
  not not_173 (not_173_out, F13);
  not not_174 (not_174_out, OP6);
  not not_175 (not_175_out, OP5);
  not not_176 (not_176_out, OP3);
  not not_177 (not_177_out, OP2);
  not not_178 (not_178_out, F14);
  not not_179 (not_179_out, F12);
  not not_180 (not_180_out, OP6);
  not not_181 (not_181_out, OP5);
  not not_182 (not_182_out, OP4);
  not not_183 (not_183_out, OP3);
  not not_184 (not_184_out, OP2);
  not not_185 (not_185_out, OP4);
  not not_186 (not_186_out, F14);
  not not_187 (not_187_out, F13);
  not not_188 (not_188_out, F12);
  not not_189 (not_189_out, OP4);
  not not_190 (not_190_out, OP3);
  not not_191 (not_191_out, F30);
  not not_192 (not_192_out, F25);
  not not_193 (not_193_out, F13);
  not not_194 (not_194_out, F12);
  not not_195 (not_195_out, OP6);
  not not_196 (not_196_out, OP3);
  not not_197 (not_197_out, OP2);
  not not_198 (not_198_out, OP6);
  not not_199 (not_199_out, OP3);
  not not_200 (not_200_out, F14);
  not not_201 (not_201_out, F13);
  not not_202 (not_202_out, F12);
  not not_203 (not_203_out, OP3);
  not not_204 (not_204_out, OP2);
  not not_205 (not_205_out, F14);
  not not_206 (not_206_out, F12);
  not not_207 (not_207_out, OP6);
  not not_208 (not_208_out, OP4);
  not not_209 (not_209_out, OP3);
  not not_210 (not_210_out, OP2);
  not not_211 (not_211_out, F14);
  not not_212 (not_212_out, F13);
  not not_213 (not_213_out, F12);
  not not_214 (not_214_out, OP6);
  not not_215 (not_215_out, OP4);
  not not_216 (not_216_out, OP3);
  not not_217 (not_217_out, OP2);
  not not_218 (not_218_out, F14);
  not not_219 (not_219_out, F13);
  not not_220 (not_220_out, F12);
  not not_221 (not_221_out, OP4);
  not not_222 (not_222_out, OP3);
  not not_223 (not_223_out, OP2);
  not not_224 (not_224_out, F14);
  not not_225 (not_225_out, F13);
  not not_226 (not_226_out, OP4);
  not not_227 (not_227_out, OP3);
  not not_228 (not_228_out, OP2);
  not not_229 (not_229_out, OP4);
  not not_230 (not_230_out, F14);
  not not_231 (not_231_out, F13);
  not not_232 (not_232_out, F12);
  not not_233 (not_233_out, OP4);
  not not_234 (not_234_out, OP3);
  not not_235 (not_235_out, F14);
  not not_236 (not_236_out, F13);
  not not_237 (not_237_out, F12);
  not not_238 (not_238_out, OP3);
  not not_239 (not_239_out, OP2);
  not not_240 (not_240_out, OP6);
  not not_241 (not_241_out, OP3);
  not not_242 (not_242_out, F14);
  not not_243 (not_243_out, F13);
  not not_244 (not_244_out, F12);
  not not_245 (not_245_out, OP6);
  not not_246 (not_246_out, OP4);
  not not_247 (not_247_out, OP3);
  not not_248 (not_248_out, OP2);
  not not_249 (not_249_out, OP4);
  not not_250 (not_250_out, OP3);
  not not_251 (not_251_out, OP2);
  not not_252 (not_252_out, F12);
  not not_253 (not_253_out, OP3);
  not not_254 (not_254_out, OP2);
  not not_255 (not_255_out, OP3);
  not not_256 (not_256_out, OP2);
  and and_1 (MemToReg, not_1_out, F13, not_2_out, not_3_out, not_4_out, not_5_out, not_6_out, not_7_out);
  and and_2 (and_2_out, not_8_out, F13, not_9_out, not_10_out, OP5, not_11_out, not_12_out, not_13_out);
  and and_3 (and_3_out, not_14_out, not_15_out, not_16_out, not_17_out, OP5, not_18_out, not_19_out, not_20_out);
  and and_4 (and_4_out, not_21_out, not_22_out, not_23_out, not_24_out, not_25_out, OP4, not_26_out, not_27_out);
  and and_5 (and_5_out, F14, F13, F12, not_28_out, not_29_out, OP4, not_30_out, not_31_out);
  and and_6 (and_6_out, F14, F13, not_32_out, not_33_out, not_34_out, OP4, not_35_out, not_36_out);
  and and_7 (and_7_out, F14, not_37_out, not_38_out, not_39_out, not_40_out, OP4, not_41_out, not_42_out);
  and and_8 (and_8_out, not_43_out, F13, not_44_out, not_45_out, not_46_out, OP4, not_47_out, not_48_out);
  and and_9 (and_9_out, not_49_out, not_50_out, not_51_out, not_52_out, F12, not_53_out, not_54_out, OP4, not_55_out, not_56_out);
  and and_10 (and_10_out, not_57_out, not_58_out, F14, not_59_out, F12, not_60_out, not_61_out, OP4, not_62_out, not_63_out);
  and and_11 (and_11_out, F30, not_64_out, F14, not_65_out, F12, not_66_out, not_67_out, OP4, not_68_out, not_69_out);
  and and_12 (and_12_out, not_70_out, F13, not_71_out, not_72_out, not_73_out, not_74_out, not_75_out, not_76_out);
  and and_13 (and_13_out, not_77_out, F13, not_78_out, not_79_out, OP5, not_80_out, not_81_out, not_82_out);
  and and_14 (and_14_out, not_83_out, not_84_out, not_85_out, not_86_out, OP5, not_87_out, not_88_out, not_89_out);
  and and_15 (and_15_out, not_90_out, not_91_out, not_92_out, not_93_out, not_94_out, not_95_out, OP5, OP4, not_96_out, not_97_out);
  and and_16 (and_16_out, F30, not_98_out, not_99_out, not_100_out, not_101_out, not_102_out, OP5, OP4, not_103_out, not_104_out);
  and and_17 (and_17_out, not_105_out, not_106_out, F14, F13, F12, not_107_out, OP5, OP4, not_108_out, not_109_out);
  and and_18 (and_18_out, not_110_out, not_111_out, F14, F13, not_112_out, not_113_out, OP5, OP4, not_114_out, not_115_out);
  and and_19 (and_19_out, not_116_out, not_117_out, not_118_out, F13, not_119_out, not_120_out, OP5, OP4, not_121_out, not_122_out);
  and and_20 (and_20_out, not_123_out, not_124_out, not_125_out, F13, F12, not_126_out, OP5, OP4, not_127_out, not_128_out);
  and and_21 (and_21_out, not_129_out, not_130_out, not_131_out, not_132_out, not_133_out, OP4, not_134_out, not_135_out);
  and and_22 (and_22_out, F14, F13, F12, not_136_out, not_137_out, OP4, not_138_out, not_139_out);
  and and_23 (and_23_out, F14, F13, not_140_out, not_141_out, not_142_out, OP4, not_143_out, not_144_out);
  and and_24 (and_24_out, F14, not_145_out, not_146_out, not_147_out, not_148_out, OP4, not_149_out, not_150_out);
  and and_25 (and_25_out, not_151_out, F13, not_152_out, not_153_out, not_154_out, OP4, not_155_out, not_156_out);
  and and_26 (and_26_out, not_157_out, not_158_out, not_159_out, not_160_out, F12, not_161_out, not_162_out, OP4, not_163_out, not_164_out);
  and and_27 (and_27_out, not_165_out, not_166_out, F14, not_167_out, F12, not_168_out, not_169_out, OP4, not_170_out, not_171_out);
  and and_28 (and_28_out, F30, not_172_out, F14, not_173_out, F12, not_174_out, not_175_out, OP4, not_176_out, not_177_out);
  and and_29 (and_29_out, not_178_out, F13, not_179_out, not_180_out, not_181_out, not_182_out, not_183_out, not_184_out);
  and and_30 (and_30_out, OP6, OP5, not_185_out, OP3, OP2);
  and and_31 (and_31_out, not_186_out, not_187_out, not_188_out, OP6, OP5, not_189_out, not_190_out, OP2);
  and and_32 (and_32_out, not_191_out, not_192_out, F14, not_193_out, not_194_out, not_195_out, OP5, OP4, not_196_out, not_197_out);
  and and_33 (and_33_out, not_198_out, OP5, OP4, not_199_out, OP2);
  and and_34 (ecall, not_200_out, not_201_out, not_202_out, OP6, OP5, OP4, not_203_out, not_204_out);
  and and_35 (and_35_out, not_205_out, F13, not_206_out, not_207_out, OP5, not_208_out, not_209_out, not_210_out);
  and and_36 (and_36_out, not_211_out, not_212_out, not_213_out, not_214_out, OP5, not_215_out, not_216_out, not_217_out);
  and and_37 (BEQ, not_218_out, not_219_out, not_220_out, OP6, OP5, not_221_out, not_222_out, not_223_out);
  and and_38 (BNE, not_224_out, not_225_out, F12, OP6, OP5, not_226_out, not_227_out, not_228_out);
  and and_39 (Jal, OP6, OP5, not_229_out, OP3, OP2);
  and and_40 (jalr, not_230_out, not_231_out, not_232_out, OP6, OP5, not_233_out, not_234_out, OP2);
  and and_41 (URET, not_235_out, not_236_out, not_237_out, OP6, OP5, OP4, not_238_out, not_239_out);
  and and_42 (LUI, not_240_out, OP5, OP4, not_241_out, OP2);
  and and_43 (SB, not_242_out, not_243_out, not_244_out, not_245_out, OP5, not_246_out, not_247_out, not_248_out);
  and and_44 (BGEU, F14, F13, F12, OP6, OP5, not_249_out, not_250_out, not_251_out);
  and and_45 (CSRRSI, F14, F13, not_252_out, OP6, OP5, OP4, not_253_out, not_254_out);
  and and_46 (CSRRCI, F14, F13, F12, OP6, OP5, OP4, not_255_out, not_256_out);
  or or_1 (MemWrite, and_2_out, and_3_out);
  or or_2 (S_Type, and_35_out, and_36_out);
  or or_3 (ALU_Src, and_4_out, and_5_out, and_6_out, and_7_out, and_8_out, and_9_out, and_10_out, and_11_out, and_12_out, and_13_out, and_14_out);
  or or_4 (RegWrite, and_15_out, and_16_out, and_17_out, and_18_out, and_19_out, and_20_out, and_21_out, and_22_out, and_23_out, and_24_out, and_25_out, and_26_out, and_27_out, and_28_out, and_29_out, and_30_out, and_31_out, and_32_out, and_33_out);
endmodule

// ALU
module ALU (
  input  [31:0] X,
  input  [31:0] Y,
  input  [3:0] AluOP,
  output out_4,
  output Equal,
  output out_6,
  output [31:0] Result,
  output [31:0] Result_2
);

  wire [0:0] comparator_1_lt, comparator_2_lt;
  wire [31:0] adder_1_out, AND_out, divider_1_out, divider_1_rem, multiplier_1_cout, multiplier_1_out,
       NOR_out, OR_out, shifter_1_out, shifter_2_out, shifter_3_out, subtractor_1_out, XOR_out;

  assign AND_out = X & Y;  // AND_Gate AND, 32 bits wide
  assign OR_out = X | Y;  // OR_Gate OR, 32 bits wide
  Shifter #(.width(32), .shift("ll")) shifter_1 (.in(X), .\dist (Y[4:0]), .out(shifter_1_out));
  Shifter #(.width(32), .shift("ar")) shifter_2 (.in(X), .\dist (Y[4:0]), .out(shifter_2_out));
  Shifter #(.width(32), .shift("lr")) shifter_3 (.in(X), .\dist (Y[4:0]), .out(shifter_3_out));
  Multiplier #(.width(32)) multiplier_1 (.a(X), .b(Y), .out(multiplier_1_out), .cout(multiplier_1_cout));  // open: cin
  Divider #(.width(32)) divider_1 (.a(X), .b(Y), .out(divider_1_out), .rem(divider_1_rem));  // open: upper
  Adder #(.width(32)) adder_1 (.a(X), .b(Y), .out(adder_1_out));  // open: cin, cout
  Subtractor #(.width(32)) subtractor_1 (.a(X), .b(Y), .out(subtractor_1_out));  // open: bin, bout
  assign XOR_out = X ^ Y;  // XOR_Gate XOR, 32 bits wide
  assign NOR_out = ~(X | Y);  // NOR_Gate NOR, 32 bits wide
  Comparator #(.width(32), .mode("twosComplement")) comparator_1 (
    .a(X), .b(Y), .eq(Equal), .lt(comparator_1_lt[0]));  // open: gt
  Comparator #(.width(32), .mode("unsigned")) comparator_2 (.a(X), .b(Y), .lt(comparator_2_lt[0]));  // open: gt, eq
  not not_1 (out_4, comparator_2_lt[0]);
  Multiplexer #(.select(4), .width(32), .disabled("Z"), .enable("false")) multiplexer_1 (
    .in0(shifter_1_out), .in1(shifter_2_out), .in2(shifter_3_out), .in3(multiplier_1_out),
    .in4(divider_1_out), .in5(adder_1_out), .in6(subtractor_1_out), .in7(AND_out), .in8(OR_out),
    .in9(XOR_out), .in10(NOR_out), .in11({{31{1'b0}}, comparator_1_lt[0]}),
    .in12({{31{1'b0}}, comparator_2_lt[0]}), .in13({32{1'b0}}), .in14({32{1'b0}}), .in15({32{1'b0}}),
    .out(Result), .sel(AluOP));
  Multiplexer #(.select(4), .width(32), .disabled("Z"), .enable("false")) multiplexer_2 (
    .in0({32{1'b0}}), .in1({32{1'b0}}), .in2({32{1'b0}}), .in3(multiplier_1_cout), .in4(divider_1_rem),
    .in5({32{1'b0}}), .in6({32{1'b0}}), .in7({32{1'b0}}), .in8({32{1'b0}}), .in9({32{1'b0}}),
    .in10({32{1'b0}}), .in11({32{1'b0}}), .in12({32{1'b0}}), .in13({32{1'b0}}), .in14({32{1'b0}}),
    .in15({32{1'b0}}), .out(Result_2), .sel(AluOP));
  Multiplexer #(.select(4), .width(1), .disabled("Z"), .enable("false")) multiplexer_3 (
    .in0(1'b0), .in1(1'b0), .in2(1'b0), .in3(1'b0), .in4(1'b0), .in5(1'b0), .in6(1'b0), .in7(1'b0),
    .in8(1'b0), .in9(1'b0), .in10(1'b0), .in11(comparator_1_lt[0]), .in12(comparator_2_lt[0]), .in13(1'b0),
    .in14(1'b0), .in15(1'b0), .out(out_6), .sel(AluOP));

  // Other names for the same wires on the sheet: Result2[31:0] = Result_2; S[3:0] = AluOP; tunnel = out_6;
  //   tunnel_t = out_4

  // Notes on the sheet:
  //   不要改变此引脚区域内容，也不要改变ALU封装形式
  //   输入引脚
  //   输出引脚
endmodule

module Regifile (
  input  [31:0] Din,
  input  Clk,
  input  WE,
  input  [4:0] R1_num,
  input  [4:0] W_num,
  input  [4:0] R2_num,
  output [31:0] R1,
  output [31:0] R2
);

  // RegisterFile registerfile_1: pin names not known; wires that end beside it: Din, Clk, WE, W_num, R1_num, R2_num, R1, R2
endmodule

module \理想流水线  (
  output RegWrite,
  output MemWrite,
  output [31:0] IF_PC,
  output [31:0] ID_PC,
  output [31:0] EX_PC,
  output [31:0] M_PC,
  output [31:0] WB_PC,
  output [31:0] RDin,
  output [31:0] MDin,
  output [31:0] LedData
);

  wire alu_1_equal, alu_1_out_4, and_1_out, and_2_out, and_3_out, and_4_out, and_5_out, branch, CLK,
       clock_1_out, clock_2_out, comparator_1_eq, comparator_2_eq, comparator_2_lt, d_ff_1_q, ecall,
       EX_MEM_out_17, EX_MEM_out_19, EX_MEM_out_20, EX_MEM_out_21, Go, halt, ID_EX_out_30, ID_EX_out_31,
       ID_EX_out_32, ID_EX_out_33, ID_EX_out_34, ID_EX_out_36, ID_EX_out_37, ID_EX_out_38, ID_EX_out_39, IR1,
       IR2, IR3, jal, jalr, MEM_WB_out_15, MEM_WB_out_17, nand_1_out, not_1_out, not_2_out, not_3_out,
       not_4_out, register_1_q, RST, run, W1, W2, W3, \单周期硬布线控制器_1_alu_src , \单周期硬布线控制器_1_beq ,
       \单周期硬布线控制器_1_bgeu , \单周期硬布线控制器_1_bne , \单周期硬布线控制器_1_ecall , \单周期硬布线控制器_1_lui , \单周期硬布线控制器_1_memtoreg ,
       \单周期硬布线控制器_1_memwrite , \单周期硬布线控制器_1_regwrite , \单周期硬布线控制器_1_s_type , \单周期硬布线控制器_1_sb ;
  wire [0:0] adder_2_out;
  wire [1:0] \byte , priority_encoder_1_out, priority_encoder_2_out;
  wire [3:0] decoder_1_out0, ID_EX_out_35, multiplexer_7_out, \单周期硬布线控制器_1_alu_op ;
  wire [4:0] EX_MEM_out_26, ID_EX_writereg_2, multiplexer_2_out, multiplexer_3_out, W_num;
  wire [11:0] multiplexer_4_out;
  wire [12:0] CNT_num;
  wire [15:0] \LoadUse次数 , \总周期数 , \插入气泡数 , \无条件分支数 , \条件分支成功数 ;
  wire [31:0] alu_1_result, B_dest, bit_extender_1_out, bit_extender_2_out, bit_extender_3_out,
       bit_extender_4_out, bit_extender_5_out, EX_IR, EX_MEM_out_25, EX_MEM_out_27, ID_EX_eb_2, ID_EX_ei_s_2,
       ID_EX_ej_2, ID_EX_eu_2, ID_IR, IF_ID_out_10, IF_IR, J_dest, MEM_IR, MEM_WB_out_20, MEM_WB_out_21,
       MEM_WB_out_23, mips_ram_1_p6, multiplexer_1_out, multiplexer_5_out, pc_4, R1, R2, regifile_1_r1,
       regifile_1_r2, sbdata, shifter_1_out, shifter_2_out, shifter_3_out, shifter_4_out, shifter_5_out,
       shifter_6_out, undriven, undriven_2, undriven_3, WB_IR;
  wire [31:1] I_dest;
  wire [31:2] EX_MEM_out_24;

  Button \u_总复位  (.out(RST));
  Button _1 (.out(IR1));
  Button _2 (.out(IR2));
  Button _3 (.out(IR3));
  // Probe on \总周期数 
  // Probe on \总周期数 
  Button \u_继续运行  (.out(Go));
  LED #(.active("true")) led_1 (.in(W1));
  LED #(.active("true")) led_2 (.in(W2));
  LED #(.active("true")) led_3 (.in(W3));
  Priority_Encoder #(.select(2), .disabled("Z")) priority_encoder_1 (
    .in0(1'b1), .in3(branch), .out(priority_encoder_1_out));  // open: in1, in2, gs, en_out, en_in
  Multiplexer #(.select(2), .width(32), .disabled("Z"), .enable("false")) multiplexer_1 (
    .in0(pc_4), .in1(J_dest), .in2({I_dest, 1'b0}), .in3(B_dest), .out(multiplexer_1_out),
    .sel(priority_encoder_1_out));
  not not_1 (not_1_out, halt);
  Register #(.width(1), .trigger("rising"), .Select("low")) register_1 (
    .D(and_2_out), .en(run), .Q(register_1_q), .clk(CLK));  // open: clr
  Hex_Digit_Display hex_digit_display_1 (.value(LedData[31:28]));  // open: dp
  // Probe on IF_PC[19:0]
  // RiscV_Probe riscv_probe_1: pin names not known; wires that end beside it: IF_IR
  Register #(.width(32), .trigger("rising"), .Select("low")) PC (
    .D(multiplexer_1_out), .en(run), .Q(IF_PC), .clk(CLK));  // open: clr
  or or_1 (run, Go, not_1_out);
  not not_2 (not_2_out, comparator_1_eq);
  Comparator #(.width(32), .mode("unsigned")) comparator_1 (.a(R2), .b(32'h22), .eq(comparator_1_eq));  // open: gt, lt
  Register #(.width(1), .trigger("rising"), .Select("low")) register_2 (
    .D(register_1_q), .en(run), .Q(halt), .clk(CLK));  // open: clr
  Hex_Digit_Display hex_digit_display_2 (.value(LedData[27:24]));  // open: dp
  Hex_Digit_Display hex_digit_display_3 (.value(LedData[23:20]));  // open: dp
  // Probe on ID_PC[19:0]
  // RiscV_Probe riscv_probe_2: pin names not known; wires that end beside it: ID_IR
  Adder #(.width(32)) adder_1 (.a(IF_PC), .b(32'h4), .out(pc_4));  // open: cin, cout
  and and_1 (and_1_out, ecall, comparator_1_eq);
  and and_2 (and_2_out, ecall, not_2_out);
  not not_3 (not_3_out, halt);
  Counter #(.width(16), .max('hffff), .ongoal("wrap"), .trigger("rising"), .behavior("new")) counter_1 (
    .count(not_3_out), .Q(\总周期数 ), .clk(CLK));  // open: load, D, carry, clr, preset, down
  Hex_Digit_Display hex_digit_display_4 (.value(LedData[15:12]));  // open: dp
  Hex_Digit_Display hex_digit_display_5 (.value(LedData[19:16]));  // open: dp
  Register #(.width(32), .trigger("rising"), .Select("low")) register_3 (
    .D(R1), .en(and_1_out), .Q(LedData), .clk(CLK));  // open: clr
  Hex_Digit_Display hex_digit_display_6 (.value(LedData[11:8]));  // open: dp
  Hex_Digit_Display hex_digit_display_7 (.value(LedData[7:4]));  // open: dp
  Clock #(.highDuration(1), .lowDuration(1)) clock_1 (.out(clock_1_out));
  // Probe on EX_PC[19:0]
  // RiscV_Probe riscv_probe_3: pin names not known; wires that end beside it: clock_1_out, EX_IR, CLK
  IF_ID IF_ID (
    .in_5(IF_IR), .out_10(IF_ID_out_10), .CLK(CLK), .in_4(IF_PC), .out_9(ID_PC), .in_7(IF_IR),
    .out_12(ID_IR), .run(run), .in_1(1'b0), .stall(1'b0));  // open: in_6, out_11
  ROM #(.addrWidth(10), .dataWidth(32), .Select("high")) rom_1 (.addr(IF_PC[11:2]), .data(IF_IR));
  Hex_Digit_Display hex_digit_display_8 (.value(LedData[3:0]));  // open: dp
  // Probe on \总周期数 
  // Probe on M_PC[19:0]
  // RiscV_Probe riscv_probe_4: pin names not known; wires that end beside it: MEM_IR
  \单周期硬布线控制器  \u_单周期硬布线控制器_1  (
    .Funct({IF_ID_out_10[30], IF_ID_out_10[25], IF_ID_out_10[14:12]}), .OP(IF_ID_out_10[6:2]),
    .ALU_OP(\单周期硬布线控制器_1_alu_op ), .MemToReg(\单周期硬布线控制器_1_memtoreg ), .MemWrite(\单周期硬布线控制器_1_memwrite ),
    .ALU_SRC(\单周期硬布线控制器_1_alu_src ), .RegWrite(\单周期硬布线控制器_1_regwrite ), .ecall(\单周期硬布线控制器_1_ecall ),
    .S_type(\单周期硬布线控制器_1_s_type ), .Beq(\单周期硬布线控制器_1_beq ), .JAL(jal), .Bne(\单周期硬布线控制器_1_bne ),
    .in_3(IF_ID_out_10[21]), .Jalr(jalr), .LUI(\单周期硬布线控制器_1_lui ), .SB(\单周期硬布线控制器_1_sb ),
    .BGEU(\单周期硬布线控制器_1_bgeu ));  // open: uret, CSRRSI, CSRRCI
  Multiplexer #(.select(1), .width(5), .disabled("Z"), .enable("false")) multiplexer_2 (
    .in0(IF_ID_out_10[19:15]), .in1(5'b01010), .out(multiplexer_2_out), .sel(\单周期硬布线控制器_1_ecall ));
  Multiplexer #(.select(1), .width(5), .disabled("Z"), .enable("false")) multiplexer_3 (
    .in0(IF_ID_out_10[24:20]), .in1(5'b10001), .out(multiplexer_3_out), .sel(\单周期硬布线控制器_1_ecall ));
  // Probe on \总周期数 
  // Probe on \无条件分支数 
  // Probe on \条件分支成功数 
  // Probe on \插入气泡数 
  // Probe on \LoadUse次数 
  Multiplexer #(.select(1), .width(12), .disabled("Z"), .enable("false")) multiplexer_4 (
    .in0(IF_ID_out_10[31:20]), .in1({IF_ID_out_10[31:25], IF_ID_out_10[11:7]}), .out(multiplexer_4_out),
    .sel(\单周期硬布线控制器_1_s_type ));
  assign bit_extender_1_out = {{20{IF_ID_out_10[31]}}, {IF_ID_out_10[31], IF_ID_out_10[7], IF_ID_out_10[30:25], IF_ID_out_10[11:8]}};  // Bit_Extender bit_extender_1
  assign bit_extender_2_out = {{12{IF_ID_out_10[31]}}, {IF_ID_out_10[31], IF_ID_out_10[19:12], IF_ID_out_10[20], IF_ID_out_10[30:21]}};  // Bit_Extender bit_extender_2
  assign bit_extender_3_out = {{12{IF_ID_out_10[31]}}, IF_ID_out_10[31:12]};  // Bit_Extender bit_extender_3
  // Probe on IF_PC[11:0]
  // Probe on WB_PC[19:0]
  // RiscV_Probe riscv_probe_5: pin names not known; wires that end beside it: WB_IR
  Regifile regifile_1 (
    .Din(RDin), .Clk(CLK), .R1(regifile_1_r1), .R2(regifile_1_r2), .WE(RegWrite), .W_num(W_num),
    .R1_num(multiplexer_2_out), .R2_num(multiplexer_3_out));
  assign bit_extender_4_out = {{20{multiplexer_4_out[11]}}, multiplexer_4_out};  // Bit_Extender bit_extender_4
  // Probe on ID_PC[11:0]
  // Probe on EX_PC[11:0]
  ID_EX ID_EX (
    .Beq(\单周期硬布线控制器_1_beq ), .Bne(\单周期硬布线控制器_1_bne ), .Bgeu(\单周期硬布线控制器_1_bgeu ),
    .MemToReg(\单周期硬布线控制器_1_memtoreg ), .MemWrite(\单周期硬布线控制器_1_memwrite ), .AluOP(\单周期硬布线控制器_1_alu_op ),
    .AluSrcB(\单周期硬布线控制器_1_alu_src ), .RegWrite(\单周期硬布线控制器_1_regwrite ), .LUI(\单周期硬布线控制器_1_lui ),
    .Sb(\单周期硬布线控制器_1_sb ), .CLK(CLK), .R1(regifile_1_r1), .R2(regifile_1_r2), .WriteReg(IF_ID_out_10[11:7]),
    .R1_2(R1), .R2_2(R2), .WriteReg_2(ID_EX_writereg_2), .out_30(ID_EX_out_30), .out_31(ID_EX_out_31),
    .out_32(ID_EX_out_32), .out_33(ID_EX_out_33), .out_36(ID_EX_out_36), .out_37(ID_EX_out_37),
    .out_38(ID_EX_out_38), .out_39(ID_EX_out_39), .out_34(ID_EX_out_34), .out_35(ID_EX_out_35), .pc(ID_PC),
    .pc_2(EX_PC), .EB(bit_extender_1_out), .EJ(bit_extender_2_out), .EU(bit_extender_3_out),
    .EB_2(ID_EX_eb_2), .EJ_2(ID_EX_ej_2), .EU_2(ID_EX_eu_2), .EI_S(bit_extender_4_out),
    .EI_S_2(ID_EX_ei_s_2), .jal(jal), .ir(ID_IR), .ir_2(EX_IR), .ecall(\单周期硬布线控制器_1_ecall ), .out_42(ecall),
    .run(run), .in_1(1'b0), .jalr(jalr));  // open: out_40, out_41, out_43, r1src, out_45, r2src, pred, pred_2, uret, uret_2
  // Probe on M_PC[11:0]
  D_Flip_Flop #(.trigger("high"), .Pre_Clr_Positions("LEGACY"), .NegatePresetClear("false"), .enable("true"), .NewFFLayout("false")) d_ff_1 (.Q(d_ff_1_q));  // open: clk, D, Qn, preset, en, reset
  // Probe on 13'h13
  Multiplexer #(.select(1), .width(32), .disabled("Z"), .enable("false")) multiplexer_5 (
    .in0(R2), .in1(ID_EX_ei_s_2), .out(multiplexer_5_out), .sel(ID_EX_out_36));
  // Probe on WB_PC[11:0]
  Comparator #(.width(13), .mode("twosComplement")) comparator_2 (
    .a(CNT_num), .b(13'h13), .eq(comparator_2_eq), .lt(comparator_2_lt));  // open: gt
  Clock #(.highDuration(1), .lowDuration(1)) clock_2 (.out(clock_2_out));
  not not_4 (not_4_out, alu_1_equal);
  ALU alu_1 (
    .X(R1), .Y(multiplexer_5_out), .AluOP(ID_EX_out_35), .Equal(alu_1_equal), .Result(alu_1_result),
    .out_4(alu_1_out_4));  // open: Result_2, out_6
  Adder #(.width(32)) adder_2 (.a(ID_EX_ei_s_2), .b(undriven), .out({I_dest, adder_2_out[0]}));  // open: cin, cout
  Shifter #(.width(32), .shift("ll")) shifter_1 (.in(ID_EX_eb_2), .\dist (5'b00001), .out(shifter_1_out));
  Shifter #(.width(32), .shift("ll")) shifter_2 (.in(ID_EX_ej_2), .\dist (5'b00001), .out(shifter_2_out));
  Shifter #(.width(32), .shift("ll")) shifter_3 (.in(ID_EX_eu_2), .\dist (5'b01100), .out(shifter_3_out));
  nand nand_1 (nand_1_out, d_ff_1_q, comparator_2_eq);
  Counter #(.width(13), .max('h1fff), .ongoal("stay"), .trigger("rising"), .behavior("old")) counter_2 (
    .count(comparator_2_lt), .Q(CNT_num), .clk(clock_2_out));  // open: load, D, carry, clr, preset
  and and_3 (and_3_out, ID_EX_out_30, alu_1_equal);
  and and_4 (and_4_out, ID_EX_out_31, not_4_out);
  and and_5 (and_5_out, ID_EX_out_32, alu_1_out_4);
  Adder #(.width(32)) adder_3 (.a(shifter_1_out), .b(undriven_2), .out(B_dest));  // open: cin, cout
  Adder #(.width(32)) adder_4 (.a(shifter_2_out), .b(undriven_3), .out(J_dest));  // open: cin, cout
  assign CLK = nand_1_out ? clock_2_out : 1'bz;  // Controlled_Buffer controlled_buffer_1
  or or_2 (branch, and_3_out, and_4_out, and_5_out);
  Pull_Resistor #(.pull(1)) pull_resistor_1 (.node(CLK));
  EX_MEM EX_MEM (
    .MemToReg(ID_EX_out_33), .MemWrite(ID_EX_out_34), .out_17(EX_MEM_out_17), .out_18(MemWrite),
    .RegWrite(ID_EX_out_37), .out_19(EX_MEM_out_19), .LUI(ID_EX_out_38), .out_20(EX_MEM_out_20),
    .Sb(ID_EX_out_39), .out_21(EX_MEM_out_21), .Alu(alu_1_result), .out_24({EX_MEM_out_24, \byte }), .R2(R2),
    .out_25(EX_MEM_out_25), .udata(shifter_3_out), .out_27(EX_MEM_out_27), .pc(EX_PC), .out_28(M_PC),
    .ir(EX_IR), .out_29(MEM_IR), .CLK(CLK), .in_11(ID_EX_writereg_2), .out_26(EX_MEM_out_26), .run(run),
    .in_1(1'b0));  // open: jal, out_22, jalr, out_23
  Multiplexer #(.select(1), .width(32), .disabled("Z"), .enable("false")) multiplexer_6 (
    .in0(EX_MEM_out_25), .in1(sbdata), .out(MDin), .sel(EX_MEM_out_21));
  Decoder #(.select(2), .tristate("false"), .disabled("Z"), .enable("false")) decoder_1 (
    .out0(decoder_1_out0[0]), .out1(decoder_1_out0[1]), .out2(decoder_1_out0[2]), .out3(decoder_1_out0[3]),
    .sel(\byte ));
  assign bit_extender_5_out = {{24{1'b0}}, EX_MEM_out_25[7:0]};  // Bit_Extender bit_extender_5
  Shifter #(.width(32), .shift("ll")) shifter_4 (.in(bit_extender_5_out), .\dist (5'b01000), .out(shifter_4_out));
  Shifter #(.width(32), .shift("ll")) shifter_5 (.in(bit_extender_5_out), .\dist (5'b10000), .out(shifter_5_out));
  Shifter #(.width(32), .shift("ll")) shifter_6 (.in(bit_extender_5_out), .\dist (5'b11000), .out(shifter_6_out));
  Multiplexer #(.select(1), .width(4), .disabled("Z"), .enable("false")) multiplexer_7 (
    .in0(4'b1111), .in1(decoder_1_out0), .out(multiplexer_7_out), .sel(EX_MEM_out_21));
  Multiplexer #(.select(2), .width(32), .disabled("Z"), .enable("false")) multiplexer_8 (
    .in0(bit_extender_5_out), .in1(shifter_4_out), .in2(shifter_5_out), .in3(shifter_6_out), .out(sbdata),
    .sel(\byte ));
  // MIPS_RAM mips_ram_1: pin names not known; wires that end beside it: EX_MEM_out_24[11:2], MDin, MemWrite, multiplexer_7_out, CLK, mips_ram_1_p6
  MEM_WB MEM_WB (
    .in_2(EX_MEM_out_17), .out_15(MEM_WB_out_15), .in_3(EX_MEM_out_19), .out_16(RegWrite),
    .in_4(EX_MEM_out_20), .out_17(MEM_WB_out_17), .in_7({EX_MEM_out_24, \byte }), .out_20(MEM_WB_out_20),
    .in_8(mips_ram_1_p6), .out_21(MEM_WB_out_21), .in_10(EX_MEM_out_27), .out_23(MEM_WB_out_23),
    .in_9(EX_MEM_out_26), .out_22(W_num), .in_11(M_PC), .out_24(WB_PC), .in_12(MEM_IR), .out_25(WB_IR),
    .CLK(CLK), .run(run), .in_1(1'b0));  // open: in_5, out_18, in_6, out_19
  Priority_Encoder #(.select(2), .disabled("Z")) priority_encoder_2 (
    .in0(1'b1), .in1(MEM_WB_out_15), .in3(MEM_WB_out_17), .out(priority_encoder_2_out));  // open: in2, gs, en_out, en_in
  Multiplexer #(.select(2), .width(32), .disabled("Z"), .enable("false")) multiplexer_9 (
    .in0(MEM_WB_out_20), .in1(MEM_WB_out_21), .in3(MEM_WB_out_23), .out(RDin), .sel(priority_encoder_2_out));  // open: in2

  // Other names for the same wires on the sheet: MEM_PC[31:0] = M_PC

  // Notes on the sheet:
  //   中断源
  //   时空图监测，可删除
  //   中断等待指示
  //   数码管输出
  //   contents of rom_1 (hex, n*v repeats v):
  //   413 493 913 993 46413 14e493 296913 39e993 842023 942223 1242423 1342623 a00893 493 913 993 73
  //   I
  //   S
  //   Beq
  //   Bne
  //   Bgeu
  //   MemToReg
  //   MemWrite
  //   AluOP
  //   AluSrcB
  //   Regwrite
  //   Lui
  //   Sb
  //   Ecall
  //   B
  //   J
  //   控制位
  //   流水调试日志用
  //   暂停节拍，不能为0
  //   戳工具置1进入计数暂停模式，ctrl+k时钟自动运行到对应节拍暂停
  //   ctrl+k关闭时钟连续运行，将控制位置零，进入单步调试模式调试
  //   用这个时钟源需要去掉电路中的其他时钟源
  //   可计数暂停的时钟源
  //   为方便自动评测，需要输出流水线各段保存的PC值，注意是PC不是PC+4，另外ID段寄存器写入信息，Mem段内存写入信息也要输出
endmodule

module \气泡流水线  (
  output RegWrite,
  output MemWrite,
  output [31:0] IF_PC,
  output [31:0] ID_PC,
  output [31:0] EX_PC,
  output [31:0] M_PC,
  output [31:0] WB_PC,
  output [31:0] RDin,
  output [31:0] MDin,
  output [31:0] LedData
);

  wire alu_1_equal, alu_1_out_4, and_1_out, and_2_out, and_3_out, and_4_out, and_5_out, and_6_out, branch,
       bubblecontrol_1_branchtaken, bubblecontrol_1_exflush, bubblecontrol_1_jal_2, bubblecontrol_1_jalr_2,
       bubblecontrol_1_stall, CLK, clock_1_out, clock_2_out, comparator_1_eq, comparator_2_eq,
       comparator_2_lt, d_ff_1_q, ecall, EX_MEM_out_17, EX_MEM_out_19, EX_MEM_out_20, EX_MEM_out_21,
       EX_MEM_out_22, EX_MEM_out_23, Go, halt, ID_EX_out_30, ID_EX_out_31, ID_EX_out_32, ID_EX_out_33,
       ID_EX_out_34, ID_EX_out_36, ID_EX_out_37, ID_EX_out_38, ID_EX_out_39, ID_EX_out_40, ID_EX_out_41, IR1,
       IR2, IR3, jal, jalr, MEM_WB_out_15, MEM_WB_out_17, MEM_WB_out_18, MEM_WB_out_19, nand_1_out,
       not_1_out, not_2_out, not_3_out, not_4_out, not_5_out, or_3_out, register_1_q, RST, run, W1, W2, W3,
       \单周期硬布线控制器_1_alu_src , \单周期硬布线控制器_1_beq , \单周期硬布线控制器_1_bgeu , \单周期硬布线控制器_1_bne , \单周期硬布线控制器_1_ecall ,
       \单周期硬布线控制器_1_lui , \单周期硬布线控制器_1_memtoreg , \单周期硬布线控制器_1_memwrite , \单周期硬布线控制器_1_regwrite ,
       \单周期硬布线控制器_1_s_type , \单周期硬布线控制器_1_sb ;
  wire [0:0] adder_2_out;
  wire [1:0] \byte , priority_encoder_1_out, priority_encoder_2_out;
  wire [3:0] decoder_1_out0, ID_EX_out_35, multiplexer_7_out, \单周期硬布线控制器_1_alu_op ;
  wire [4:0] EX_MEM_out_26, ID_EX_writereg_2, multiplexer_2_out, multiplexer_3_out, W_num;
  wire [11:0] multiplexer_4_out;
  wire [12:0] CNT_num;
  wire [15:0] \LoadUse次数 , \总周期数 , \插入气泡数 , \无条件分支数 , \条件分支成功数 ;
  wire [31:0] adder_5_out, alu_1_result, B_dest, bit_extender_1_out, bit_extender_2_out, bit_extender_3_out,
       bit_extender_4_out, bit_extender_5_out, EX_IR, EX_MEM_out_25, EX_MEM_out_27, ID_EX_eb_2, ID_EX_ei_s_2,
       ID_EX_ej_2, ID_EX_eu_2, ID_IR, IF_ID_out_10, IF_IR, J_dest, MEM_IR, MEM_WB_out_20, MEM_WB_out_21,
       MEM_WB_out_23, mips_ram_1_p6, multiplexer_1_out, multiplexer_5_out, pc_4, R1, R2, regifile_1_r1,
       regifile_1_r2, sbdata, shifter_1_out, shifter_2_out, shifter_3_out, shifter_4_out, shifter_5_out,
       shifter_6_out, WB_IR;
  wire [31:1] I_dest;
  wire [31:2] EX_MEM_out_24;

  Button \u_总复位  (.out(RST));
  Button _1 (.out(IR1));
  Button _2 (.out(IR2));
  Button _3 (.out(IR3));
  // Probe on \总周期数 
  // Probe on \总周期数 
  Button \u_继续运行  (.out(Go));
  LED #(.active("true")) led_1 (.in(W1));
  LED #(.active("true")) led_2 (.in(W2));
  LED #(.active("true")) led_3 (.in(W3));
  Hex_Digit_Display hex_digit_display_1 (.value(LedData[31:28]));  // open: dp
  // Probe on IF_PC[19:0]
  // RiscV_Probe riscv_probe_1: pin names not known; wires that end beside it: IF_IR
  not not_1 (not_1_out, bubblecontrol_1_stall);
  Priority_Encoder #(.select(2), .disabled("Z")) priority_encoder_1 (
    .in0(1'b1), .in1(bubblecontrol_1_jal_2), .in2(bubblecontrol_1_jalr_2), .in3(branch),
    .out(priority_encoder_1_out));  // open: gs, en_out, en_in
  Multiplexer #(.select(2), .width(32), .disabled("Z"), .enable("false")) multiplexer_1 (
    .in0(pc_4), .in1(J_dest), .in2({I_dest, 1'b0}), .in3(B_dest), .out(multiplexer_1_out),
    .sel(priority_encoder_1_out));
  Hex_Digit_Display hex_digit_display_2 (.value(LedData[27:24]));  // open: dp
  Hex_Digit_Display hex_digit_display_3 (.value(LedData[23:20]));  // open: dp
  // Probe on ID_PC[19:0]
  // RiscV_Probe riscv_probe_2: pin names not known; wires that end beside it: ID_IR
  Register #(.width(32), .trigger("rising"), .Select("low")) PC (
    .D(multiplexer_1_out), .en(and_1_out), .Q(IF_PC), .clk(CLK));  // open: clr
  and and_1 (and_1_out, not_1_out, run);
  or or_1 (run, Go, not_2_out);
  not not_2 (not_2_out, halt);
  Comparator #(.width(32), .mode("unsigned")) comparator_1 (.a(R2), .b(32'h22), .eq(comparator_1_eq));  // open: gt, lt
  Register #(.width(1), .trigger("rising"), .Select("low")) register_1 (
    .D(and_3_out), .en(run), .Q(register_1_q), .clk(CLK));  // open: clr
  Hex_Digit_Display hex_digit_display_4 (.value(LedData[19:16]));  // open: dp
  Hex_Digit_Display hex_digit_display_5 (.value(LedData[15:12]));  // open: dp
  Adder #(.width(32)) adder_1 (.a(IF_PC), .b(32'h4), .out(pc_4));  // open: cin, cout
  not not_3 (not_3_out, comparator_1_eq);
  Register #(.width(1), .trigger("rising"), .Select("low")) register_2 (
    .D(register_1_q), .en(run), .Q(halt), .clk(CLK));  // open: clr
  Hex_Digit_Display hex_digit_display_6 (.value(LedData[7:4]));  // open: dp
  Hex_Digit_Display hex_digit_display_7 (.value(LedData[11:8]));  // open: dp
  Clock #(.highDuration(1), .lowDuration(1)) clock_1 (.out(clock_1_out));
  // Probe on EX_PC[19:0]
  // RiscV_Probe riscv_probe_3: pin names not known; wires that end beside it: clock_1_out, EX_IR, CLK
  and and_2 (and_2_out, ecall, comparator_1_eq);
  and and_3 (and_3_out, ecall, not_3_out);
  not not_4 (not_4_out, halt);
  Counter #(.width(16), .max('hffff), .ongoal("wrap"), .trigger("rising"), .behavior("new")) counter_1 (
    .count(not_4_out), .Q(\总周期数 ), .clk(CLK));  // open: load, D, carry, clr, preset, down
  Hex_Digit_Display hex_digit_display_8 (.value(LedData[3:0]));  // open: dp
  ROM #(.addrWidth(10), .dataWidth(32), .Select("high")) rom_1 (.addr(IF_PC[11:2]), .data(IF_IR));
  Register #(.width(32), .trigger("rising"), .Select("low")) register_3 (
    .D(R1), .en(and_2_out), .Q(LedData), .clk(CLK));  // open: clr
  // Probe on \总周期数 
  // Probe on M_PC[19:0]
  // RiscV_Probe riscv_probe_4: pin names not known; wires that end beside it: MEM_IR
  IF_ID IF_ID (
    .in_5(IF_IR), .out_10(IF_ID_out_10), .CLK(CLK), .in_4(IF_PC), .out_9(ID_PC), .in_7(IF_IR),
    .out_12(ID_IR), .run(run), .in_1(bubblecontrol_1_branchtaken), .stall(bubblecontrol_1_stall));  // open: in_6, out_11
  // Probe on \总周期数 
  // Probe on \无条件分支数 
  // Probe on \条件分支成功数 
  // Probe on \插入气泡数 
  // Probe on \LoadUse次数 
  // Probe on IF_PC[11:0]
  // Probe on WB_PC[19:0]
  // RiscV_Probe riscv_probe_5: pin names not known; wires that end beside it: WB_IR
  \单周期硬布线控制器  \u_单周期硬布线控制器_1  (
    .Funct({IF_ID_out_10[30], IF_ID_out_10[25], IF_ID_out_10[14:12]}), .OP(IF_ID_out_10[6:2]),
    .ALU_OP(\单周期硬布线控制器_1_alu_op ), .MemToReg(\单周期硬布线控制器_1_memtoreg ), .MemWrite(\单周期硬布线控制器_1_memwrite ),
    .ALU_SRC(\单周期硬布线控制器_1_alu_src ), .RegWrite(\单周期硬布线控制器_1_regwrite ), .ecall(\单周期硬布线控制器_1_ecall ),
    .S_type(\单周期硬布线控制器_1_s_type ), .Beq(\单周期硬布线控制器_1_beq ), .JAL(jal), .Bne(\单周期硬布线控制器_1_bne ),
    .in_3(IF_ID_out_10[21]), .Jalr(jalr), .LUI(\单周期硬布线控制器_1_lui ), .SB(\单周期硬布线控制器_1_sb ),
    .BGEU(\单周期硬布线控制器_1_bgeu ));  // open: uret, CSRRSI, CSRRCI
  Multiplexer #(.select(1), .width(5), .disabled("Z"), .enable("false")) multiplexer_2 (
    .in0(IF_ID_out_10[19:15]), .in1(5'b01010), .out(multiplexer_2_out), .sel(\单周期硬布线控制器_1_ecall ));
  Multiplexer #(.select(1), .width(5), .disabled("Z"), .enable("false")) multiplexer_3 (
    .in0(IF_ID_out_10[24:20]), .in1(5'b10001), .out(multiplexer_3_out), .sel(\单周期硬布线控制器_1_ecall ));
  // Probe on EX_PC[11:0]
  // Probe on ID_PC[11:0]
  Multiplexer #(.select(1), .width(12), .disabled("Z"), .enable("false")) multiplexer_4 (
    .in0(IF_ID_out_10[31:20]), .in1({IF_ID_out_10[31:25], IF_ID_out_10[11:7]}), .out(multiplexer_4_out),
    .sel(\单周期硬布线控制器_1_s_type ));
  assign bit_extender_1_out = {{20{IF_ID_out_10[31]}}, {IF_ID_out_10[31], IF_ID_out_10[7], IF_ID_out_10[30:25], IF_ID_out_10[11:8]}};  // Bit_Extender bit_extender_1
  assign bit_extender_2_out = {{12{IF_ID_out_10[31]}}, {IF_ID_out_10[31], IF_ID_out_10[19:12], IF_ID_out_10[20], IF_ID_out_10[30:21]}};  // Bit_Extender bit_extender_2
  assign bit_extender_3_out = {{12{IF_ID_out_10[31]}}, IF_ID_out_10[31:12]};  // Bit_Extender bit_extender_3
  // Probe on M_PC[11:0]
  D_Flip_Flop #(.trigger("high"), .Pre_Clr_Positions("LEGACY"), .NegatePresetClear("false"), .enable("true"), .NewFFLayout("false")) d_ff_1 (.Q(d_ff_1_q));  // open: clk, D, Qn, preset, en, reset
  // Probe on 13'h13
  BubbleControl bubblecontrol_1 (
    .jal_2(bubblecontrol_1_jal_2), .jalr_2(bubblecontrol_1_jalr_2), .jal(ID_EX_out_40), .jalr(ID_EX_out_41),
    .branch(branch), .stall(bubblecontrol_1_stall), .inst(IF_ID_out_10), .EXflush(bubblecontrol_1_exflush),
    .EXW_num(ID_EX_writereg_2), .MEMW_num(EX_MEM_out_26), .EXRW(ID_EX_out_37), .MEMRW(EX_MEM_out_19),
    .halt(halt), .\无条件分支 (\无条件分支数 ), .\条件分支 (\条件分支成功数 ), .\气泡 (\插入气泡数 ),
    .branchtaken(bubblecontrol_1_branchtaken), .clk(CLK), .ecall(\单周期硬布线控制器_1_ecall ),
    .in_8(\单周期硬布线控制器_1_alu_src ));
  Regifile regifile_1 (
    .Din(RDin), .Clk(CLK), .R1(regifile_1_r1), .R2(regifile_1_r2), .WE(RegWrite), .W_num(W_num),
    .R1_num(multiplexer_2_out), .R2_num(multiplexer_3_out));
  assign bit_extender_4_out = {{20{multiplexer_4_out[11]}}, multiplexer_4_out};  // Bit_Extender bit_extender_4
  // Probe on WB_PC[11:0]
  Comparator #(.width(13), .mode("twosComplement")) comparator_2 (
    .a(CNT_num), .b(13'h13), .eq(comparator_2_eq), .lt(comparator_2_lt));  // open: gt
  Clock #(.highDuration(1), .lowDuration(1)) clock_2 (.out(clock_2_out));
  ID_EX ID_EX (
    .Beq(\单周期硬布线控制器_1_beq ), .Bne(\单周期硬布线控制器_1_bne ), .Bgeu(\单周期硬布线控制器_1_bgeu ),
    .MemToReg(\单周期硬布线控制器_1_memtoreg ), .MemWrite(\单周期硬布线控制器_1_memwrite ), .AluOP(\单周期硬布线控制器_1_alu_op ),
    .AluSrcB(\单周期硬布线控制器_1_alu_src ), .RegWrite(\单周期硬布线控制器_1_regwrite ), .LUI(\单周期硬布线控制器_1_lui ),
    .Sb(\单周期硬布线控制器_1_sb ), .CLK(CLK), .R1(regifile_1_r1), .R2(regifile_1_r2), .WriteReg(IF_ID_out_10[11:7]),
    .R1_2(R1), .R2_2(R2), .WriteReg_2(ID_EX_writereg_2), .out_30(ID_EX_out_30), .out_31(ID_EX_out_31),
    .out_32(ID_EX_out_32), .out_33(ID_EX_out_33), .out_36(ID_EX_out_36), .out_37(ID_EX_out_37),
    .out_38(ID_EX_out_38), .out_39(ID_EX_out_39), .out_34(ID_EX_out_34), .out_35(ID_EX_out_35), .pc(ID_PC),
    .pc_2(EX_PC), .EB(bit_extender_1_out), .EJ(bit_extender_2_out), .EU(bit_extender_3_out),
    .EB_2(ID_EX_eb_2), .EJ_2(ID_EX_ej_2), .EU_2(ID_EX_eu_2), .EI_S(bit_extender_4_out),
    .EI_S_2(ID_EX_ei_s_2), .out_40(ID_EX_out_40), .jal(jal), .ir(ID_IR), .ir_2(EX_IR),
    .ecall(\单周期硬布线控制器_1_ecall ), .out_42(ecall), .run(run), .in_1(bubblecontrol_1_exflush), .jalr(jalr),
    .out_41(ID_EX_out_41));  // open: out_43, r1src, out_45, r2src, pred, pred_2, uret, uret_2
  nand nand_1 (nand_1_out, d_ff_1_q, comparator_2_eq);
  Counter #(.width(13), .max('h1fff), .ongoal("stay"), .trigger("rising"), .behavior("old")) counter_2 (
    .count(comparator_2_lt), .Q(CNT_num), .clk(clock_2_out));  // open: load, D, carry, clr, preset
  Multiplexer #(.select(1), .width(32), .disabled("Z"), .enable("false")) multiplexer_5 (
    .in0(R2), .in1(ID_EX_ei_s_2), .out(multiplexer_5_out), .sel(ID_EX_out_36));
  Shifter #(.width(32), .shift("ll")) shifter_1 (.in(ID_EX_eb_2), .\dist (5'b00001), .out(shifter_1_out));
  Shifter #(.width(32), .shift("ll")) shifter_2 (.in(ID_EX_ej_2), .\dist (5'b00001), .out(shifter_2_out));
  Shifter #(.width(32), .shift("ll")) shifter_3 (.in(ID_EX_eu_2), .\dist (5'b01100), .out(shifter_3_out));
  assign CLK = nand_1_out ? clock_2_out : 1'bz;  // Controlled_Buffer controlled_buffer_1
  not not_5 (not_5_out, alu_1_equal);
  ALU alu_1 (
    .X(R1), .Y(multiplexer_5_out), .AluOP(ID_EX_out_35), .Equal(alu_1_equal), .Result(alu_1_result),
    .out_4(alu_1_out_4));  // open: Result_2, out_6
  Adder #(.width(32)) adder_2 (.a(ID_EX_ei_s_2), .b(R1), .out({I_dest, adder_2_out[0]}));  // open: cin, cout
  Pull_Resistor #(.pull(1)) pull_resistor_1 (.node(CLK));
  and and_4 (and_4_out, ID_EX_out_30, alu_1_equal);
  or or_2 (branch, and_4_out, and_5_out, and_6_out);
  and and_5 (and_5_out, ID_EX_out_31, not_5_out);
  and and_6 (and_6_out, ID_EX_out_32, alu_1_out_4);
  Adder #(.width(32)) adder_3 (.a(shifter_1_out), .b(EX_PC), .out(B_dest));  // open: cin, cout
  Adder #(.width(32)) adder_4 (.a(shifter_2_out), .b(EX_PC), .out(J_dest));  // open: cin, cout
  EX_MEM EX_MEM (
    .MemToReg(ID_EX_out_33), .MemWrite(ID_EX_out_34), .out_17(EX_MEM_out_17), .out_18(MemWrite),
    .RegWrite(ID_EX_out_37), .out_19(EX_MEM_out_19), .LUI(ID_EX_out_38), .out_20(EX_MEM_out_20),
    .Sb(ID_EX_out_39), .out_21(EX_MEM_out_21), .Alu(alu_1_result), .out_24({EX_MEM_out_24, \byte }), .R2(R2),
    .out_25(EX_MEM_out_25), .udata(shifter_3_out), .out_27(EX_MEM_out_27), .pc(EX_PC), .out_28(M_PC),
    .ir(EX_IR), .out_29(MEM_IR), .CLK(CLK), .in_11(ID_EX_writereg_2), .out_26(EX_MEM_out_26), .run(run),
    .in_1(1'b0), .jal(ID_EX_out_40), .out_22(EX_MEM_out_22), .jalr(ID_EX_out_41), .out_23(EX_MEM_out_23));
  Multiplexer #(.select(1), .width(32), .disabled("Z"), .enable("false")) multiplexer_6 (
    .in0(EX_MEM_out_25), .in1(sbdata), .out(MDin), .sel(EX_MEM_out_21));
  Decoder #(.select(2), .tristate("false"), .disabled("Z"), .enable("false")) decoder_1 (
    .out0(decoder_1_out0[0]), .out1(decoder_1_out0[1]), .out2(decoder_1_out0[2]), .out3(decoder_1_out0[3]),
    .sel(\byte ));
  assign bit_extender_5_out = {{24{1'b0}}, EX_MEM_out_25[7:0]};  // Bit_Extender bit_extender_5
  Multiplexer #(.select(1), .width(4), .disabled("Z"), .enable("false")) multiplexer_7 (
    .in0(4'b1111), .in1(decoder_1_out0), .out(multiplexer_7_out), .sel(EX_MEM_out_21));
  Shifter #(.width(32), .shift("ll")) shifter_4 (.in(bit_extender_5_out), .\dist (5'b01000), .out(shifter_4_out));
  Shifter #(.width(32), .shift("ll")) shifter_5 (.in(bit_extender_5_out), .\dist (5'b10000), .out(shifter_5_out));
  Shifter #(.width(32), .shift("ll")) shifter_6 (.in(bit_extender_5_out), .\dist (5'b11000), .out(shifter_6_out));
  Multiplexer #(.select(2), .width(32), .disabled("Z"), .enable("false")) multiplexer_8 (
    .in0(bit_extender_5_out), .in1(shifter_4_out), .in2(shifter_5_out), .in3(shifter_6_out), .out(sbdata),
    .sel(\byte ));
  // MIPS_RAM mips_ram_1: pin names not known; wires that end beside it: EX_MEM_out_24[11:2], MDin, MemWrite, multiplexer_7_out, CLK, mips_ram_1_p6
  MEM_WB MEM_WB (
    .in_2(EX_MEM_out_17), .out_15(MEM_WB_out_15), .in_3(EX_MEM_out_19), .out_16(RegWrite),
    .in_4(EX_MEM_out_20), .out_17(MEM_WB_out_17), .in_7({EX_MEM_out_24, \byte }), .out_20(MEM_WB_out_20),
    .in_8(mips_ram_1_p6), .out_21(MEM_WB_out_21), .in_10(EX_MEM_out_27), .out_23(MEM_WB_out_23),
    .in_9(EX_MEM_out_26), .out_22(W_num), .in_11(M_PC), .out_24(WB_PC), .in_12(MEM_IR), .out_25(WB_IR),
    .CLK(CLK), .run(run), .in_1(1'b0), .in_5(EX_MEM_out_22), .out_18(MEM_WB_out_18), .in_6(EX_MEM_out_23),
    .out_19(MEM_WB_out_19));
  or or_3 (or_3_out, MEM_WB_out_18, MEM_WB_out_19);
  Adder #(.width(32)) adder_5 (.a(WB_PC), .b(32'h4), .out(adder_5_out));  // open: cin, cout
  Priority_Encoder #(.select(2), .disabled("Z")) priority_encoder_2 (
    .in0(1'b1), .in1(MEM_WB_out_15), .in2(or_3_out), .in3(MEM_WB_out_17), .out(priority_encoder_2_out));  // open: gs, en_out, en_in
  Multiplexer #(.select(2), .width(32), .disabled("Z"), .enable("false")) multiplexer_9 (
    .in0(MEM_WB_out_20), .in1(MEM_WB_out_21), .in2(adder_5_out), .in3(MEM_WB_out_23), .out(RDin),
    .sel(priority_encoder_2_out));

  // Other names for the same wires on the sheet: MEM_PC[31:0] = M_PC

  // Notes on the sheet:
  //   中断源
  //   时空图监测，可删除
  //   中断等待指示
  //   数码管输出
  //   contents of rom_1 (hex, n*v repeats v):
  //   100493 100006f 100493 200913 300993 100006f 100493 200913 300993 100006f 100493 200913 300993
  //   100006f 100493 200913 300993 3bc000ef 100413 100493 1f49493 900533 2200893 73 24d493 48463 fedff06f
  //   900533 2200893 73 100493 249493 900533 2200893 73 48463 fedff06f 100493 1f49493 900533 2200893 73
  //   4034d493 900533 2200893 73 4044d493 900533 2200893 73 4044d493 900533 2200893 73 4044d493 900533
  //   2200893 73 4044d493 900533 2200893 73 4044d493 900533 2200893 73 4044d493 900533 2200893 73 4044d493
  //   900533 2200893 73 100413 1f41993 41f9d993 433 c00913 300b13 140413 f47413 800293 100313 499993
  //   89e9b3 1300533 2200893 73 406282b3 fe0294e3 140413 f00f93 1f47433 1c41413 800293 100313 49d993
  //   89e9b3 1300533 2200893 73 406282b3 fe0294e3 1c45413 406b0b33 b0463 f95ff06f 2b3 fff2c293 829293
  //   ff2e293 500533 2200893 73 fff00413 493 84a023 140413 448493 84a023 140413 448493 84a023 140413
  //   448493 84a023 140413 448493 84a023 140413 448493 84a023 140413 448493 84a023 140413 448493 84a023
  //   140413 448493 84a023 140413 448493 84a023 140413 448493 84a023 140413 448493 84a023 140413 448493
  //   84a023 140413 448493 84a023 140413 448493 84a023 140413 448493 84a023 140413 448493 140413 433
  //   3c00493 42983 4aa03 149a2b3 28663 134a023 1442023 ffc48493 fe9412e3 800533 2200893 73 440413 3c00493
  //   fc9416e3 3200893 73 fff00293 7700493 849493 7748493 900533 2200893 73 1000e13 54c4b3 900533 2200893
  //   73 fffe0e13 fe0e16e3 a00893 73 800e13 fedc04b7 fff00413 1045413 84e4b3 900533 2200893 73 ba984b7
  //   900533 73 76544b7 900533 73 32104b7 900533 73 fffe0e13 fa0e1ee3 a00893 73 313 2000e13 493 100913
  //   930023 900533 2200893 73 12484b3 130313 fffe0e13 fe0e12e3 800e13 313 32483 900533 2200893 73 430313
  //   fffe0e13 fe0e14e3 a00893 73 f00493 100913 409909b3 900533 2200893 73 fff48493 ff29f6e3 a00893 73
  //   a00893 73 413 140413 800533 2200893 73 240413 800533 2200893 73 340413 800533 2200893 73 440413
  //   800533 2200893 73 540413 800533 2200893 73 640413 800533 2200893 73 740413 800533 2200893 73 840413
  //   800533 2200893 2200893 73 8067
  //   I
  //   S
  //   Beq
  //   Bne
  //   Bgeu
  //   MemToReg
  //   MemWrite
  //   AluOP
  //   AluSrcB
  //   Regwrite
  //   Lui
  //   Sb
  //   Ecall
  //   B
  //   J
  //   控制位
  //   流水调试日志用
  //   暂停节拍，不能为0
  //   戳工具置1进入计数暂停模式，ctrl+k时钟自动运行到对应节拍暂停
  //   ctrl+k关闭时钟连续运行，将控制位置零，进入单步调试模式调试
  //   可计数暂停的时钟源
  //   为方便自动评测，需要输出流水线各段保存的PC值，注意是PC不是PC+4，另外ID段寄存器写入信息，Mem段内存写入信息也要输出
endmodule
module \重定向流水线  (
  output RegWrite,
  output MemWrite,
  output [31:0] IF_PC,
  output [31:0] ID_PC,
  output [31:0] EX_PC,
  output [31:0] M_PC,
  output [31:0] WB_PC,
  output [31:0] RDin,
  output [31:0] MDin,
  output [31:0] LedData
);

  wire alu_1_equal, alu_1_out_4, and_1_out, and_2_out, and_3_out, and_4_out, and_5_out, and_6_out, branch,
       CLK, clock_1_out, clock_2_out, comparator_1_eq, comparator_2_eq, comparator_2_lt, d_ff_1_q, ecall,
       EX_MEM_out_17, EX_MEM_out_19, EX_MEM_out_20, EX_MEM_out_21, EX_MEM_out_22, EX_MEM_out_23, Go, halt,
       ID_EX_out_30, ID_EX_out_31, ID_EX_out_32, ID_EX_out_33, ID_EX_out_34, ID_EX_out_36, ID_EX_out_37,
       ID_EX_out_38, ID_EX_out_39, ID_EX_out_40, ID_EX_out_41, IR1, IR2, IR3, jal, jalr, MEM_WB_out_15,
       MEM_WB_out_17, MEM_WB_out_18, MEM_WB_out_19, nand_1_out, not_1_out, not_2_out, not_3_out, not_4_out,
       not_5_out, or_3_out, redirectcontrol_1_branchtaken, redirectcontrol_1_flush2, redirectcontrol_1_jal_2,
       redirectcontrol_1_jalr_2, redirectcontrol_1_stall, register_1_q, RST, run, W1, W2, W3,
       \单周期硬布线控制器_1_alu_src , \单周期硬布线控制器_1_beq , \单周期硬布线控制器_1_bgeu , \单周期硬布线控制器_1_bne , \单周期硬布线控制器_1_ecall ,
       \单周期硬布线控制器_1_lui , \单周期硬布线控制器_1_memtoreg , \单周期硬布线控制器_1_memwrite , \单周期硬布线控制器_1_regwrite ,
       \单周期硬布线控制器_1_s_type , \单周期硬布线控制器_1_sb ;
  wire [0:0] adder_2_out;
  wire [1:0] \byte , ID_EX_out_43, ID_EX_out_45, priority_encoder_1_out, priority_encoder_2_out,
       redirectcontrol_1_r1_src, redirectcontrol_1_r2_src;
  wire [3:0] decoder_1_out0, ID_EX_out_35, multiplexer_10_out, \单周期硬布线控制器_1_alu_op ;
  wire [4:0] EX_MEM_out_26, ID_EX_writereg_2, multiplexer_2_out, multiplexer_3_out, W_num;
  wire [11:0] multiplexer_4_out;
  wire [12:0] CNT_num;
  wire [15:0] \LoadUse次数 , \总周期数 , \插入气泡数 , \无条件分支数 , \条件分支成功数 ;
  wire [31:0] adder_5_out, alu_1_result, B_dest, bit_extender_1_out, bit_extender_2_out, bit_extender_3_out,
       bit_extender_4_out, bit_extender_5_out, EX_IR, EX_MEM_out_25, ID_EX_eb_2, ID_EX_ei_s_2, ID_EX_ej_2,
       ID_EX_eu_2, ID_EX_r1_2, ID_EX_r2_2, ID_IR, IF_ID_out_10, IF_IR, J_dest, MEM_ALU, MEM_IR, MEM_U,
       MEM_WB_out_20, MEM_WB_out_21, MEM_WB_out_23, mips_ram_1_p6, multiplexer_1_out, multiplexer_7_out,
       pc_4, R1, R2, regifile_1_r1, regifile_1_r2, sbdata, shifter_1_out, shifter_2_out, shifter_3_out,
       shifter_4_out, shifter_5_out, shifter_6_out, WB_IR;
  wire [31:1] I_dest;
  wire [31:2] EX_MEM_out_24;

  Button \u_总复位  (.out(RST));
  Button _1 (.out(IR1));
  Button _2 (.out(IR2));
  Button _3 (.out(IR3));
  // Probe on \总周期数 
  // Probe on \总周期数 
  Button \u_继续运行  (.out(Go));
  LED #(.active("true")) led_1 (.in(W1));
  LED #(.active("true")) led_2 (.in(W2));
  LED #(.active("true")) led_3 (.in(W3));
  Hex_Digit_Display hex_digit_display_1 (.value(LedData[31:28]));  // open: dp
  // Probe on IF_PC[19:0]
  // RiscV_Probe riscv_probe_1: pin names not known; wires that end beside it: IF_IR
  not not_1 (not_1_out, redirectcontrol_1_stall);
  Priority_Encoder #(.select(2), .disabled("Z")) priority_encoder_1 (
    .in0(1'b1), .in1(redirectcontrol_1_jal_2), .in2(redirectcontrol_1_jalr_2), .in3(branch),
    .out(priority_encoder_1_out));  // open: gs, en_out, en_in
  Multiplexer #(.select(2), .width(32), .disabled("Z"), .enable("false")) multiplexer_1 (
    .in0(pc_4), .in1(J_dest), .in2({I_dest, 1'b0}), .in3(B_dest), .out(multiplexer_1_out),
    .sel(priority_encoder_1_out));
  Hex_Digit_Display hex_digit_display_2 (.value(LedData[27:24]));  // open: dp
  Hex_Digit_Display hex_digit_display_3 (.value(LedData[23:20]));  // open: dp
  // Probe on ID_PC[19:0]
  // RiscV_Probe riscv_probe_2: pin names not known; wires that end beside it: ID_IR
  Register #(.width(32), .trigger("rising"), .Select("low")) PC (
    .D(multiplexer_1_out), .en(and_1_out), .Q(IF_PC), .clk(CLK));  // open: clr
  and and_1 (and_1_out, not_1_out, run);
  or or_1 (run, Go, not_2_out);
  not not_2 (not_2_out, halt);
  Comparator #(.width(32), .mode("unsigned")) comparator_1 (.a(R2), .b(32'h22), .eq(comparator_1_eq));  // open: gt, lt
  Register #(.width(1), .trigger("rising"), .Select("low")) register_1 (
    .D(and_3_out), .en(run), .Q(register_1_q), .clk(CLK));  // open: clr
  Hex_Digit_Display hex_digit_display_4 (.value(LedData[19:16]));  // open: dp
  Hex_Digit_Display hex_digit_display_5 (.value(LedData[15:12]));  // open: dp
  Adder #(.width(32)) adder_1 (.a(IF_PC), .b(32'h4), .out(pc_4));  // open: cin, cout
  not not_3 (not_3_out, comparator_1_eq);
  Register #(.width(1), .trigger("rising"), .Select("low")) register_2 (
    .D(register_1_q), .en(run), .Q(halt), .clk(CLK));  // open: clr
  Hex_Digit_Display hex_digit_display_6 (.value(LedData[7:4]));  // open: dp
  Hex_Digit_Display hex_digit_display_7 (.value(LedData[11:8]));  // open: dp
  Clock #(.highDuration(1), .lowDuration(1)) clock_1 (.out(clock_1_out));
  // Probe on EX_PC[19:0]
  // RiscV_Probe riscv_probe_3: pin names not known; wires that end beside it: clock_1_out, EX_IR, CLK
  and and_2 (and_2_out, ecall, comparator_1_eq);
  and and_3 (and_3_out, ecall, not_3_out);
  not not_4 (not_4_out, halt);
  Counter #(.width(16), .max('hffff), .ongoal("wrap"), .trigger("rising"), .behavior("new")) counter_1 (
    .count(not_4_out), .Q(\总周期数 ), .clk(CLK));  // open: load, D, carry, clr, preset, down
  Hex_Digit_Display hex_digit_display_8 (.value(LedData[3:0]));  // open: dp
  ROM #(.addrWidth(10), .dataWidth(32), .Select("high")) rom_1 (.addr(IF_PC[11:2]), .data(IF_IR));
  Register #(.width(32), .trigger("rising"), .Select("low")) register_3 (
    .D(R1), .en(and_2_out), .Q(LedData), .clk(CLK));  // open: clr
  // Probe on \总周期数 
  // Probe on M_PC[19:0]
  // RiscV_Probe riscv_probe_4: pin names not known; wires that end beside it: MEM_IR
  IF_ID IF_ID (
    .in_5(IF_IR), .out_10(IF_ID_out_10), .CLK(CLK), .in_4(IF_PC), .out_9(ID_PC), .in_7(IF_IR),
    .out_12(ID_IR), .run(run), .in_1(redirectcontrol_1_branchtaken), .stall(redirectcontrol_1_stall));  // open: in_6, out_11
  // Probe on \总周期数 
  // Probe on \无条件分支数 
  // Probe on \条件分支成功数 
  // Probe on \插入气泡数 
  // Probe on \LoadUse次数 
  // Probe on IF_PC[11:0]
  // Probe on WB_PC[19:0]
  // RiscV_Probe riscv_probe_5: pin names not known; wires that end beside it: WB_IR
  \单周期硬布线控制器  \u_单周期硬布线控制器_1  (
    .Funct({IF_ID_out_10[30], IF_ID_out_10[25], IF_ID_out_10[14:12]}), .OP(IF_ID_out_10[6:2]),
    .ALU_OP(\单周期硬布线控制器_1_alu_op ), .MemToReg(\单周期硬布线控制器_1_memtoreg ), .MemWrite(\单周期硬布线控制器_1_memwrite ),
    .ALU_SRC(\单周期硬布线控制器_1_alu_src ), .RegWrite(\单周期硬布线控制器_1_regwrite ), .ecall(\单周期硬布线控制器_1_ecall ),
    .S_type(\单周期硬布线控制器_1_s_type ), .Beq(\单周期硬布线控制器_1_beq ), .JAL(jal), .Bne(\单周期硬布线控制器_1_bne ),
    .in_3(IF_ID_out_10[21]), .Jalr(jalr), .LUI(\单周期硬布线控制器_1_lui ), .SB(\单周期硬布线控制器_1_sb ),
    .BGEU(\单周期硬布线控制器_1_bgeu ));  // open: uret, CSRRSI, CSRRCI
  Multiplexer #(.select(1), .width(5), .disabled("Z"), .enable("false")) multiplexer_2 (
    .in0(IF_ID_out_10[19:15]), .in1(5'b01010), .out(multiplexer_2_out), .sel(\单周期硬布线控制器_1_ecall ));
  Multiplexer #(.select(1), .width(5), .disabled("Z"), .enable("false")) multiplexer_3 (
    .in0(IF_ID_out_10[24:20]), .in1(5'b10001), .out(multiplexer_3_out), .sel(\单周期硬布线控制器_1_ecall ));
  // Probe on EX_PC[11:0]
  // Probe on ID_PC[11:0]
  Multiplexer #(.select(1), .width(12), .disabled("Z"), .enable("false")) multiplexer_4 (
    .in0(IF_ID_out_10[31:20]), .in1({IF_ID_out_10[31:25], IF_ID_out_10[11:7]}), .out(multiplexer_4_out),
    .sel(\单周期硬布线控制器_1_s_type ));
  assign bit_extender_1_out = {{20{IF_ID_out_10[31]}}, {IF_ID_out_10[31], IF_ID_out_10[7], IF_ID_out_10[30:25], IF_ID_out_10[11:8]}};  // Bit_Extender bit_extender_1
  assign bit_extender_2_out = {{12{IF_ID_out_10[31]}}, {IF_ID_out_10[31], IF_ID_out_10[19:12], IF_ID_out_10[20], IF_ID_out_10[30:21]}};  // Bit_Extender bit_extender_2
  assign bit_extender_3_out = {{12{IF_ID_out_10[31]}}, IF_ID_out_10[31:12]};  // Bit_Extender bit_extender_3
  // Probe on M_PC[11:0]
  D_Flip_Flop #(.trigger("high"), .Pre_Clr_Positions("LEGACY"), .NegatePresetClear("false"), .enable("true"), .NewFFLayout("false")) d_ff_1 (.Q(d_ff_1_q));  // open: clk, D, Qn, preset, en, reset
  // Probe on 13'hb65
  Regifile regifile_1 (
    .Din(RDin), .Clk(CLK), .R1(regifile_1_r1), .R2(regifile_1_r2), .WE(RegWrite), .W_num(W_num),
    .R1_num(multiplexer_2_out), .R2_num(multiplexer_3_out));
  assign bit_extender_4_out = {{20{multiplexer_4_out[11]}}, multiplexer_4_out};  // Bit_Extender bit_extender_4
  // Probe on WB_PC[11:0]
  Comparator #(.width(13), .mode("twosComplement")) comparator_2 (
    .a(CNT_num), .b(13'hb65), .eq(comparator_2_eq), .lt(comparator_2_lt));  // open: gt
  Clock #(.highDuration(1), .lowDuration(1)) clock_2 (.out(clock_2_out));
  ReDirectControl redirectcontrol_1 (
    .halt(halt), .clk(CLK), .jal_2(redirectcontrol_1_jal_2), .jalr_2(redirectcontrol_1_jalr_2),
    .stall(redirectcontrol_1_stall), .branchtaken(redirectcontrol_1_branchtaken), .instr(IF_ID_out_10),
    .ecall(\单周期硬布线控制器_1_ecall ), .alusrc(\单周期硬布线控制器_1_alu_src ), .flush2(redirectcontrol_1_flush2),
    .ex_W_num(ID_EX_writereg_2), .jal(ID_EX_out_40), .jalr(ID_EX_out_41), .ex_regwrite(ID_EX_out_37),
    .branch(branch), .mem_W_num(EX_MEM_out_26), .mem_regwrite(EX_MEM_out_19), .\无条件 (\无条件分支数 ),
    .\条件 (\条件分支成功数 ), .\气泡 (\插入气泡数 ), .r1_src(redirectcontrol_1_r1_src), .r2_src(redirectcontrol_1_r2_src),
    .ex_toreg(ID_EX_out_33), .loaduse(\LoadUse次数 ), .stype(\单周期硬布线控制器_1_s_type ));
  ID_EX ID_EX (
    .Beq(\单周期硬布线控制器_1_beq ), .Bne(\单周期硬布线控制器_1_bne ), .Bgeu(\单周期硬布线控制器_1_bgeu ),
    .MemToReg(\单周期硬布线控制器_1_memtoreg ), .MemWrite(\单周期硬布线控制器_1_memwrite ), .AluOP(\单周期硬布线控制器_1_alu_op ),
    .AluSrcB(\单周期硬布线控制器_1_alu_src ), .RegWrite(\单周期硬布线控制器_1_regwrite ), .LUI(\单周期硬布线控制器_1_lui ),
    .Sb(\单周期硬布线控制器_1_sb ), .CLK(CLK), .R1(regifile_1_r1), .R2(regifile_1_r2), .WriteReg(IF_ID_out_10[11:7]),
    .R1_2(ID_EX_r1_2), .R2_2(ID_EX_r2_2), .WriteReg_2(ID_EX_writereg_2), .out_30(ID_EX_out_30),
    .out_31(ID_EX_out_31), .out_32(ID_EX_out_32), .out_33(ID_EX_out_33), .out_36(ID_EX_out_36),
    .out_37(ID_EX_out_37), .out_38(ID_EX_out_38), .out_39(ID_EX_out_39), .out_34(ID_EX_out_34),
    .out_35(ID_EX_out_35), .pc(ID_PC), .pc_2(EX_PC), .EB(bit_extender_1_out), .EJ(bit_extender_2_out),
    .EU(bit_extender_3_out), .EB_2(ID_EX_eb_2), .EJ_2(ID_EX_ej_2), .EU_2(ID_EX_eu_2),
    .EI_S(bit_extender_4_out), .EI_S_2(ID_EX_ei_s_2), .out_40(ID_EX_out_40), .jal(jal), .ir(ID_IR),
    .ir_2(EX_IR), .ecall(\单周期硬布线控制器_1_ecall ), .out_42(ecall), .run(run), .in_1(redirectcontrol_1_flush2),
    .jalr(jalr), .out_41(ID_EX_out_41), .out_43(ID_EX_out_43), .r1src(redirectcontrol_1_r1_src),
    .out_45(ID_EX_out_45), .r2src(redirectcontrol_1_r2_src));  // open: pred, pred_2, uret, uret_2
  nand nand_1 (nand_1_out, d_ff_1_q, comparator_2_eq);
  Counter #(.width(13), .max('h1fff), .ongoal("stay"), .trigger("rising"), .behavior("old")) counter_2 (
    .count(comparator_2_lt), .Q(CNT_num), .clk(clock_2_out));  // open: load, D, carry, clr, preset
  Shifter #(.width(32), .shift("ll")) shifter_1 (.in(ID_EX_eb_2), .\dist (5'b00001), .out(shifter_1_out));
  Shifter #(.width(32), .shift("ll")) shifter_2 (.in(ID_EX_ej_2), .\dist (5'b00001), .out(shifter_2_out));
  Shifter #(.width(32), .shift("ll")) shifter_3 (.in(ID_EX_eu_2), .\dist (5'b01100), .out(shifter_3_out));
  assign CLK = nand_1_out ? clock_2_out : 1'bz;  // Controlled_Buffer controlled_buffer_1
  Multiplexer #(.select(2), .width(32), .disabled("Z"), .enable("false")) multiplexer_5 (
    .in0(ID_EX_r1_2), .in1(RDin), .in2(MEM_ALU), .out(R1), .sel(ID_EX_out_43));  // open: in3
  Multiplexer #(.select(2), .width(32), .disabled("Z"), .enable("false")) multiplexer_6 (
    .in0(ID_EX_r2_2), .in1(RDin), .in2(MEM_ALU), .out(R2), .sel(ID_EX_out_45));  // open: in3
  Adder #(.width(32)) adder_2 (.a(ID_EX_ei_s_2), .b(R1), .out({I_dest, adder_2_out[0]}));  // open: cin, cout
  Pull_Resistor #(.pull(1)) pull_resistor_1 (.node(CLK));
  Multiplexer #(.select(1), .width(32), .disabled("Z"), .enable("false")) multiplexer_7 (
    .in0(R2), .in1(ID_EX_ei_s_2), .out(multiplexer_7_out), .sel(ID_EX_out_36));
  Adder #(.width(32)) adder_3 (.a(shifter_1_out), .b(EX_PC), .out(B_dest));  // open: cin, cout
  Adder #(.width(32)) adder_4 (.a(shifter_2_out), .b(EX_PC), .out(J_dest));  // open: cin, cout
  or or_2 (branch, and_4_out, and_5_out, and_6_out);
  and and_4 (and_4_out, ID_EX_out_30, alu_1_equal);
  and and_5 (and_5_out, ID_EX_out_31, not_5_out);
  not not_5 (not_5_out, alu_1_equal);
  and and_6 (and_6_out, ID_EX_out_32, alu_1_out_4);
  ALU alu_1 (
    .X(R1), .Y(multiplexer_7_out), .AluOP(ID_EX_out_35), .Equal(alu_1_equal), .Result(alu_1_result),
    .out_4(alu_1_out_4));  // open: Result_2, out_6
  EX_MEM EX_MEM (
    .MemToReg(ID_EX_out_33), .MemWrite(ID_EX_out_34), .out_17(EX_MEM_out_17), .out_18(MemWrite),
    .RegWrite(ID_EX_out_37), .out_19(EX_MEM_out_19), .LUI(ID_EX_out_38), .out_20(EX_MEM_out_20),
    .Sb(ID_EX_out_39), .out_21(EX_MEM_out_21), .Alu(alu_1_result), .out_24({EX_MEM_out_24, \byte }), .R2(R2),
    .out_25(EX_MEM_out_25), .udata(shifter_3_out), .out_27(MEM_U), .pc(EX_PC), .out_28(M_PC), .ir(EX_IR),
    .out_29(MEM_IR), .CLK(CLK), .in_11(ID_EX_writereg_2), .out_26(EX_MEM_out_26), .run(run), .in_1(1'b0),
    .jal(ID_EX_out_40), .out_22(EX_MEM_out_22), .jalr(ID_EX_out_41), .out_23(EX_MEM_out_23));
  Multiplexer #(.select(1), .width(32), .disabled("Z"), .enable("false")) multiplexer_8 (
    .in0({EX_MEM_out_24, \byte }), .in1(MEM_U), .out(MEM_ALU), .sel(EX_MEM_out_20));
  Multiplexer #(.select(1), .width(32), .disabled("Z"), .enable("false")) multiplexer_9 (
    .in0(EX_MEM_out_25), .in1(sbdata), .out(MDin), .sel(EX_MEM_out_21));
  Decoder #(.select(2), .tristate("false"), .disabled("Z"), .enable("false")) decoder_1 (
    .out0(decoder_1_out0[0]), .out1(decoder_1_out0[1]), .out2(decoder_1_out0[2]), .out3(decoder_1_out0[3]),
    .sel(\byte ));
  assign bit_extender_5_out = {{24{1'b0}}, EX_MEM_out_25[7:0]};  // Bit_Extender bit_extender_5
  Multiplexer #(.select(1), .width(4), .disabled("Z"), .enable("false")) multiplexer_10 (
    .in0(4'b1111), .in1(decoder_1_out0), .out(multiplexer_10_out), .sel(EX_MEM_out_21));
  Shifter #(.width(32), .shift("ll")) shifter_4 (.in(bit_extender_5_out), .\dist (5'b01000), .out(shifter_4_out));
  Shifter #(.width(32), .shift("ll")) shifter_5 (.in(bit_extender_5_out), .\dist (5'b10000), .out(shifter_5_out));
  Shifter #(.width(32), .shift("ll")) shifter_6 (.in(bit_extender_5_out), .\dist (5'b11000), .out(shifter_6_out));
  Multiplexer #(.select(2), .width(32), .disabled("Z"), .enable("false")) multiplexer_11 (
    .in0(bit_extender_5_out), .in1(shifter_4_out), .in2(shifter_5_out), .in3(shifter_6_out), .out(sbdata),
    .sel(\byte ));
  // MIPS_RAM mips_ram_1: pin names not known; wires that end beside it: EX_MEM_out_24[11:2], MDin, MemWrite, multiplexer_10_out, CLK, mips_ram_1_p6
  MEM_WB MEM_WB (
    .in_2(EX_MEM_out_17), .out_15(MEM_WB_out_15), .in_3(EX_MEM_out_19), .out_16(RegWrite),
    .in_4(EX_MEM_out_20), .out_17(MEM_WB_out_17), .in_7({EX_MEM_out_24, \byte }), .out_20(MEM_WB_out_20),
    .in_8(mips_ram_1_p6), .out_21(MEM_WB_out_21), .in_10(MEM_U), .out_23(MEM_WB_out_23),
    .in_9(EX_MEM_out_26), .out_22(W_num), .in_11(M_PC), .out_24(WB_PC), .in_12(MEM_IR), .out_25(WB_IR),
    .CLK(CLK), .run(run), .in_1(1'b0), .in_5(EX_MEM_out_22), .out_18(MEM_WB_out_18), .in_6(EX_MEM_out_23),
    .out_19(MEM_WB_out_19));
  or or_3 (or_3_out, MEM_WB_out_18, MEM_WB_out_19);
  Adder #(.width(32)) adder_5 (.a(WB_PC), .b(32'h4), .out(adder_5_out));  // open: cin, cout
  Priority_Encoder #(.select(2), .disabled("Z")) priority_encoder_2 (
    .in0(1'b1), .in1(MEM_WB_out_15), .in2(or_3_out), .in3(MEM_WB_out_17), .out(priority_encoder_2_out));  // open: gs, en_out, en_in
  Multiplexer #(.select(2), .width(32), .disabled("Z"), .enable("false")) multiplexer_12 (
    .in0(MEM_WB_out_20), .in1(MEM_WB_out_21), .in2(adder_5_out), .in3(MEM_WB_out_23), .out(RDin),
    .sel(priority_encoder_2_out));

  // Other names for the same wires on the sheet: MEM_PC[31:0] = M_PC

  // Notes on the sheet:
  //   中断源
  //   时空图监测，可删除
  //   中断等待指示
  //   数码管输出
  //   contents of rom_1 (hex, n*v repeats v):
  //   100493 100006f 100493 200913 300993 100006f 100493 200913 300993 100006f 100493 200913 300993
  //   100006f 100493 200913 300993 3bc000ef 100413 100493 1f49493 900533 2200893 73 24d493 48463 fedff06f
  //   900533 2200893 73 100493 249493 900533 2200893 73 48463 fedff06f 100493 1f49493 900533 2200893 73
  //   4034d493 900533 2200893 73 4044d493 900533 2200893 73 4044d493 900533 2200893 73 4044d493 900533
  //   2200893 73 4044d493 900533 2200893 73 4044d493 900533 2200893 73 4044d493 900533 2200893 73 4044d493
  //   900533 2200893 73 100413 1f41993 41f9d993 433 c00913 300b13 140413 f47413 800293 100313 499993
  //   89e9b3 1300533 2200893 73 406282b3 fe0294e3 140413 f00f93 1f47433 1c41413 800293 100313 49d993
  //   89e9b3 1300533 2200893 73 406282b3 fe0294e3 1c45413 406b0b33 b0463 f95ff06f 2b3 fff2c293 829293
  //   ff2e293 500533 2200893 73 fff00413 493 84a023 140413 448493 84a023 140413 448493 84a023 140413
  //   448493 84a023 140413 448493 84a023 140413 448493 84a023 140413 448493 84a023 140413 448493 84a023
  //   140413 448493 84a023 140413 448493 84a023 140413 448493 84a023 140413 448493 84a023 140413 448493
  //   84a023 140413 448493 84a023 140413 448493 84a023 140413 448493 84a023 140413 448493 140413 433
  //   3c00493 42983 4aa03 149a2b3 28663 134a023 1442023 ffc48493 fe9412e3 800533 2200893 73 440413 3c00493
  //   fc9416e3 3200893 73 fff00293 7700493 849493 7748493 900533 2200893 73 1000e13 54c4b3 900533 2200893
  //   73 fffe0e13 fe0e16e3 a00893 73 800e13 fedc04b7 fff00413 1045413 84e4b3 900533 2200893 73 ba984b7
  //   900533 73 76544b7 900533 73 32104b7 900533 73 fffe0e13 fa0e1ee3 a00893 73 313 2000e13 493 100913
  //   930023 900533 2200893 73 12484b3 130313 fffe0e13 fe0e12e3 800e13 313 32483 900533 2200893 73 430313
  //   fffe0e13 fe0e14e3 a00893 73 f00493 100913 409909b3 900533 2200893 73 fff48493 ff29f6e3 a00893 73
  //   a00893 73 413 140413 800533 2200893 73 240413 800533 2200893 73 340413 800533 2200893 73 440413
  //   800533 2200893 73 540413 800533 2200893 73 640413 800533 2200893 73 740413 800533 2200893 73 840413
  //   800533 2200893 2200893 73 8067
  //   I
  //   S
  //   Beq
  //   Bne
  //   Bgeu
  //   MemToReg
  //   MemWrite
  //   AluOP
  //   AluSrcB
  //   Regwrite
  //   Lui
  //   Sb
  //   Ecall
  //   B
  //   J
  //   控制位
  //   流水调试日志用
  //   暂停节拍，不能为0
  //   戳工具置1进入计数暂停模式，ctrl+k时钟自动运行到对应节拍暂停
  //   ctrl+k关闭时钟连续运行，将控制位置零，进入单步调试模式调试
  //   可计数暂停的时钟源
  //   为方便自动评测，需要输出流水线各段保存的PC值，注意是PC不是PC+4，另外ID段寄存器写入信息，Mem段内存写入信息也要输出
endmodule

module \中断按键参考电路  (
  input  \同步清零信号 ,
  output \与中断屏蔽位与 
);

  wire \_1号中断_out , and_1_out, clock_1_out, d_ff_1_q, or_1_out, or_2_out;

  Clock #(.highDuration(1), .lowDuration(1)) clock_1 (.out(clock_1_out));
  Button \_1号中断  (.out(\_1号中断_out ));
  or or_1 (or_1_out, \与中断屏蔽位与 , d_ff_1_q);
  LED #(.active("true")) \_1号中断等待指示灯  (.in(or_1_out));
  D_Flip_Flop #(.trigger("rising"), .Pre_Clr_Positions("LEGACY"), .NegatePresetClear("false"), .enable("true"), .NewFFLayout("false")) d_ff_1 (
    .clk(\_1号中断_out ), .D(1'b1), .Q(d_ff_1_q), .reset(\与中断屏蔽位与 ));  // open: Qn, preset, en
  or or_2 (or_2_out, d_ff_1_q, \与中断屏蔽位与 );
  and and_1 (and_1_out, or_2_out, ~\同步清零信号 );  // AND_Gate
  D_Flip_Flop #(.trigger("rising"), .Pre_Clr_Positions("LEGACY"), .NegatePresetClear("false"), .enable("true"), .NewFFLayout("false")) IR1 (
    .clk(clock_1_out), .D(and_1_out), .Q(\与中断屏蔽位与 ));  // open: Qn, preset, en, reset

  // Notes on the sheet:
  //   中断信号采样参考电路
  //   Reset 
endmodule

module \单周期_单级中断  (
  input  IR1,
  input  IR2,
  input  IR3,
  output RegWrite,
  output MemWrite,
  output [31:0] PC,
  output [31:0] IR,
  output [31:0] RDin,
  output [31:0] MDin,
  output [31:0] LedData
);

  wire alu_1_equal, alu_1_out_4, and_1_out, and_2_out, and_3_out, and_4_out, and_6_out, and_8_out, and_9_out,
       and_10_out, B, CLK, CLR1, CLR2, CLR3, comparator_1_eq, comparator_2_eq, comparator_3_eq,
       comparator_4_eq, comparator_5_eq, d_ff_1_q, d_ff_2_q, d_ff_3_q, ecall, Go, halt, IE, INT, INT1, INT2,
       INT3, IR1_t, IR2_t, IR3_t, IRA, IRB, IRC, jmp, not_1_out, not_2_out, not_3_out, not_4_out, not_5_out,
       or_5_out, or_6_out, or_7_out, or_8_out, or_9_out, priority_encoder_3_gs, RST, sb, URET, W1, W2, W3,
       \单周期硬布线控制器_1_alu_src , \单周期硬布线控制器_1_beq , \单周期硬布线控制器_1_bgeu , \单周期硬布线控制器_1_bne , \单周期硬布线控制器_1_jal ,
       \单周期硬布线控制器_1_jalr , \单周期硬布线控制器_1_lui , \单周期硬布线控制器_1_memtoreg , \单周期硬布线控制器_1_s_type ;
  wire [0:0] adder_2_out;
  wire [1:0] priority_encoder_1_out, priority_encoder_2_out, priority_encoder_3_out, priority_encoder_4_out,
       register_2_q;
  wire [3:0] decoder_1_out0, multiplexer_9_out, \单周期硬布线控制器_1_alu_op ;
  wire [4:0] multiplexer_3_out, R2_num;
  wire [11:0] multiplexer_5_out;
  wire [15:0] \总周期数 ;
  wire [31:0] ALUout, B_dest, bit_extender_1_out, bit_extender_2_out, bit_extender_3_out, bit_extender_4_out,
       bit_extender_5_out, EPC, INTAddr, J_dest, mips_ram_1_p8, multiplexer_2_out, multiplexer_7_out, PC_4,
       PC_next, R1, R2, sbdata, shifter_1_out, shifter_2_out, shifter_4_out, shifter_5_out, shifter_6_out, ui;
  wire [31:1] I_dest;

  Clock #(.highDuration(1), .lowDuration(1)) clock_1 (.out(CLK));
  Button _1 ();  // open: out
  Button _2 ();  // open: out
  Button _3 ();  // open: out
  Button \u_继续运行  (.out(Go));
  LED #(.active("true")) led_1 (.in(W1));
  LED #(.active("true")) led_2 (.in(W2));
  LED #(.active("true")) led_3 (.in(W3));
  Priority_Encoder #(.select(2), .disabled("Z")) priority_encoder_1 (
    .in0(1'b1), .in1(\单周期硬布线控制器_1_jal ), .in2(\单周期硬布线控制器_1_jalr ), .in3(B), .out(priority_encoder_1_out));  // open: gs, en_out, en_in
  Multiplexer #(.select(2), .width(32), .disabled("Z"), .enable("false")) multiplexer_1 (
    .in0(PC_4), .in1(J_dest), .in2({I_dest, 1'b0}), .in3(B_dest), .out(PC_next), .sel(priority_encoder_1_out));
  or or_1 (W1, INT1, d_ff_1_q);
  or or_2 (W2, INT2, d_ff_2_q);
  or or_3 (W3, INT3, d_ff_3_q);
  Hex_Digit_Display hex_digit_display_1 (.value(LedData[31:28]));  // open: dp
  or or_4 (jmp, \单周期硬布线控制器_1_jalr , \单周期硬布线控制器_1_jal );
  Comparator #(.width(16), .mode("twosComplement")) comparator_1 (
    .a(16'h23b), .b(\总周期数 ), .eq(comparator_1_eq));  // open: gt, lt
  Comparator #(.width(16), .mode("twosComplement")) comparator_2 (
    .a(\总周期数 ), .b(16'h1), .eq(comparator_2_eq));  // open: gt, lt
  Comparator #(.width(16), .mode("twosComplement")) comparator_3 (
    .a(\总周期数 ), .b(16'h4), .eq(comparator_3_eq));  // open: gt, lt
  Comparator #(.width(16), .mode("twosComplement")) comparator_4 (
    .a(\总周期数 ), .b(16'h7), .eq(comparator_4_eq));  // open: gt, lt
  D_Flip_Flop #(.trigger("rising"), .Pre_Clr_Positions("LEGACY"), .NegatePresetClear("false"), .enable("true"), .NewFFLayout("false")) d_ff_1 (
    .clk(IRA), .D(1'b1), .Q(d_ff_1_q), .reset(INT1));  // open: Qn, preset, en
  D_Flip_Flop #(.trigger("rising"), .Pre_Clr_Positions("LEGACY"), .NegatePresetClear("false"), .enable("true"), .NewFFLayout("false")) d_ff_2 (
    .clk(IRB), .D(1'b1), .Q(d_ff_2_q), .reset(INT2));  // open: Qn, preset, en
  D_Flip_Flop #(.trigger("rising"), .Pre_Clr_Positions("LEGACY"), .NegatePresetClear("false"), .enable("true"), .NewFFLayout("false")) d_ff_3 (
    .clk(IRC), .D(1'b1), .Q(d_ff_3_q), .reset(INT3));  // open: Qn, preset, en
  Hex_Digit_Display hex_digit_display_2 (.value(LedData[27:24]));  // open: dp
  Hex_Digit_Display hex_digit_display_3 (.value(LedData[23:20]));  // open: dp
  or or_5 (or_5_out, comparator_1_eq, comparator_2_eq);
  Pull_Resistor #(.pull(0)) pull_resistor_1 (.node(IRA));
  assign IRA = or_5_out ? ~CLK : 1'bz;  // Controlled_Inverter controlled_inverter_1
  Pull_Resistor #(.pull(0)) pull_resistor_2 (.node(IRB));
  assign IRB = comparator_3_eq ? ~CLK : 1'bz;  // Controlled_Inverter controlled_inverter_2
  Pull_Resistor #(.pull(0)) pull_resistor_3 (.node(IRC));
  assign IRC = comparator_4_eq ? ~CLK : 1'bz;  // Controlled_Inverter controlled_inverter_3
  or or_6 (or_6_out, d_ff_1_q, INT1);
  or or_7 (or_7_out, d_ff_2_q, INT2);
  or or_8 (or_8_out, d_ff_3_q, INT3);
  Hex_Digit_Display hex_digit_display_4 (.value(LedData[15:12]));  // open: dp
  Hex_Digit_Display hex_digit_display_5 (.value(LedData[19:16]));  // open: dp
  Priority_Encoder #(.select(2), .disabled("Z")) priority_encoder_2 (
    .in0(1'b1), .in1(INT), .in2(URET), .out(priority_encoder_2_out));  // open: in3, gs, en_out, en_in
  Multiplexer #(.select(2), .width(32), .disabled("Z"), .enable("false")) multiplexer_2 (
    .in0(PC_next), .in1(INTAddr), .in2(EPC), .out(multiplexer_2_out), .sel(priority_encoder_2_out));  // open: in3
  not not_1 (not_1_out, halt);
  and and_1 (and_1_out, or_6_out, ~CLR1);  // AND_Gate
  and and_2 (and_2_out, or_7_out, ~CLR2);  // AND_Gate
  and and_3 (and_3_out, or_8_out, ~CLR3);  // AND_Gate
  Hex_Digit_Display hex_digit_display_6 (.value(LedData[7:4]));  // open: dp
  Hex_Digit_Display hex_digit_display_7 (.value(LedData[11:8]));  // open: dp
  // Probe on \总周期数 
  Register #(.width(32), .trigger("rising"), .Select("low")) u_PC (
    .D(multiplexer_2_out), .en(or_9_out), .Q(PC), .clk(CLK), .clr(RST));
  or or_9 (or_9_out, Go, not_1_out);
  Comparator #(.width(32), .mode("unsigned")) comparator_5 (.a(R2), .b(32'h22), .eq(comparator_5_eq));  // open: gt, lt
  D_Flip_Flop #(.trigger("rising"), .Pre_Clr_Positions("LEGACY"), .NegatePresetClear("false"), .enable("true"), .NewFFLayout("false")) u_IR1 (
    .clk(CLK), .D(and_1_out), .Q(INT1));  // open: Qn, preset, en, reset
  D_Flip_Flop #(.trigger("rising"), .Pre_Clr_Positions("LEGACY"), .NegatePresetClear("false"), .enable("true"), .NewFFLayout("false")) IR1_2 (
    .clk(CLK), .D(and_2_out), .Q(INT2));  // open: Qn, preset, en, reset
  D_Flip_Flop #(.trigger("rising"), .Pre_Clr_Positions("LEGACY"), .NegatePresetClear("false"), .enable("true"), .NewFFLayout("false")) IR1_3 (
    .clk(CLK), .D(and_3_out), .Q(INT3));  // open: Qn, preset, en, reset
  Hex_Digit_Display hex_digit_display_8 (.value(LedData[3:0]));  // open: dp
  Adder #(.width(32)) adder_1 (.a(PC), .b(32'h4), .out(PC_4));  // open: cin, cout
  and and_4 (and_4_out, ecall, comparator_5_eq);
  and and_5 (halt, ecall, not_2_out);
  not not_2 (not_2_out, comparator_5_eq);
  // RiscV_Probe riscv_probe_1: pin names not known; wires that end beside it: IR
  Register #(.width(32), .trigger("rising"), .Select("low")) register_1 (
    .D(R1), .en(and_4_out), .Q(LedData), .clk(CLK));  // open: clr
  not not_3 (not_3_out, halt);
  Counter #(.width(16), .max('hffff), .ongoal("wrap"), .trigger("rising"), .behavior("new")) counter_1 (
    .count(not_3_out), .Q(\总周期数 ), .clk(CLK));  // open: load, D, carry, clr, preset, down
  or or_10 (IR1_t, IR1, IRA);
  ROM #(.addrWidth(10), .dataWidth(32), .Select("high")) rom_1 (.addr(PC[11:2]), .data(IR));
  or or_11 (IR2_t, IR2, IRB);
  Priority_Encoder #(.select(2), .disabled("Z")) priority_encoder_3 (
    .in0(INT1), .in1(INT2), .in2(INT3), .out(priority_encoder_3_out), .gs(priority_encoder_3_gs));  // open: in3, en_out, en_in
  not not_4 (not_4_out, URET);
  \单周期硬布线控制器  \u_单周期硬布线控制器_1  (
    .Funct({IR[30], IR[25], IR[14:12]}), .OP(IR[6:2]), .ALU_OP(\单周期硬布线控制器_1_alu_op ),
    .MemToReg(\单周期硬布线控制器_1_memtoreg ), .MemWrite(MemWrite), .ALU_SRC(\单周期硬布线控制器_1_alu_src ),
    .RegWrite(RegWrite), .ecall(ecall), .S_type(\单周期硬布线控制器_1_s_type ), .Beq(\单周期硬布线控制器_1_beq ),
    .JAL(\单周期硬布线控制器_1_jal ), .Bne(\单周期硬布线控制器_1_bne ), .in_3(IR[21]), .uret(URET), .Jalr(\单周期硬布线控制器_1_jalr ),
    .LUI(\单周期硬布线控制器_1_lui ), .SB(sb), .BGEU(\单周期硬布线控制器_1_bgeu ));  // open: CSRRSI, CSRRCI
  Multiplexer #(.select(1), .width(5), .disabled("Z"), .enable("false")) multiplexer_3 (
    .in0(IR[19:15]), .in1(5'b01010), .out(multiplexer_3_out), .sel(ecall));
  Multiplexer #(.select(1), .width(5), .disabled("Z"), .enable("false")) multiplexer_4 (
    .in0(IR[24:20]), .in1(5'b10001), .out(R2_num), .sel(ecall));
  and and_6 (and_6_out, priority_encoder_3_gs, not_4_out);
  or or_12 (IR3_t, IR3, IRC);
  Multiplexer #(.select(1), .width(12), .disabled("Z"), .enable("false")) multiplexer_5 (
    .in0(IR[31:20]), .in1({IR[31:25], IR[11:7]}), .out(multiplexer_5_out), .sel(\单周期硬布线控制器_1_s_type ));
  assign bit_extender_1_out = {{20{IR[31]}}, {IR[31], IR[7], IR[30:25], IR[11:8]}};  // Bit_Extender bit_extender_1
  assign bit_extender_2_out = {{12{IR[31]}}, {IR[31], IR[19:12], IR[20], IR[30:21]}};  // Bit_Extender bit_extender_2
  assign bit_extender_3_out = {{12{IR[31]}}, IR[31:12]};  // Bit_Extender bit_extender_3
  Multiplexer #(.select(2), .width(32), .disabled("Z"), .enable("false")) multiplexer_6 (
    .in0(32'h30ac), .in1(32'h3150), .in2(32'h31f4), .out(INTAddr), .sel(priority_encoder_3_out));  // open: in3
  and and_7 (INT, priority_encoder_3_gs, IE);
  D_Flip_Flop #(.trigger("rising"), .Pre_Clr_Positions("LEGACY"), .NegatePresetClear("false"), .enable("true"), .NewFFLayout("false")) u_IE (
    .clk(CLK), .D(and_6_out), .Qn(IE));  // open: Q, preset, en, reset
  Regifile regifile_1 (
    .Din(RDin), .Clk(CLK), .R1(R1), .R2(R2), .WE(RegWrite), .W_num(IR[11:7]), .R1_num(multiplexer_3_out),
    .R2_num(R2_num));
  assign bit_extender_4_out = {{20{multiplexer_5_out[11]}}, multiplexer_5_out};  // Bit_Extender bit_extender_4
  Shifter #(.width(32), .shift("ll")) shifter_1 (.in(bit_extender_1_out), .\dist (5'b00001), .out(shifter_1_out));
  Shifter #(.width(32), .shift("ll")) shifter_2 (.in(bit_extender_2_out), .\dist (5'b00001), .out(shifter_2_out));
  Shifter #(.width(32), .shift("ll")) shifter_3 (.in(bit_extender_3_out), .\dist (5'b01100), .out(ui));
  Adder #(.width(32)) adder_2 (.a(bit_extender_4_out), .b(R1), .out({I_dest, adder_2_out[0]}));  // open: cin, cout
  Adder #(.width(32)) adder_3 (.a(shifter_1_out), .b(PC), .out(B_dest));  // open: cin, cout
  Adder #(.width(32)) adder_4 (.a(shifter_2_out), .b(PC), .out(J_dest));  // open: cin, cout
  Multiplexer #(.select(1), .width(32), .disabled("Z"), .enable("false")) multiplexer_7 (
    .in0(R2), .in1(bit_extender_4_out), .out(multiplexer_7_out), .sel(\单周期硬布线控制器_1_alu_src ));
  Demultiplexer #(.select(2), .width(1), .tristate("false"), .disabled("Z"), .enable("false")) demultiplexer_1 (
    .out0(CLR1), .out1(CLR2), .out2(CLR3), .in(URET), .sel(register_2_q));  // open: out3
  Register #(.width(2), .trigger("rising"), .Select("low")) register_2 (
    .D(priority_encoder_3_out), .en(INT), .Q(register_2_q), .clk(CLK));  // open: clr
  and and_8 (and_8_out, \单周期硬布线控制器_1_beq , alu_1_equal);
  and and_9 (and_9_out, \单周期硬布线控制器_1_bne , not_5_out);
  not not_5 (not_5_out, alu_1_equal);
  and and_10 (and_10_out, \单周期硬布线控制器_1_bgeu , alu_1_out_4);
  ALU alu_1 (
    .X(R1), .Y(multiplexer_7_out), .AluOP(\单周期硬布线控制器_1_alu_op ), .Equal(alu_1_equal), .Result(ALUout),
    .out_4(alu_1_out_4));  // open: Result_2, out_6
  Multiplexer #(.select(1), .width(32), .disabled("Z"), .enable("false")) multiplexer_8 (
    .in0(R2), .in1(sbdata), .out(MDin), .sel(sb));
  Register #(.width(32), .trigger("rising"), .Select("low")) mEPC (
    .D(PC_next), .en(INT), .Q(EPC), .clk(CLK));  // open: clr
  or or_13 (B, and_8_out, and_9_out, and_10_out);
  Decoder #(.select(2), .tristate("false"), .disabled("Z"), .enable("false")) decoder_1 (
    .out0(decoder_1_out0[0]), .out1(decoder_1_out0[1]), .out2(decoder_1_out0[2]), .out3(decoder_1_out0[3]),
    .sel(ALUout[1:0]));
  assign bit_extender_5_out = {{24{1'b0}}, R2[7:0]};  // Bit_Extender bit_extender_5
  Multiplexer #(.select(1), .width(4), .disabled("Z"), .enable("false")) multiplexer_9 (
    .in0(4'b1111), .in1(decoder_1_out0), .out(multiplexer_9_out), .sel(sb));
  Shifter #(.width(32), .shift("ll")) shifter_4 (.in(bit_extender_5_out), .\dist (5'b01000), .out(shifter_4_out));
  Shifter #(.width(32), .shift("ll")) shifter_5 (.in(bit_extender_5_out), .\dist (5'b10000), .out(shifter_5_out));
  Shifter #(.width(32), .shift("ll")) shifter_6 (.in(bit_extender_5_out), .\dist (5'b11000), .out(shifter_6_out));
  // MIPS_RAM mips_ram_1: pin names not known; wires that end beside it: sbdata, ALUout[11:2], MDin, MemWrite, multiplexer_9_out, CLK, 1'b1, mips_ram_1_p8
  Multiplexer #(.select(2), .width(32), .disabled("Z"), .enable("false")) multiplexer_10 (
    .in0(bit_extender_5_out), .in1(shifter_4_out), .in2(shifter_5_out), .in3(shifter_6_out), .out(sbdata),
    .sel(ALUout[1:0]));
  Priority_Encoder #(.select(2), .disabled("Z")) priority_encoder_4 (
    .in0(1'b1), .in1(\单周期硬布线控制器_1_memtoreg ), .in2(jmp), .in3(\单周期硬布线控制器_1_lui ), .out(priority_encoder_4_out));  // open: gs, en_out, en_in
  Multiplexer #(.select(2), .width(32), .disabled("Z"), .enable("false")) multiplexer_11 (
    .in0(ALUout), .in1(mips_ram_1_p8), .in2(PC_4), .in3(ui), .out(RDin), .sel(priority_encoder_4_out));

  // Other names for the same wires on the sheet: byte[1:0] = ALUout[1:0]

  // Notes on the sheet:
  //   中断源
  //   中断等待指示
  //   总复位信号应将除ROM以外所有存储组件全部清零
  //   单级中断测试信号模拟器
  //   数码管输出
  //   Reset 
  //   Reset 
  //   Reset 
  //   数码管输出应该用寄存器锁存，否则显示数据只能一闪而过
  //   指令探针
  //   指令存储器
  //   指令字
  //   contents of rom_1 (hex, n*v repeats v):
  //   100493 100006f 100493 200913 300993 100006f 100493 200913 300993 100006f 100493 200913 300993
  //   100006f 100493 200913 300993 29c000ef 100413 100493 1f49493 900533 2200893 73 24d493 48463 fedff06f
  //   900533 2200893 73 100493 249493 900533 2200893 73 48463 fedff06f 100493 1f49493 900533 2200893 73
  //   4034d493 900533 2200893 73 4044d493 900533 2200893 73 4044d493 900533 2200893 73 4044d493 900533
  //   2200893 73 4044d493 900533 2200893 73 4044d493 900533 2200893 73 4044d493 900533 2200893 73 4044d493
  //   900533 2200893 73 100413 1f41993 41f9d993 433 c00913 300b13 140413 f47413 800293 100313 499993
  //   89e9b3 1300533 2200893 73 406282b3 fe0294e3 140413 f00f93 1f47433 1c41413 800293 100313 49d993
  //   89e9b3 1300533 2200893 73 406282b3 fe0294e3 1c45413 406b0b33 b0463 f95ff06f 2b3 fff2c293 829293
  //   ff2e293 500533 2200893 73 fff00413 493 84a023 140413 448493 84a023 140413 448493 84a023 140413
  //   448493 84a023 140413 448493 84a023 140413 448493 84a023 140413 448493 84a023 140413 448493 84a023
  //   140413 448493 84a023 140413 448493 84a023 140413 448493 84a023 140413 448493 84a023 140413 448493
  //   84a023 140413 448493 84a023 140413 448493 84a023 140413 448493 84a023 140413 448493 140413 433
  //   3c00493 42983 4aa03 149a2b3 28663 134a023 1442023 ffc48493 fe9412e3 800533 2200893 73 440413 3c00493
  //   fc9416e3 a00893 73 413 140413 800533 2200893 73 240413 800533 2200893 73 340413 800533 2200893 73
  //   440413 800533 2200893 73 540413 800533 2200893 73 640413 800533 2200893 73 740413 800533 2200893 73
  //   840413 800533 2200893 2200893 73 8067
  //   JAL
  //   JALR
  //   URET
  //   I
  //   S
  //   Beq
  //   Bne
  //   Bgeu
  //   MemToReg
  //   MemWrite
  //   AluOP
  //   AluSrcB
  //   RegWrite
  //   LUI
  //   Sb
  //   B
  //   J
  //   为方便自动评测，需要输出PC，IR，寄存器堆写如数据RDin
  //   RAM写使能MemWrite、RAM写入数据MDin等信号
  //   数据存储器
endmodule

module \单周期_多级中断  (
  input  IR1,
  input  IR2,
  input  IR3,
  output RegWrite,
  output MemWrite,
  output [31:0] PC,
  output [31:0] IR,
  output [31:0] RDin,
  output [31:0] MDin,
  output [31:0] LedData
);

  wire alu_1_equal, alu_1_out_4, and_1_out, and_2_out, and_3_out, and_4_out, and_6_out, and_7_out, and_8_out,
       and_9_out, and_10_out, and_11_out, and_12_out, and_13_out, and_14_out, and_15_out, B, CLK, CLR1, CLR2,
       CLR3, comparator_1_eq, comparator_2_eq, comparator_3_eq, comparator_4_eq, comparator_5_eq,
       comparator_6_eq, CSRRCI, CSRRSI, d_ff_1_q, d_ff_2_q, d_ff_3_q, d_ff_4_q, decoder_1_out1,
       decoder_1_out2, decoder_1_out3, decoder_2_out1, decoder_2_out2, decoder_2_out3, ecall, Go, halt, IE,
       INT, INT1, INT1_q, INT2, INT2_q, INT3, INT3_q, IR1_t, IR2_t, IR3_t, IRA, IRB, IRC, jmp,
       multiplexer_8_out, multiplexer_9_out, not_1_out, not_2_out, not_3_out, not_4_out, not_5_out,
       not_6_out, not_7_out, or_5_out, or_6_out, or_7_out, or_8_out, or_9_out, or_10_out, or_14_out,
       or_15_out, RST, sb, sup, URET, W1, W2, W3, \单周期硬布线控制器_1_alu_src , \单周期硬布线控制器_1_beq ,
       \单周期硬布线控制器_1_bgeu , \单周期硬布线控制器_1_bne , \单周期硬布线控制器_1_jal , \单周期硬布线控制器_1_jalr , \单周期硬布线控制器_1_lui ,
       \单周期硬布线控制器_1_memtoreg , \单周期硬布线控制器_1_s_type ;
  wire [0:0] adder_2_out;
  wire [1:0] INTR, INTR_NOW, priority_encoder_1_out, priority_encoder_2_out, priority_encoder_5_out;
  wire [3:0] decoder_3_out0, multiplexer_12_out, \单周期硬布线控制器_1_alu_op ;
  wire [4:0] multiplexer_4_out, R2_num;
  wire [11:0] multiplexer_6_out;
  wire [15:0] \总周期数 ;
  wire [31:0] ALUout, B_dest, bit_extender_1_out, bit_extender_2_out, bit_extender_3_out, bit_extender_4_out,
       bit_extender_5_out, EPC, INTAddr, J_dest, mEPC1_q, mEPC2_q, mEPC3_q, mips_ram_1_p8, multiplexer_2_out,
       multiplexer_10_out, PC_4, PC_next, R1, R2, sbdata, shifter_1_out, shifter_2_out, shifter_4_out,
       shifter_5_out, shifter_6_out, ui;
  wire [31:1] I_dest;

  Clock #(.highDuration(1), .lowDuration(1)) clock_1 (.out(CLK));
  Button _1 ();  // open: out
  Button _2 ();  // open: out
  Button _3 ();  // open: out
  Button \u_继续运行  (.out(Go));
  LED #(.active("true")) led_1 (.in(W1));
  LED #(.active("true")) led_2 (.in(W2));
  LED #(.active("true")) led_3 (.in(W3));
  Priority_Encoder #(.select(2), .disabled("Z")) priority_encoder_1 (
    .in0(1'b1), .in1(\单周期硬布线控制器_1_jal ), .in2(\单周期硬布线控制器_1_jalr ), .in3(B), .out(priority_encoder_1_out));  // open: gs, en_out, en_in
  Multiplexer #(.select(2), .width(32), .disabled("Z"), .enable("false")) multiplexer_1 (
    .in0(PC_4), .in1(J_dest), .in2({I_dest, 1'b0}), .in3(B_dest), .out(PC_next), .sel(priority_encoder_1_out));
  or or_1 (W1, INT1, d_ff_1_q);
  or or_2 (W2, INT2, d_ff_2_q);
  or or_3 (W3, INT3, d_ff_3_q);
  Hex_Digit_Display hex_digit_display_1 (.value(LedData[31:28]));  // open: dp
  or or_4 (jmp, \单周期硬布线控制器_1_jalr , \单周期硬布线控制器_1_jal );
  Comparator #(.width(16), .mode("twosComplement")) comparator_1 (
    .a(16'h258), .b(\总周期数 ), .eq(comparator_1_eq));  // open: gt, lt
  Comparator #(.width(16), .mode("twosComplement")) comparator_2 (
    .a(\总周期数 ), .b(16'h1), .eq(comparator_2_eq));  // open: gt, lt
  Comparator #(.width(16), .mode("twosComplement")) comparator_3 (
    .a(\总周期数 ), .b(16'h4), .eq(comparator_3_eq));  // open: gt, lt
  Comparator #(.width(16), .mode("twosComplement")) comparator_4 (
    .a(\总周期数 ), .b(16'h7), .eq(comparator_4_eq));  // open: gt, lt
  or or_5 (or_5_out, comparator_4_eq, comparator_5_eq);
  Comparator #(.width(16), .mode("twosComplement")) comparator_5 (
    .a(\总周期数 ), .b(16'h241), .eq(comparator_5_eq));  // open: gt, lt
  D_Flip_Flop #(.trigger("rising"), .Pre_Clr_Positions("LEGACY"), .NegatePresetClear("false"), .enable("true"), .NewFFLayout("false")) d_ff_1 (
    .clk(IRA), .D(1'b1), .Q(d_ff_1_q), .reset(INT1));  // open: Qn, preset, en
  D_Flip_Flop #(.trigger("rising"), .Pre_Clr_Positions("LEGACY"), .NegatePresetClear("false"), .enable("true"), .NewFFLayout("false")) d_ff_2 (
    .clk(IRB), .D(1'b1), .Q(d_ff_2_q), .reset(INT2));  // open: Qn, preset, en
  D_Flip_Flop #(.trigger("rising"), .Pre_Clr_Positions("LEGACY"), .NegatePresetClear("false"), .enable("true"), .NewFFLayout("false")) d_ff_3 (
    .clk(IRC), .D(1'b1), .Q(d_ff_3_q), .reset(INT3));  // open: Qn, preset, en
  Hex_Digit_Display hex_digit_display_2 (.value(LedData[23:20]));  // open: dp
  Hex_Digit_Display hex_digit_display_3 (.value(LedData[27:24]));  // open: dp
  or or_6 (or_6_out, comparator_1_eq, comparator_2_eq);
  Pull_Resistor #(.pull(0)) pull_resistor_1 (.node(IRA));
  assign IRA = or_6_out ? ~CLK : 1'bz;  // Controlled_Inverter controlled_inverter_1
  Pull_Resistor #(.pull(0)) pull_resistor_2 (.node(IRB));
  assign IRB = comparator_3_eq ? ~CLK : 1'bz;  // Controlled_Inverter controlled_inverter_2
  Pull_Resistor #(.pull(0)) pull_resistor_3 (.node(IRC));
  assign IRC = or_5_out ? ~CLK : 1'bz;  // Controlled_Inverter controlled_inverter_3
  or or_7 (or_7_out, d_ff_1_q, INT1);
  or or_8 (or_8_out, d_ff_2_q, INT2);
  or or_9 (or_9_out, d_ff_3_q, INT3);
  Hex_Digit_Display hex_digit_display_4 (.value(LedData[19:16]));  // open: dp
  Hex_Digit_Display hex_digit_display_5 (.value(LedData[15:12]));  // open: dp
  Priority_Encoder #(.select(2), .disabled("Z")) priority_encoder_2 (
    .in0(1'b1), .in1(INT), .in2(URET), .out(priority_encoder_2_out));  // open: in3, gs, en_out, en_in
  Multiplexer #(.select(2), .width(32), .disabled("Z"), .enable("false")) multiplexer_2 (
    .in0(PC_next), .in1(INTAddr), .in2(EPC), .out(multiplexer_2_out), .sel(priority_encoder_2_out));  // open: in3
  not not_1 (not_1_out, halt);
  and and_1 (and_1_out, or_7_out, ~CLR1);  // AND_Gate
  and and_2 (and_2_out, or_8_out, ~CLR2);  // AND_Gate
  and and_3 (and_3_out, or_9_out, ~CLR3);  // AND_Gate
  Hex_Digit_Display hex_digit_display_6 (.value(LedData[11:8]));  // open: dp
  Hex_Digit_Display hex_digit_display_7 (.value(LedData[7:4]));  // open: dp
  // Probe on \总周期数 
  Register #(.width(32), .trigger("rising"), .Select("low")) u_PC (
    .D(multiplexer_2_out), .en(or_10_out), .Q(PC), .clk(CLK), .clr(RST));
  or or_10 (or_10_out, Go, not_1_out);
  Comparator #(.width(32), .mode("unsigned")) comparator_6 (.a(R2), .b(32'h22), .eq(comparator_6_eq));  // open: gt, lt
  D_Flip_Flop #(.trigger("rising"), .Pre_Clr_Positions("LEGACY"), .NegatePresetClear("false"), .enable("true"), .NewFFLayout("false")) u_IR1 (
    .clk(CLK), .D(and_1_out), .Q(INT1));  // open: Qn, preset, en, reset
  D_Flip_Flop #(.trigger("rising"), .Pre_Clr_Positions("LEGACY"), .NegatePresetClear("false"), .enable("true"), .NewFFLayout("false")) IR1_2 (
    .clk(CLK), .D(and_2_out), .Q(INT2));  // open: Qn, preset, en, reset
  D_Flip_Flop #(.trigger("rising"), .Pre_Clr_Positions("LEGACY"), .NegatePresetClear("false"), .enable("true"), .NewFFLayout("false")) IR1_3 (
    .clk(CLK), .D(and_3_out), .Q(INT3));  // open: Qn, preset, en, reset
  Hex_Digit_Display hex_digit_display_8 (.value(LedData[3:0]));  // open: dp
  Adder #(.width(32)) adder_1 (.a(PC), .b(32'h4), .out(PC_4));  // open: cin, cout
  and and_4 (and_4_out, ecall, comparator_6_eq);
  and and_5 (halt, ecall, not_2_out);
  not not_2 (not_2_out, comparator_6_eq);
  // RiscV_Probe riscv_probe_1: pin names not known; wires that end beside it: IR
  Register #(.width(32), .trigger("rising"), .Select("low")) register_1 (
    .D(R1), .en(and_4_out), .Q(LedData), .clk(CLK));  // open: clr
  not not_3 (not_3_out, halt);
  Counter #(.width(16), .max('hffff), .ongoal("wrap"), .trigger("rising"), .behavior("new")) counter_1 (
    .count(not_3_out), .Q(\总周期数 ), .clk(CLK));  // open: load, D, carry, clr, preset, down
  Decoder #(.select(2), .tristate("false"), .disabled("Z"), .enable("false")) decoder_1 (
    .out1(decoder_1_out1), .out2(decoder_1_out2), .out3(decoder_1_out3), .sel(INTR));  // open: out0
  or or_11 (IR1_t, IR1, IRA);
  ROM #(.addrWidth(10), .dataWidth(32), .Select("high")) rom_1 (.addr(PC[11:2]), .data(IR));
  // RiscV_Probe riscv_probe_2: pin names not known; wires that end beside it: IR
  or or_12 (IR2_t, IR2, IRB);
  Priority_Encoder #(.select(2), .disabled("Z")) priority_encoder_3 (
    .in0(1'b1), .in1(INT1), .in2(INT2), .in3(INT3), .out(INTR));  // open: gs, en_out, en_in
  Multiplexer #(.select(2), .width(32), .disabled("Z"), .enable("false")) multiplexer_3 (
    .in1(32'h30ac), .in2(32'h3158), .in3(32'h3204), .out(INTAddr), .sel(INTR));  // open: in0
  and and_6 (and_6_out, decoder_1_out1, sup);
  and and_7 (and_7_out, decoder_1_out2, sup);
  and and_8 (and_8_out, decoder_1_out3, sup);
  \单周期硬布线控制器  \u_单周期硬布线控制器_1  (
    .Funct({IR[30], IR[25], IR[14:12]}), .OP(IR[6:2]), .ALU_OP(\单周期硬布线控制器_1_alu_op ),
    .MemToReg(\单周期硬布线控制器_1_memtoreg ), .MemWrite(MemWrite), .ALU_SRC(\单周期硬布线控制器_1_alu_src ),
    .RegWrite(RegWrite), .ecall(ecall), .S_type(\单周期硬布线控制器_1_s_type ), .Beq(\单周期硬布线控制器_1_beq ),
    .JAL(\单周期硬布线控制器_1_jal ), .Bne(\单周期硬布线控制器_1_bne ), .in_3(IR[21]), .uret(URET), .Jalr(\单周期硬布线控制器_1_jalr ),
    .LUI(\单周期硬布线控制器_1_lui ), .SB(sb), .BGEU(\单周期硬布线控制器_1_bgeu ), .CSRRSI(CSRRSI), .CSRRCI(CSRRCI));
  Multiplexer #(.select(1), .width(5), .disabled("Z"), .enable("false")) multiplexer_4 (
    .in0(IR[19:15]), .in1(5'b01010), .out(multiplexer_4_out), .sel(ecall));
  Multiplexer #(.select(1), .width(5), .disabled("Z"), .enable("false")) multiplexer_5 (
    .in0(IR[24:20]), .in1(5'b10001), .out(R2_num), .sel(ecall));
  Register #(.width(32), .trigger("rising"), .Select("low")) mEPC1 (
    .D(PC_next), .en(and_6_out), .Q(mEPC1_q), .clk(CLK));  // open: clr
  Register #(.width(32), .trigger("rising"), .Select("low")) mEPC2 (
    .D(PC_next), .en(and_7_out), .Q(mEPC2_q), .clk(CLK));  // open: clr
  Register #(.width(32), .trigger("rising"), .Select("low")) mEPC3 (
    .D(PC_next), .en(and_8_out), .Q(mEPC3_q), .clk(CLK));  // open: clr
  or or_13 (IR3_t, IR3, IRC);
  Multiplexer #(.select(1), .width(12), .disabled("Z"), .enable("false")) multiplexer_6 (
    .in0(IR[31:20]), .in1({IR[31:25], IR[11:7]}), .out(multiplexer_6_out), .sel(\单周期硬布线控制器_1_s_type ));
  assign bit_extender_1_out = {{20{IR[31]}}, {IR[31], IR[7], IR[30:25], IR[11:8]}};  // Bit_Extender bit_extender_1
  assign bit_extender_2_out = {{12{IR[31]}}, {IR[31], IR[19:12], IR[20], IR[30:21]}};  // Bit_Extender bit_extender_2
  assign bit_extender_3_out = {{12{IR[31]}}, IR[31:12]};  // Bit_Extender bit_extender_3
  Multiplexer #(.select(2), .width(32), .disabled("Z"), .enable("false")) multiplexer_7 (
    .in1(mEPC1_q), .in2(mEPC2_q), .in3(mEPC3_q), .out(EPC), .sel(INTR_NOW));  // open: in0
  Regifile regifile_1 (
    .Din(RDin), .Clk(CLK), .R1(R1), .R2(R2), .WE(RegWrite), .W_num(IR[11:7]), .R1_num(multiplexer_4_out),
    .R2_num(R2_num));
  assign bit_extender_4_out = {{20{multiplexer_6_out[11]}}, multiplexer_6_out};  // Bit_Extender bit_extender_4
  Shifter #(.width(32), .shift("ll")) shifter_1 (.in(bit_extender_1_out), .\dist (5'b00001), .out(shifter_1_out));
  Shifter #(.width(32), .shift("ll")) shifter_2 (.in(bit_extender_2_out), .\dist (5'b00001), .out(shifter_2_out));
  Shifter #(.width(32), .shift("ll")) shifter_3 (.in(bit_extender_3_out), .\dist (5'b01100), .out(ui));
  or or_14 (or_14_out, INT, CSRRCI);
  Adder #(.width(32)) adder_2 (.a(bit_extender_4_out), .b(R1), .out({I_dest, adder_2_out[0]}));  // open: cin, cout
  Adder #(.width(32)) adder_3 (.a(shifter_1_out), .b(PC), .out(B_dest));  // open: cin, cout
  Adder #(.width(32)) adder_4 (.a(shifter_2_out), .b(PC), .out(J_dest));  // open: cin, cout
  Multiplexer #(.select(1), .width(1), .disabled("Z"), .enable("false")) multiplexer_8 (
    .in0(d_ff_4_q), .in1(1'b1), .out(multiplexer_8_out), .sel(or_14_out));
  Multiplexer #(.select(1), .width(1), .disabled("Z"), .enable("false")) multiplexer_9 (
    .in0(multiplexer_8_out), .in1(1'b0), .out(multiplexer_9_out), .sel(CSRRSI));
  Multiplexer #(.select(1), .width(32), .disabled("Z"), .enable("false")) multiplexer_10 (
    .in0(R2), .in1(bit_extender_4_out), .out(multiplexer_10_out), .sel(\单周期硬布线控制器_1_alu_src ));
  Comparator #(.width(2), .mode("unsigned")) comparator_7 (.a(INTR), .b(INTR_NOW), .gt(sup));  // open: eq, lt
  D_Flip_Flop #(.trigger("rising"), .Pre_Clr_Positions("LEGACY"), .NegatePresetClear("false"), .enable("true"), .NewFFLayout("false")) d_ff_4 (
    .clk(CLK), .D(multiplexer_9_out), .Q(d_ff_4_q), .Qn(IE), .reset(URET));  // open: preset, en
  and and_9 (and_9_out, \单周期硬布线控制器_1_beq , alu_1_equal);
  and and_10 (and_10_out, \单周期硬布线控制器_1_bne , not_4_out);
  not not_4 (not_4_out, alu_1_equal);
  and and_11 (and_11_out, \单周期硬布线控制器_1_bgeu , alu_1_out_4);
  ALU alu_1 (
    .X(R1), .Y(multiplexer_10_out), .AluOP(\单周期硬布线控制器_1_alu_op ), .Equal(alu_1_equal), .Result(ALUout),
    .out_4(alu_1_out_4));  // open: Result_2, out_6
  or or_15 (or_15_out, URET, sup);
  Multiplexer #(.select(1), .width(32), .disabled("Z"), .enable("false")) multiplexer_11 (
    .in0(R2), .in1(sbdata), .out(MDin), .sel(sb));
  and and_12 (and_12_out, IE, or_15_out);
  Decoder #(.select(2), .tristate("false"), .disabled("Z"), .enable("false")) decoder_2 (
    .out1(decoder_2_out1), .out2(decoder_2_out2), .out3(decoder_2_out3), .sel(INTR));  // open: out0
  or or_16 (B, and_9_out, and_10_out, and_11_out);
  Decoder #(.select(2), .tristate("false"), .disabled("Z"), .enable("false")) decoder_3 (
    .out0(decoder_3_out0[0]), .out1(decoder_3_out0[1]), .out2(decoder_3_out0[2]), .out3(decoder_3_out0[3]),
    .sel(ALUout[1:0]));
  assign bit_extender_5_out = {{24{1'b0}}, R2[7:0]};  // Bit_Extender bit_extender_5
  and and_13 (and_13_out, and_12_out, decoder_2_out1);
  and and_14 (and_14_out, and_12_out, decoder_2_out2);
  and and_15 (and_15_out, and_12_out, decoder_2_out3);
  Multiplexer #(.select(1), .width(4), .disabled("Z"), .enable("false")) multiplexer_12 (
    .in0(4'b1111), .in1(decoder_3_out0), .out(multiplexer_12_out), .sel(sb));
  Shifter #(.width(32), .shift("ll")) shifter_4 (.in(bit_extender_5_out), .\dist (5'b01000), .out(shifter_4_out));
  Shifter #(.width(32), .shift("ll")) shifter_5 (.in(bit_extender_5_out), .\dist (5'b10000), .out(shifter_5_out));
  Shifter #(.width(32), .shift("ll")) shifter_6 (.in(bit_extender_5_out), .\dist (5'b11000), .out(shifter_6_out));
  not not_5 (not_5_out, CLR1);
  not not_6 (not_6_out, CLR2);
  not not_7 (not_7_out, CLR3);
  // MIPS_RAM mips_ram_1: pin names not known; wires that end beside it: sbdata, ALUout[11:2], MDin, MemWrite, multiplexer_12_out, CLK, 1'b1, mips_ram_1_p8
  and and_16 (INT, sup, IE);
  Demultiplexer #(.select(2), .width(1), .tristate("false"), .disabled("Z"), .enable("false")) demultiplexer_1 (
    .out1(CLR1), .out2(CLR2), .out3(CLR3), .in(URET), .sel(INTR_NOW));  // open: out0
  D_Flip_Flop #(.trigger("rising"), .Pre_Clr_Positions("LEGACY"), .NegatePresetClear("false"), .enable("true"), .NewFFLayout("false")) u_INT1 (
    .clk(CLK), .D(not_5_out), .Q(INT1_q), .en(and_13_out));  // open: Qn, preset, reset
  D_Flip_Flop #(.trigger("rising"), .Pre_Clr_Positions("LEGACY"), .NegatePresetClear("false"), .enable("true"), .NewFFLayout("false")) u_INT2 (
    .clk(CLK), .D(not_6_out), .Q(INT2_q), .en(and_14_out));  // open: Qn, preset, reset
  D_Flip_Flop #(.trigger("rising"), .Pre_Clr_Positions("LEGACY"), .NegatePresetClear("false"), .enable("true"), .NewFFLayout("false")) u_INT3 (
    .clk(CLK), .D(not_7_out), .Q(INT3_q), .en(and_15_out));  // open: Qn, preset, reset
  Multiplexer #(.select(2), .width(32), .disabled("Z"), .enable("false")) multiplexer_13 (
    .in0(bit_extender_5_out), .in1(shifter_4_out), .in2(shifter_5_out), .in3(shifter_6_out), .out(sbdata),
    .sel(ALUout[1:0]));
  Priority_Encoder #(.select(2), .disabled("Z")) priority_encoder_4 (
    .in0(1'b1), .in1(INT1_q), .in2(INT2_q), .in3(INT3_q), .out(INTR_NOW));  // open: gs, en_out, en_in
  Priority_Encoder #(.select(2), .disabled("Z")) priority_encoder_5 (
    .in0(1'b1), .in1(\单周期硬布线控制器_1_memtoreg ), .in2(jmp), .in3(\单周期硬布线控制器_1_lui ), .out(priority_encoder_5_out));  // open: gs, en_out, en_in
  Multiplexer #(.select(2), .width(32), .disabled("Z"), .enable("false")) multiplexer_14 (
    .in0(ALUout), .in1(mips_ram_1_p8), .in2(PC_4), .in3(ui), .out(RDin), .sel(priority_encoder_5_out));

  // Other names for the same wires on the sheet: byte[1:0] = ALUout[1:0]

  // Notes on the sheet:
  //   中断源
  //   中断等待指示
  //   总复位信号应将除ROM以外所有存储组件全部清零
  //   多级中断测试信号模拟器
  //   数码管输出
  //   Reset 
  //   Reset 
  //   Reset 
  //   数码管输出应该用寄存器锁存，否则显示数据只能一闪而过
  //   指令探针
  //   指令存储器
  //   指令字
  //   contents of rom_1 (hex, n*v repeats v):
  //   7d000113 100413 1f41993 41f9d993 433 c00913 800b13 140413 f47413 800293 100313 499993 89e9b3 1300533
  //   2200893 73 406282b3 fe0294e3 140413 f00f93 1f47433 1c41413 800293 100313 49d993 89e9b3 1300533
  //   2200893 73 406282b3 fe0294e3 1c45413 406b0b33 b0463 f95ff06f 2b3 fff2c293 1029293 fff2e293 500533
  //   2200893 73 f5dff06f 1112023 410113 a12023 410113 812023 410113 1312023 410113 1412023 410113 1512023
  //   410113 1612023 410113 40e073 100b13 300a13 100a93 1600433 441413 14469b3 1300533 2200893 73 fe0416e3
  //   415a0a33 fe0a10e3 40f073 ffc10113 12b03 ffc10113 12a83 ffc10113 12a03 ffc10113 12983 ffc10113 12403
  //   ffc10113 12503 ffc10113 12883 200073 1112023 410113 a12023 410113 812023 410113 1312023 410113
  //   1412023 410113 1512023 410113 1612023 410113 40e073 200b13 300a13 100a93 1600433 441413 14469b3
  //   1300533 2200893 73 fe0416e3 415a0a33 fe0a10e3 40f073 ffc10113 12b03 ffc10113 12a83 ffc10113 12a03
  //   ffc10113 12983 ffc10113 12403 ffc10113 12503 ffc10113 12883 200073 1112023 410113 a12023 410113
  //   812023 410113 1312023 410113 1412023 410113 1512023 410113 1612023 410113 40e073 300b13 300a13
  //   100a93 1600433 441413 14469b3 1300533 2200893 73 fe0416e3 415a0a33 fe0a10e3 40f073 ffc10113 12b03
  //   ffc10113 12a83 ffc10113 12a03 ffc10113 12983 ffc10113 12403 ffc10113 12503 ffc10113 12883 200073
  //   JAL
  //   JALR
  //   URET
  //   I
  //   S
  //   Beq
  //   Bne
  //   Bgeu
  //   MemToReg
  //   MemWrite
  //   AluOP
  //   AluSrcB
  //   RegWrite
  //   LUI
  //   Sb
  //   B
  //   J
  //   为方便自动评测，需要输出PC，IR，寄存器堆写如数据RDin
  //   RAM写使能MemWrite、RAM写入数据MDin等信号
  //   数据存储器
endmodule

module \流水中断  (
  output RegWrite,
  output MemWrite,
  output [31:0] IF_PC,
  output [31:0] ID_PC,
  output [31:0] EX_PC,
  output [31:0] M_PC,
  output [31:0] WB_PC,
  output [31:0] RDin,
  output [31:0] MDin,
  output [31:0] LedData
);

  wire alu_1_equal, alu_1_out_4, and_1_out, and_2_out, and_3_out, and_4_out, and_5_out, and_6_out, and_7_out,
       and_9_out, and_10_out, and_11_out, branch, CLK, clock_1_out, clock_2_out, CLR1, CLR2, CLR3,
       comparator_1_eq, comparator_2_eq, comparator_2_lt, d_ff_1_q, d_ff_2_q, d_ff_3_q, d_ff_4_q, ecall,
       ex_i, ex_j, EX_MEM_out_17, EX_MEM_out_19, EX_MEM_out_20, EX_MEM_out_21, EX_MEM_out_22, EX_MEM_out_23,
       ex_uret, Go, halt, ID_EX_out_30, ID_EX_out_31, ID_EX_out_32, ID_EX_out_33, ID_EX_out_34, ID_EX_out_36,
       ID_EX_out_37, ID_EX_out_38, ID_EX_out_39, IE, INT, INT1, INT2, INT3, IR1, IR2, IR3, jal, jalr,
       MEM_WB_out_15, MEM_WB_out_17, MEM_WB_out_18, MEM_WB_out_19, nand_1_out, not_1_out, not_2_out,
       not_3_out, not_4_out, not_5_out, not_6_out, or_5_out, or_6_out, or_7_out, or_8_out, or_9_out,
       or_11_out, priority_encoder_3_gs, redirectcontrol_1_branchtaken, redirectcontrol_1_flush2,
       redirectcontrol_1_jal_2, redirectcontrol_1_jalr_2, redirectcontrol_1_stall, register_1_q, RST, run,
       uret, W1, W2, W3, \单周期硬布线控制器_1_alu_src , \单周期硬布线控制器_1_beq , \单周期硬布线控制器_1_bgeu , \单周期硬布线控制器_1_bne ,
       \单周期硬布线控制器_1_ecall , \单周期硬布线控制器_1_lui , \单周期硬布线控制器_1_memtoreg , \单周期硬布线控制器_1_memwrite ,
       \单周期硬布线控制器_1_regwrite , \单周期硬布线控制器_1_s_type , \单周期硬布线控制器_1_sb ;
  wire [0:0] adder_3_out;
  wire [1:0] \byte , ID_EX_out_43, ID_EX_out_45, priority_encoder_1_out, priority_encoder_2_out,
       priority_encoder_3_out, priority_encoder_4_out, priority_encoder_5_out, redirectcontrol_1_r1_src,
       redirectcontrol_1_r2_src, register_4_q;
  wire [3:0] decoder_1_out0, ID_EX_out_35, multiplexer_13_out, \单周期硬布线控制器_1_alu_op ;
  wire [4:0] EX_MEM_out_26, ID_EX_writereg_2, multiplexer_3_out, multiplexer_4_out, W_num;
  wire [11:0] multiplexer_5_out;
  wire [12:0] CNT_num;
  wire [15:0] \LoadUse次数 , \总周期数 , \插入气泡数 , \无条件分支数 , \条件分支成功数 ;
  wire [31:0] adder_2_out, adder_6_out, alu_1_result, B_dest, bit_extender_1_out, bit_extender_2_out,
       bit_extender_3_out, bit_extender_4_out, bit_extender_5_out, EPC, EX_IR, EX_MEM_out_25, ID_EX_eb_2,
       ID_EX_ei_s_2, ID_EX_ej_2, ID_EX_eu_2, ID_EX_r1_2, ID_EX_r2_2, ID_IR, IF_ID_out_10, IF_IR, IntAddr,
       J_dest, MEM_ALU, MEM_IR, MEM_U, MEM_WB_out_20, MEM_WB_out_21, MEM_WB_out_23, mips_ram_1_p6,
       multiplexer_1_out, multiplexer_2_out, multiplexer_7_out, multiplexer_10_out, pc_4, R1, R2,
       regifile_1_r1, regifile_1_r2, sbdata, shifter_1_out, shifter_2_out, shifter_3_out, shifter_4_out,
       shifter_5_out, shifter_6_out, WB_IR;
  wire [31:1] I_dest;
  wire [31:2] EX_MEM_out_24;

  Button \u_总复位  (.out(RST));
  Button _1 (.out(IR1));
  Button _2 (.out(IR2));
  Button _3 (.out(IR3));
  // Probe on \总周期数 
  // Probe on \总周期数 
  Button \u_继续运行  (.out(Go));
  LED #(.active("true")) led_1 (.in(W1));
  LED #(.active("true")) led_2 (.in(W2));
  LED #(.active("true")) led_3 (.in(W3));
  Hex_Digit_Display hex_digit_display_1 (.value(LedData[31:28]));  // open: dp
  // Probe on IF_PC[19:0]
  // RiscV_Probe riscv_probe_1: pin names not known; wires that end beside it: IF_IR
  not not_1 (not_1_out, redirectcontrol_1_stall);
  Priority_Encoder #(.select(2), .disabled("Z")) priority_encoder_1 (
    .in0(1'b1), .in1(redirectcontrol_1_jal_2), .in2(redirectcontrol_1_jalr_2), .in3(branch),
    .out(priority_encoder_1_out));  // open: gs, en_out, en_in
  Multiplexer #(.select(2), .width(32), .disabled("Z"), .enable("false")) multiplexer_1 (
    .in0(pc_4), .in1(J_dest), .in2({I_dest, 1'b0}), .in3(B_dest), .out(multiplexer_1_out),
    .sel(priority_encoder_1_out));
  or or_1 (W1, INT1, d_ff_3_q);
  D_Flip_Flop #(.trigger("rising"), .Pre_Clr_Positions("LEGACY"), .NegatePresetClear("false"), .enable("true"), .NewFFLayout("false")) d_ff_1 (
    .clk(IR2), .D(1'b1), .Q(d_ff_1_q), .reset(INT2));  // open: Qn, preset, en
  or or_2 (W2, INT2, d_ff_1_q);
  D_Flip_Flop #(.trigger("rising"), .Pre_Clr_Positions("LEGACY"), .NegatePresetClear("false"), .enable("true"), .NewFFLayout("false")) d_ff_2 (
    .clk(IR3), .D(1'b1), .Q(d_ff_2_q), .reset(INT3));  // open: Qn, preset, en
  or or_3 (W3, INT3, d_ff_2_q);
  Hex_Digit_Display hex_digit_display_2 (.value(LedData[23:20]));  // open: dp
  Hex_Digit_Display hex_digit_display_3 (.value(LedData[27:24]));  // open: dp
  // Probe on ID_PC[19:0]
  // RiscV_Probe riscv_probe_2: pin names not known; wires that end beside it: ID_IR
  Priority_Encoder #(.select(2), .disabled("Z")) priority_encoder_2 (
    .in0(1'b1), .in1(INT), .in2(ex_uret), .out(priority_encoder_2_out));  // open: in3, gs, en_out, en_in
  or or_4 (run, Go, not_2_out);
  not not_2 (not_2_out, halt);
  Comparator #(.width(32), .mode("unsigned")) comparator_1 (.a(R2), .b(32'h22), .eq(comparator_1_eq));  // open: gt, lt
  Register #(.width(1), .trigger("rising"), .Select("low")) register_1 (
    .D(and_6_out), .en(run), .Q(register_1_q), .clk(CLK));  // open: clr
  D_Flip_Flop #(.trigger("rising"), .Pre_Clr_Positions("LEGACY"), .NegatePresetClear("false"), .enable("true"), .NewFFLayout("false")) d_ff_3 (
    .clk(IR1), .D(1'b1), .Q(d_ff_3_q), .reset(INT1));  // open: Qn, preset, en
  Hex_Digit_Display hex_digit_display_4 (.value(LedData[19:16]));  // open: dp
  Hex_Digit_Display hex_digit_display_5 (.value(LedData[15:12]));  // open: dp
  Register #(.width(32), .trigger("rising"), .Select("low")) PC (
    .D(multiplexer_2_out), .en(and_1_out), .Q(IF_PC), .clk(CLK));  // open: clr
  Multiplexer #(.select(2), .width(32), .disabled("Z"), .enable("false")) multiplexer_2 (
    .in0(multiplexer_1_out), .in1(IntAddr), .in2(EPC), .out(multiplexer_2_out), .sel(priority_encoder_2_out));  // open: in3
  and and_1 (and_1_out, not_1_out, run);
  not not_3 (not_3_out, comparator_1_eq);
  Register #(.width(1), .trigger("rising"), .Select("low")) register_2 (
    .D(register_1_q), .en(run), .Q(halt), .clk(CLK));  // open: clr
  or or_5 (or_5_out, d_ff_3_q, INT1);
  and and_2 (and_2_out, or_5_out, ~CLR1);  // AND_Gate
  or or_6 (or_6_out, d_ff_1_q, INT2);
  and and_3 (and_3_out, or_6_out, ~CLR2);  // AND_Gate
  or or_7 (or_7_out, d_ff_2_q, INT3);
  and and_4 (and_4_out, or_7_out, ~CLR3);  // AND_Gate
  Hex_Digit_Display hex_digit_display_6 (.value(LedData[11:8]));  // open: dp
  Hex_Digit_Display hex_digit_display_7 (.value(LedData[7:4]));  // open: dp
  Clock #(.highDuration(1), .lowDuration(1)) clock_1 (.out(clock_1_out));
  // Probe on EX_PC[19:0]
  // RiscV_Probe riscv_probe_3: pin names not known; wires that end beside it: clock_1_out, EX_IR, CLK
  and and_5 (and_5_out, ecall, comparator_1_eq);
  and and_6 (and_6_out, ecall, not_3_out);
  not not_4 (not_4_out, halt);
  Counter #(.width(16), .max('hffff), .ongoal("wrap"), .trigger("rising"), .behavior("new")) counter_1 (
    .count(not_4_out), .Q(\总周期数 ), .clk(CLK));  // open: load, D, carry, clr, preset, down
  D_Flip_Flop #(.trigger("rising"), .Pre_Clr_Positions("LEGACY"), .NegatePresetClear("false"), .enable("true"), .NewFFLayout("false")) u_IR1 (
    .clk(CLK), .D(and_2_out), .Q(INT1));  // open: Qn, preset, en, reset
  D_Flip_Flop #(.trigger("rising"), .Pre_Clr_Positions("LEGACY"), .NegatePresetClear("false"), .enable("true"), .NewFFLayout("false")) IR1_2 (
    .clk(CLK), .D(and_3_out), .Q(INT2));  // open: Qn, preset, en, reset
  D_Flip_Flop #(.trigger("rising"), .Pre_Clr_Positions("LEGACY"), .NegatePresetClear("false"), .enable("true"), .NewFFLayout("false")) IR1_3 (
    .clk(CLK), .D(and_4_out), .Q(INT3));  // open: Qn, preset, en, reset
  Hex_Digit_Display hex_digit_display_8 (.value(LedData[3:0]));  // open: dp
  ROM #(.addrWidth(10), .dataWidth(32), .Select("high")) rom_1 (.addr(IF_PC[11:2]), .data(IF_IR));
  Adder #(.width(32)) adder_1 (.a(IF_PC), .b(32'h4), .out(pc_4));  // open: cin, cout
  Register #(.width(32), .trigger("rising"), .Select("low")) register_3 (
    .D(R1), .en(and_5_out), .Q(LedData), .clk(CLK));  // open: clr
  // Probe on \总周期数 
  // Probe on M_PC[19:0]
  // RiscV_Probe riscv_probe_4: pin names not known; wires that end beside it: MEM_IR
  or or_8 (or_8_out, INT, redirectcontrol_1_branchtaken);
  IF_ID IF_ID (
    .in_5(IF_IR), .out_10(IF_ID_out_10), .CLK(CLK), .in_4(IF_PC), .out_9(ID_PC), .in_7(IF_IR),
    .out_12(ID_IR), .run(run), .in_1(or_8_out), .stall(redirectcontrol_1_stall));  // open: in_6, out_11
  // Probe on \总周期数 
  // Probe on \无条件分支数 
  // Probe on \条件分支成功数 
  // Probe on \插入气泡数 
  // Probe on \LoadUse次数 
  // Probe on IF_PC[11:0]
  // Probe on WB_PC[19:0]
  // RiscV_Probe riscv_probe_5: pin names not known; wires that end beside it: WB_IR
  \单周期硬布线控制器  \u_单周期硬布线控制器_1  (
    .Funct({IF_ID_out_10[30], IF_ID_out_10[25], IF_ID_out_10[14:12]}), .OP(IF_ID_out_10[6:2]),
    .ALU_OP(\单周期硬布线控制器_1_alu_op ), .MemToReg(\单周期硬布线控制器_1_memtoreg ), .MemWrite(\单周期硬布线控制器_1_memwrite ),
    .ALU_SRC(\单周期硬布线控制器_1_alu_src ), .RegWrite(\单周期硬布线控制器_1_regwrite ), .ecall(\单周期硬布线控制器_1_ecall ),
    .S_type(\单周期硬布线控制器_1_s_type ), .Beq(\单周期硬布线控制器_1_beq ), .JAL(jal), .Bne(\单周期硬布线控制器_1_bne ),
    .in_3(IF_ID_out_10[21]), .uret(uret), .Jalr(jalr), .LUI(\单周期硬布线控制器_1_lui ), .SB(\单周期硬布线控制器_1_sb ),
    .BGEU(\单周期硬布线控制器_1_bgeu ));  // open: CSRRSI, CSRRCI
  Multiplexer #(.select(1), .width(5), .disabled("Z"), .enable("false")) multiplexer_3 (
    .in0(IF_ID_out_10[19:15]), .in1(5'b01010), .out(multiplexer_3_out), .sel(\单周期硬布线控制器_1_ecall ));
  Multiplexer #(.select(1), .width(5), .disabled("Z"), .enable("false")) multiplexer_4 (
    .in0(IF_ID_out_10[24:20]), .in1(5'b10001), .out(multiplexer_4_out), .sel(\单周期硬布线控制器_1_ecall ));
  Priority_Encoder #(.select(2), .disabled("Z")) priority_encoder_3 (
    .in0(INT1), .in1(INT2), .in2(INT3), .out(priority_encoder_3_out), .gs(priority_encoder_3_gs));  // open: in3, en_out, en_in
  // Probe on EX_PC[11:0]
  // Probe on ID_PC[11:0]
  Multiplexer #(.select(1), .width(12), .disabled("Z"), .enable("false")) multiplexer_5 (
    .in0(IF_ID_out_10[31:20]), .in1({IF_ID_out_10[31:25], IF_ID_out_10[11:7]}), .out(multiplexer_5_out),
    .sel(\单周期硬布线控制器_1_s_type ));
  assign bit_extender_1_out = {{20{IF_ID_out_10[31]}}, {IF_ID_out_10[31], IF_ID_out_10[7], IF_ID_out_10[30:25], IF_ID_out_10[11:8]}};  // Bit_Extender bit_extender_1
  assign bit_extender_2_out = {{12{IF_ID_out_10[31]}}, {IF_ID_out_10[31], IF_ID_out_10[19:12], IF_ID_out_10[20], IF_ID_out_10[30:21]}};  // Bit_Extender bit_extender_2
  assign bit_extender_3_out = {{12{IF_ID_out_10[31]}}, IF_ID_out_10[31:12]};  // Bit_Extender bit_extender_3
  Multiplexer #(.select(2), .width(32), .disabled("Z"), .enable("false")) multiplexer_6 (
    .in0(32'h30ac), .in1(32'h3150), .in2(32'h31f4), .out(IntAddr), .sel(priority_encoder_3_out));  // open: in3
  not not_5 (not_5_out, ex_uret);
  Adder #(.width(32)) adder_2 (.a(EX_PC), .b(32'h4), .out(adder_2_out));  // open: cin, cout
  // Probe on M_PC[11:0]
  D_Flip_Flop #(.trigger("high"), .Pre_Clr_Positions("LEGACY"), .NegatePresetClear("false"), .enable("true"), .NewFFLayout("false")) d_ff_4 (.Q(d_ff_4_q));  // open: clk, D, Qn, preset, en, reset
  // Probe on 13'h14
  Regifile regifile_1 (
    .Din(RDin), .Clk(CLK), .R1(regifile_1_r1), .R2(regifile_1_r2), .WE(RegWrite), .W_num(W_num),
    .R1_num(multiplexer_3_out), .R2_num(multiplexer_4_out));
  assign bit_extender_4_out = {{20{multiplexer_5_out[11]}}, multiplexer_5_out};  // Bit_Extender bit_extender_4
  and and_7 (and_7_out, priority_encoder_3_gs, not_5_out);
  Priority_Encoder #(.select(2), .disabled("Z")) priority_encoder_4 (
    .in0(1'b1), .in1(ex_j), .in2(ex_i), .in3(branch), .out(priority_encoder_4_out));  // open: gs, en_out, en_in
  // Probe on WB_PC[11:0]
  Comparator #(.width(13), .mode("twosComplement")) comparator_2 (
    .a(CNT_num), .b(13'h14), .eq(comparator_2_eq), .lt(comparator_2_lt));  // open: gt
  Clock #(.highDuration(1), .lowDuration(1)) clock_2 (.out(clock_2_out));
  ReDirectControl redirectcontrol_1 (
    .halt(halt), .clk(CLK), .jal_2(redirectcontrol_1_jal_2), .jalr_2(redirectcontrol_1_jalr_2),
    .stall(redirectcontrol_1_stall), .branchtaken(redirectcontrol_1_branchtaken), .instr(IF_ID_out_10),
    .ecall(\单周期硬布线控制器_1_ecall ), .alusrc(\单周期硬布线控制器_1_alu_src ), .flush2(redirectcontrol_1_flush2),
    .ex_W_num(ID_EX_writereg_2), .jal(ex_j), .jalr(ex_i), .ex_regwrite(ID_EX_out_37), .branch(branch),
    .mem_W_num(EX_MEM_out_26), .mem_regwrite(EX_MEM_out_19), .\无条件 (\无条件分支数 ), .\条件 (\条件分支成功数 ),
    .\气泡 (\插入气泡数 ), .r1_src(redirectcontrol_1_r1_src), .r2_src(redirectcontrol_1_r2_src),
    .ex_toreg(ID_EX_out_33), .loaduse(\LoadUse次数 ), .stype(\单周期硬布线控制器_1_s_type ));
  or or_9 (or_9_out, INT, redirectcontrol_1_flush2);
  ID_EX ID_EX (
    .Beq(\单周期硬布线控制器_1_beq ), .Bne(\单周期硬布线控制器_1_bne ), .Bgeu(\单周期硬布线控制器_1_bgeu ),
    .MemToReg(\单周期硬布线控制器_1_memtoreg ), .MemWrite(\单周期硬布线控制器_1_memwrite ), .AluOP(\单周期硬布线控制器_1_alu_op ),
    .AluSrcB(\单周期硬布线控制器_1_alu_src ), .RegWrite(\单周期硬布线控制器_1_regwrite ), .LUI(\单周期硬布线控制器_1_lui ),
    .Sb(\单周期硬布线控制器_1_sb ), .CLK(CLK), .R1(regifile_1_r1), .R2(regifile_1_r2), .WriteReg(IF_ID_out_10[11:7]),
    .R1_2(ID_EX_r1_2), .R2_2(ID_EX_r2_2), .WriteReg_2(ID_EX_writereg_2), .out_30(ID_EX_out_30),
    .out_31(ID_EX_out_31), .out_32(ID_EX_out_32), .out_33(ID_EX_out_33), .out_36(ID_EX_out_36),
    .out_37(ID_EX_out_37), .out_38(ID_EX_out_38), .out_39(ID_EX_out_39), .out_34(ID_EX_out_34),
    .out_35(ID_EX_out_35), .pc(ID_PC), .pc_2(EX_PC), .EB(bit_extender_1_out), .EJ(bit_extender_2_out),
    .EU(bit_extender_3_out), .EB_2(ID_EX_eb_2), .EJ_2(ID_EX_ej_2), .EU_2(ID_EX_eu_2),
    .EI_S(bit_extender_4_out), .EI_S_2(ID_EX_ei_s_2), .out_40(ex_j), .jal(jal), .ir(ID_IR), .ir_2(EX_IR),
    .ecall(\单周期硬布线控制器_1_ecall ), .out_42(ecall), .run(run), .in_1(or_9_out), .jalr(jalr), .out_41(ex_i),
    .out_43(ID_EX_out_43), .r1src(redirectcontrol_1_r1_src), .out_45(ID_EX_out_45),
    .r2src(redirectcontrol_1_r2_src), .uret(uret), .uret_2(ex_uret));  // open: pred, pred_2
  D_Flip_Flop #(.trigger("rising"), .Pre_Clr_Positions("LEGACY"), .NegatePresetClear("false"), .enable("true"), .NewFFLayout("false")) d_ff_5 (
    .clk(CLK), .D(and_7_out), .Qn(IE));  // open: Q, preset, en, reset
  Multiplexer #(.select(2), .width(32), .disabled("Z"), .enable("false")) multiplexer_7 (
    .in0(adder_2_out), .in1(J_dest), .in2({I_dest, 1'b0}), .in3(B_dest), .out(multiplexer_7_out),
    .sel(priority_encoder_4_out));
  nand nand_1 (nand_1_out, d_ff_4_q, comparator_2_eq);
  Counter #(.width(13), .max('h1fff), .ongoal("stay"), .trigger("rising"), .behavior("old")) counter_2 (
    .count(comparator_2_lt), .Q(CNT_num), .clk(clock_2_out));  // open: load, D, carry, clr, preset
  Shifter #(.width(32), .shift("ll")) shifter_1 (.in(ID_EX_eb_2), .\dist (5'b00001), .out(shifter_1_out));
  Shifter #(.width(32), .shift("ll")) shifter_2 (.in(ID_EX_ej_2), .\dist (5'b00001), .out(shifter_2_out));
  Shifter #(.width(32), .shift("ll")) shifter_3 (.in(ID_EX_eu_2), .\dist (5'b01100), .out(shifter_3_out));
  and and_8 (INT, priority_encoder_3_gs, IE);
  Register #(.width(32), .trigger("rising"), .Select("low")) mEPC (
    .D(multiplexer_7_out), .en(INT), .Q(EPC), .clk(CLK));  // open: clr
  assign CLK = nand_1_out ? clock_2_out : 1'bz;  // Controlled_Buffer controlled_buffer_1
  Multiplexer #(.select(2), .width(32), .disabled("Z"), .enable("false")) multiplexer_8 (
    .in0(ID_EX_r1_2), .in1(RDin), .in2(MEM_ALU), .out(R1), .sel(ID_EX_out_43));  // open: in3
  Multiplexer #(.select(2), .width(32), .disabled("Z"), .enable("false")) multiplexer_9 (
    .in0(ID_EX_r2_2), .in1(RDin), .in2(MEM_ALU), .out(R2), .sel(ID_EX_out_45));  // open: in3
  Adder #(.width(32)) adder_3 (.a(ID_EX_ei_s_2), .b(R1), .out({I_dest, adder_3_out[0]}));  // open: cin, cout
  Pull_Resistor #(.pull(1)) pull_resistor_1 (.node(CLK));
  Multiplexer #(.select(1), .width(32), .disabled("Z"), .enable("false")) multiplexer_10 (
    .in0(R2), .in1(ID_EX_ei_s_2), .out(multiplexer_10_out), .sel(ID_EX_out_36));
  Adder #(.width(32)) adder_4 (.a(shifter_1_out), .b(EX_PC), .out(B_dest));  // open: cin, cout
  Adder #(.width(32)) adder_5 (.a(shifter_2_out), .b(EX_PC), .out(J_dest));  // open: cin, cout
  Demultiplexer #(.select(2), .width(1), .tristate("false"), .disabled("Z"), .enable("false")) demultiplexer_1 (
    .out0(CLR1), .out1(CLR2), .out2(CLR3), .in(ex_uret), .sel(register_4_q));  // open: out3
  Register #(.width(2), .trigger("rising"), .Select("low")) register_4 (
    .D(priority_encoder_3_out), .en(INT), .Q(register_4_q), .clk(CLK));  // open: clr
  or or_10 (branch, and_9_out, and_10_out, and_11_out);
  and and_9 (and_9_out, ID_EX_out_30, alu_1_equal);
  and and_10 (and_10_out, ID_EX_out_31, not_6_out);
  not not_6 (not_6_out, alu_1_equal);
  and and_11 (and_11_out, ID_EX_out_32, alu_1_out_4);
  ALU alu_1 (
    .X(R1), .Y(multiplexer_10_out), .AluOP(ID_EX_out_35), .Equal(alu_1_equal), .Result(alu_1_result),
    .out_4(alu_1_out_4));  // open: Result_2, out_6
  EX_MEM EX_MEM (
    .MemToReg(ID_EX_out_33), .MemWrite(ID_EX_out_34), .out_17(EX_MEM_out_17), .out_18(MemWrite),
    .RegWrite(ID_EX_out_37), .out_19(EX_MEM_out_19), .LUI(ID_EX_out_38), .out_20(EX_MEM_out_20),
    .Sb(ID_EX_out_39), .out_21(EX_MEM_out_21), .Alu(alu_1_result), .out_24({EX_MEM_out_24, \byte }), .R2(R2),
    .out_25(EX_MEM_out_25), .udata(shifter_3_out), .out_27(MEM_U), .pc(EX_PC), .out_28(M_PC), .ir(EX_IR),
    .out_29(MEM_IR), .CLK(CLK), .in_11(ID_EX_writereg_2), .out_26(EX_MEM_out_26), .run(run), .in_1(1'b0),
    .jal(ex_j), .out_22(EX_MEM_out_22), .jalr(ex_i), .out_23(EX_MEM_out_23));
  Multiplexer #(.select(1), .width(32), .disabled("Z"), .enable("false")) multiplexer_11 (
    .in0({EX_MEM_out_24, \byte }), .in1(MEM_U), .out(MEM_ALU), .sel(EX_MEM_out_20));
  Multiplexer #(.select(1), .width(32), .disabled("Z"), .enable("false")) multiplexer_12 (
    .in0(EX_MEM_out_25), .in1(sbdata), .out(MDin), .sel(EX_MEM_out_21));
  Decoder #(.select(2), .tristate("false"), .disabled("Z"), .enable("false")) decoder_1 (
    .out0(decoder_1_out0[0]), .out1(decoder_1_out0[1]), .out2(decoder_1_out0[2]), .out3(decoder_1_out0[3]),
    .sel(\byte ));
  assign bit_extender_5_out = {{24{1'b0}}, EX_MEM_out_25[7:0]};  // Bit_Extender bit_extender_5
  Multiplexer #(.select(1), .width(4), .disabled("Z"), .enable("false")) multiplexer_13 (
    .in0(4'b1111), .in1(decoder_1_out0), .out(multiplexer_13_out), .sel(EX_MEM_out_21));
  Shifter #(.width(32), .shift("ll")) shifter_4 (.in(bit_extender_5_out), .\dist (5'b01000), .out(shifter_4_out));
  Shifter #(.width(32), .shift("ll")) shifter_5 (.in(bit_extender_5_out), .\dist (5'b10000), .out(shifter_5_out));
  Shifter #(.width(32), .shift("ll")) shifter_6 (.in(bit_extender_5_out), .\dist (5'b11000), .out(shifter_6_out));
  Multiplexer #(.select(2), .width(32), .disabled("Z"), .enable("false")) multiplexer_14 (
    .in0(bit_extender_5_out), .in1(shifter_4_out), .in2(shifter_5_out), .in3(shifter_6_out), .out(sbdata),
    .sel(\byte ));
  // MIPS_RAM mips_ram_1: pin names not known; wires that end beside it: EX_MEM_out_24[11:2], MDin, MemWrite, multiplexer_13_out, CLK, mips_ram_1_p6
  MEM_WB MEM_WB (
    .in_2(EX_MEM_out_17), .out_15(MEM_WB_out_15), .in_3(EX_MEM_out_19), .out_16(RegWrite),
    .in_4(EX_MEM_out_20), .out_17(MEM_WB_out_17), .in_7({EX_MEM_out_24, \byte }), .out_20(MEM_WB_out_20),
    .in_8(mips_ram_1_p6), .out_21(MEM_WB_out_21), .in_10(MEM_U), .out_23(MEM_WB_out_23),
    .in_9(EX_MEM_out_26), .out_22(W_num), .in_11(M_PC), .out_24(WB_PC), .in_12(MEM_IR), .out_25(WB_IR),
    .CLK(CLK), .run(run), .in_1(1'b0), .in_5(EX_MEM_out_22), .out_18(MEM_WB_out_18), .in_6(EX_MEM_out_23),
    .out_19(MEM_WB_out_19));
  or or_11 (or_11_out, MEM_WB_out_18, MEM_WB_out_19);
  Adder #(.width(32)) adder_6 (.a(WB_PC), .b(32'h4), .out(adder_6_out));  // open: cin, cout
  Priority_Encoder #(.select(2), .disabled("Z")) priority_encoder_5 (
    .in0(1'b1), .in1(MEM_WB_out_15), .in2(or_11_out), .in3(MEM_WB_out_17), .out(priority_encoder_5_out));  // open: gs, en_out, en_in
  Multiplexer #(.select(2), .width(32), .disabled("Z"), .enable("false")) multiplexer_15 (
    .in0(MEM_WB_out_20), .in1(MEM_WB_out_21), .in2(adder_6_out), .in3(MEM_WB_out_23), .out(RDin),
    .sel(priority_encoder_5_out));

  // Other names for the same wires on the sheet: MEM_PC[31:0] = M_PC

  // Notes on the sheet:
  //   中断源
  //   时空图监测，可删除
  //   中断等待指示
  //   数码管输出
  //   Reset 
  //   Reset 
  //   Reset 
  //   contents of rom_1 (hex, n*v repeats v):
  //   7d000113 100413 1f41993 41f9d993 433 c00913 800b13 140413 f47413 800293 100313 499993 89e9b3 1300533
  //   2200893 73 406282b3 fe0294e3 140413 f00f93 1f47433 1c41413 800293 100313 49d993 89e9b3 1300533
  //   2200893 73 406282b3 fe0294e3 1c45413 406b0b33 b0463 f95ff06f 2b3 fff2c293 1029293 fff2e293 500533
  //   2200893 73 f5dff06f 1112023 410113 a12023 410113 812023 410113 1312023 410113 1412023 410113 1512023
  //   410113 1612023 410113 100b13 300a13 100a93 1600433 441413 14469b3 1300533 2200893 73 fe0416e3
  //   415a0a33 fe0a10e3 ffc10113 12b03 ffc10113 12a83 ffc10113 12a03 ffc10113 12983 ffc10113 12403
  //   ffc10113 12503 ffc10113 12883 200073 1112023 410113 a12023 410113 812023 410113 1312023 410113
  //   1412023 410113 1512023 410113 1612023 410113 200b13 300a13 100a93 1600433 441413 14469b3 1300533
  //   2200893 73 fe0416e3 415a0a33 fe0a10e3 ffc10113 12b03 ffc10113 12a83 ffc10113 12a03 ffc10113 12983
  //   ffc10113 12403 ffc10113 12503 ffc10113 12883 200073 1112023 410113 a12023 410113 812023 410113
  //   1312023 410113 1412023 410113 1512023 410113 1612023 410113 300b13 300a13 100a93 1600433 441413
  //   14469b3 1300533 2200893 73 fe0416e3 415a0a33 fe0a10e3 ffc10113 12b03 ffc10113 12a83 ffc10113 12a03
  //   ffc10113 12983 ffc10113 12403 ffc10113 12503 ffc10113 12883 200073
  //   I
  //   S
  //   Beq
  //   Bne
  //   Bgeu
  //   MemToReg
  //   MemWrite
  //   AluOP
  //   AluSrcB
  //   Regwrite
  //   Lui
  //   Sb
  //   Ecall
  //   B
  //   J
  //   控制位
  //   流水调试日志用
  //   暂停节拍，不能为0
  //   戳工具置1进入计数暂停模式，ctrl+k时钟自动运行到对应节拍暂停
  //   ctrl+k关闭时钟连续运行，将控制位置零，进入单步调试模式调试
  //   可计数暂停的时钟源
  //   为方便自动评测，需要输出流水线各段保存的PC值，注意是PC不是PC+4，另外ID段寄存器写入信息，Mem段内存写入信息也要输出
endmodule

module \封装正确性测试  (
);

  wire IR1, IR2, IR3, MemW, RegW;
  wire [31:0] EX_PC, ID_PC, IF_PC, IR, LED, MDin, MDinr, MEM_PC, PC, RDin, RDinr, WB_PC;

  \单周期RISC_V  \u_单周期risc_v_1  (
    .IR1(IR1), .IR2(IR2), .IR3(IR3), .RegWrite(RegW), .MemWrite(MemW), .PC(PC), .IR(IR), .RDin(RDin),
    .MDin(MDin), .LedData(LED));
  \气泡流水线  \u_气泡流水线_1  (
    .RegWrite(RegW), .MemWrite(MemW), .IF_PC(IF_PC), .ID_PC(ID_PC), .EX_PC(EX_PC), .M_PC(MEM_PC),
    .WB_PC(WB_PC), .RDin(RDinr), .MDin(MDinr), .LedData(LED));
  \单周期_单级中断  \u_单周期_单级中断_1  (
    .IR1(IR1), .IR2(IR2), .IR3(IR3), .RegWrite(RegW), .MemWrite(MemW), .PC(PC), .IR(IR), .RDin(RDin),
    .MDin(MDin), .LedData(LED));
  \理想流水线  \u_理想流水线_1  (
    .RegWrite(RegW), .MemWrite(MemW), .IF_PC(IF_PC), .ID_PC(ID_PC), .EX_PC(EX_PC), .M_PC(MEM_PC),
    .WB_PC(WB_PC), .RDin(RDinr), .MDin(MDinr), .LedData(LED));
  \重定向流水线  \u_重定向流水线_1  (
    .RegWrite(RegW), .MemWrite(MemW), .IF_PC(IF_PC), .ID_PC(ID_PC), .EX_PC(EX_PC), .M_PC(MEM_PC),
    .WB_PC(WB_PC), .RDin(RDinr), .MDin(MDinr), .LedData(LED));
  \单周期_多级中断  \u_单周期_多级中断_1  (
    .IR1(IR1), .IR2(IR2), .IR3(IR3), .RegWrite(RegW), .MemWrite(MemW), .PC(PC), .IR(IR), .RDin(RDin),
    .MDin(MDin), .LedData(LED));

  // Notes on the sheet:
  //   单周期封装测试
  //   气泡流水封装测试
  //   单周期+单级中断封装测试
  //   请检查上面封装有无位宽不匹配，引脚标签是否和连接的标签相对应，否则无法在educoder平台上正确测试
  //   理想流水封装测试
  //   重定向流水封装测试
  //   单周期+多级中断封装测试
endmodule

module \动态分支预测  (
  output RegWrite,
  output MemWrite,
  output [31:0] IF_PC,
  output [31:0] ID_PC,
  output [31:0] EX_PC,
  output [31:0] M_PC,
  output [31:0] WB_PC,
  output [31:0] RDin,
  output [31:0] MDin,
  output [31:0] LedData
);

  wire alu_1_equal, alu_1_out_4, and_1_out, and_2_out, and_3_out, and_5_out, and_6_out, and_7_out, and_8_out,
       branch, branchtaken, CLK, clock_1_out, clock_2_out, comparator_1_eq, comparator_2_eq, comparator_2_lt,
       d_ff_1_q, ecall, ex_b, ex_branched, ex_i, ex_j, EX_MEM_out_17, EX_MEM_out_19, EX_MEM_out_20,
       EX_MEM_out_21, EX_MEM_out_22, EX_MEM_out_23, fail, Go, halt, ID_EX_out_30, ID_EX_out_31, ID_EX_out_32,
       ID_EX_out_33, ID_EX_out_34, ID_EX_out_36, ID_EX_out_37, ID_EX_out_38, ID_EX_out_39, IF_ID_out_11, IR1,
       IR2, IR3, jal, jalr, MEM_WB_out_15, MEM_WB_out_17, MEM_WB_out_18, MEM_WB_out_19, nand_1_out,
       not_1_out, not_2_out, not_3_out, not_4_out, not_5_out, not_6_out, or_3_out, or_7_out, pred_jump_ex,
       predict_jump, redirectcontrol_1_stall, register_1_q, RST, run, W1, W2, W3, xor_1_out,
       \单周期硬布线控制器_1_alu_src , \单周期硬布线控制器_1_beq , \单周期硬布线控制器_1_bgeu , \单周期硬布线控制器_1_bne , \单周期硬布线控制器_1_ecall ,
       \单周期硬布线控制器_1_lui , \单周期硬布线控制器_1_memtoreg , \单周期硬布线控制器_1_memwrite , \单周期硬布线控制器_1_regwrite ,
       \单周期硬布线控制器_1_s_type , \单周期硬布线控制器_1_sb ;
  wire [0:0] adder_2_out;
  wire [1:0] \byte , ID_EX_out_43, ID_EX_out_45, priority_encoder_1_out, priority_encoder_2_out,
       redirectcontrol_1_r1_src, redirectcontrol_1_r2_src;
  wire [3:0] decoder_1_out0, ID_EX_out_35, multiplexer_13_out, \单周期硬布线控制器_1_alu_op ;
  wire [4:0] EX_MEM_out_26, ID_EX_writereg_2, multiplexer_5_out, multiplexer_6_out, W_num;
  wire [11:0] multiplexer_7_out;
  wire [12:0] CNT_num;
  wire [15:0] \LoadUse次数 , \总周期数 , \插入气泡数 , \无条件分支数 , \条件分支成功数 ;
  wire [31:0] adder_6_out, alu_1_result, B_dest, bit_extender_1_out, bit_extender_2_out, bit_extender_3_out,
       bit_extender_4_out, bit_extender_5_out, ex_BranchAddr, EX_IR, EX_MEM_out_25, ex_pc_4, ID_EX_eb_2,
       ID_EX_ei_s_2, ID_EX_ej_2, ID_EX_eu_2, ID_EX_r1_2, ID_EX_r2_2, ID_IR, IF_ID_out_10, IF_IR, J_dest,
       jump_addr, MEM_ALU, MEM_IR, MEM_U, MEM_WB_out_20, MEM_WB_out_21, MEM_WB_out_23, mips_ram_1_p6,
       multiplexer_1_out, multiplexer_3_out, multiplexer_10_out, pc_4, prediction, R1, R2, regifile_1_r1,
       regifile_1_r2, sbdata, shifter_1_out, shifter_2_out, shifter_3_out, shifter_4_out, shifter_5_out,
       shifter_6_out, WB_IR;
  wire [31:1] I_dest;
  wire [31:2] EX_MEM_out_24;

  Button \u_总复位  (.out(RST));
  Button _1 (.out(IR1));
  Button _2 (.out(IR2));
  Button _3 (.out(IR3));
  // Probe on \总周期数 
  // Probe on \总周期数 
  Button \u_继续运行  (.out(Go));
  LED #(.active("true")) led_1 (.in(W1));
  LED #(.active("true")) led_2 (.in(W2));
  LED #(.active("true")) led_3 (.in(W3));
  Multiplexer #(.select(1), .width(32), .disabled("Z"), .enable("false")) multiplexer_1 (
    .in0(ex_pc_4), .in1(ex_BranchAddr), .out(multiplexer_1_out), .sel(ex_branched));
  or or_1 (ex_branched, ex_j, ex_i, branchtaken);
  BTB btb_1 (
    .CLK(CLK), .EX_branchtaken(ex_branched), .init(2'b11), .predict_jump(predict_jump), .EX_PC(EX_PC),
    .EX_B_dest(ex_BranchAddr), .jump_addr(jump_addr), .PC(IF_PC), .EX_branch(branch));
  Register #(.width(1), .trigger("rising"), .Select("low")) register_1 (
    .D(and_3_out), .en(run), .Q(register_1_q), .clk(CLK));  // open: clr
  Hex_Digit_Display hex_digit_display_1 (.value(LedData[31:28]));  // open: dp
  // Probe on IF_PC[19:0]
  // RiscV_Probe riscv_probe_1: pin names not known; wires that end beside it: IF_IR
  not not_1 (not_1_out, redirectcontrol_1_stall);
  Priority_Encoder #(.select(2), .disabled("Z")) priority_encoder_1 (
    .in0(ex_j), .in1(ex_i), .in2(ex_b), .out(priority_encoder_1_out));  // open: in3, gs, en_out, en_in
  Multiplexer #(.select(2), .width(32), .disabled("Z"), .enable("false")) multiplexer_2 (
    .in0(J_dest), .in1({I_dest, 1'b0}), .in2(B_dest), .out(ex_BranchAddr), .sel(priority_encoder_1_out));  // open: in3
  Comparator #(.width(32), .mode("unsigned")) comparator_1 (.a(R2), .b(32'h22), .eq(comparator_1_eq));  // open: gt, lt
  not not_2 (not_2_out, comparator_1_eq);
  Register #(.width(1), .trigger("rising"), .Select("low")) register_2 (
    .D(register_1_q), .en(run), .Q(halt), .clk(CLK));  // open: clr
  Hex_Digit_Display hex_digit_display_2 (.value(LedData[27:24]));  // open: dp
  Hex_Digit_Display hex_digit_display_3 (.value(LedData[23:20]));  // open: dp
  // Probe on ID_PC[19:0]
  // RiscV_Probe riscv_probe_2: pin names not known; wires that end beside it: ID_IR
  Multiplexer #(.select(1), .width(32), .disabled("Z"), .enable("false")) multiplexer_3 (
    .in0(prediction), .in1(multiplexer_1_out), .out(multiplexer_3_out), .sel(fail));
  and and_1 (and_1_out, not_1_out, run);
  and and_2 (and_2_out, ecall, comparator_1_eq);
  and and_3 (and_3_out, ecall, not_2_out);
  not not_3 (not_3_out, halt);
  Hex_Digit_Display hex_digit_display_4 (.value(LedData[19:16]));  // open: dp
  Hex_Digit_Display hex_digit_display_5 (.value(LedData[15:12]));  // open: dp
  Register #(.width(32), .trigger("rising"), .Select("low")) PC (
    .D(multiplexer_3_out), .en(and_1_out), .Q(IF_PC), .clk(CLK));  // open: clr
  and and_4 (fail, branch, xor_1_out);
  xor xor_1 (xor_1_out, pred_jump_ex, ex_branched);
  Register #(.width(32), .trigger("rising"), .Select("low")) register_3 (
    .D(R1), .en(and_2_out), .Q(LedData), .clk(CLK));  // open: clr
  Counter #(.width(16), .max('hffff), .ongoal("wrap"), .trigger("rising"), .behavior("new")) counter_1 (
    .count(not_3_out), .Q(\总周期数 ), .clk(CLK));  // open: load, D, carry, clr, preset, down
  Hex_Digit_Display hex_digit_display_6 (.value(LedData[11:8]));  // open: dp
  Hex_Digit_Display hex_digit_display_7 (.value(LedData[7:4]));  // open: dp
  Clock #(.highDuration(1), .lowDuration(1)) clock_1 (.out(clock_1_out));
  // Probe on EX_PC[19:0]
  // RiscV_Probe riscv_probe_3: pin names not known; wires that end beside it: clock_1_out, EX_IR, CLK
  Multiplexer #(.select(1), .width(32), .disabled("Z"), .enable("false")) multiplexer_4 (
    .in0(pc_4), .in1(jump_addr), .out(prediction), .sel(predict_jump));
  or or_2 (run, Go, not_4_out);
  not not_4 (not_4_out, halt);
  Hex_Digit_Display hex_digit_display_8 (.value(LedData[3:0]));  // open: dp
  not not_5 (not_5_out, fail);
  and and_5 (and_5_out, not_5_out, redirectcontrol_1_stall);
  ROM #(.addrWidth(10), .dataWidth(32), .Select("high")) rom_1 (.addr(IF_PC[11:2]), .data(IF_IR));
  Adder #(.width(32)) adder_1 (.a(IF_PC), .b(32'h4), .out(pc_4));  // open: cin, cout
  // Probe on \总周期数 
  // Probe on M_PC[19:0]
  // RiscV_Probe riscv_probe_4: pin names not known; wires that end beside it: MEM_IR
  IF_ID IF_ID (
    .in_5(IF_IR), .out_10(IF_ID_out_10), .CLK(CLK), .in_4(IF_PC), .out_9(ID_PC), .in_7(IF_IR),
    .out_12(ID_IR), .run(run), .in_1(fail), .stall(and_5_out), .in_6(predict_jump), .out_11(IF_ID_out_11));
  // Probe on \总周期数 
  // Probe on \无条件分支数 
  // Probe on \条件分支成功数 
  // Probe on \插入气泡数 
  // Probe on \LoadUse次数 
  // Probe on IF_PC[11:0]
  // Probe on WB_PC[19:0]
  // RiscV_Probe riscv_probe_5: pin names not known; wires that end beside it: WB_IR
  \单周期硬布线控制器  \u_单周期硬布线控制器_1  (
    .Funct({IF_ID_out_10[30], IF_ID_out_10[25], IF_ID_out_10[14:12]}), .OP(IF_ID_out_10[6:2]),
    .ALU_OP(\单周期硬布线控制器_1_alu_op ), .MemToReg(\单周期硬布线控制器_1_memtoreg ), .MemWrite(\单周期硬布线控制器_1_memwrite ),
    .ALU_SRC(\单周期硬布线控制器_1_alu_src ), .RegWrite(\单周期硬布线控制器_1_regwrite ), .ecall(\单周期硬布线控制器_1_ecall ),
    .S_type(\单周期硬布线控制器_1_s_type ), .Beq(\单周期硬布线控制器_1_beq ), .JAL(jal), .Bne(\单周期硬布线控制器_1_bne ),
    .in_3(IF_ID_out_10[21]), .Jalr(jalr), .LUI(\单周期硬布线控制器_1_lui ), .SB(\单周期硬布线控制器_1_sb ),
    .BGEU(\单周期硬布线控制器_1_bgeu ));  // open: uret, CSRRSI, CSRRCI
  Multiplexer #(.select(1), .width(5), .disabled("Z"), .enable("false")) multiplexer_5 (
    .in0(IF_ID_out_10[19:15]), .in1(5'b01010), .out(multiplexer_5_out), .sel(\单周期硬布线控制器_1_ecall ));
  Multiplexer #(.select(1), .width(5), .disabled("Z"), .enable("false")) multiplexer_6 (
    .in0(IF_ID_out_10[24:20]), .in1(5'b10001), .out(multiplexer_6_out), .sel(\单周期硬布线控制器_1_ecall ));
  // Probe on EX_PC[11:0]
  // Probe on ID_PC[11:0]
  Multiplexer #(.select(1), .width(12), .disabled("Z"), .enable("false")) multiplexer_7 (
    .in0(IF_ID_out_10[31:20]), .in1({IF_ID_out_10[31:25], IF_ID_out_10[11:7]}), .out(multiplexer_7_out),
    .sel(\单周期硬布线控制器_1_s_type ));
  assign bit_extender_1_out = {{20{IF_ID_out_10[31]}}, {IF_ID_out_10[31], IF_ID_out_10[7], IF_ID_out_10[30:25], IF_ID_out_10[11:8]}};  // Bit_Extender bit_extender_1
  assign bit_extender_2_out = {{12{IF_ID_out_10[31]}}, {IF_ID_out_10[31], IF_ID_out_10[19:12], IF_ID_out_10[20], IF_ID_out_10[30:21]}};  // Bit_Extender bit_extender_2
  assign bit_extender_3_out = {{12{IF_ID_out_10[31]}}, IF_ID_out_10[31:12]};  // Bit_Extender bit_extender_3
  // Probe on M_PC[11:0]
  D_Flip_Flop #(.trigger("high"), .Pre_Clr_Positions("LEGACY"), .NegatePresetClear("false"), .enable("true"), .NewFFLayout("false")) d_ff_1 (.Q(d_ff_1_q));  // open: clk, D, Qn, preset, en, reset
  // Probe on 13'h50
  or or_3 (or_3_out, fail, redirectcontrol_1_stall);
  Regifile regifile_1 (
    .Din(RDin), .Clk(CLK), .R1(regifile_1_r1), .R2(regifile_1_r2), .WE(RegWrite), .W_num(W_num),
    .R1_num(multiplexer_5_out), .R2_num(multiplexer_6_out));
  assign bit_extender_4_out = {{20{multiplexer_7_out[11]}}, multiplexer_7_out};  // Bit_Extender bit_extender_4
  // Probe on WB_PC[11:0]
  Comparator #(.width(13), .mode("twosComplement")) comparator_2 (
    .a(CNT_num), .b(13'h50), .eq(comparator_2_eq), .lt(comparator_2_lt));  // open: gt
  Clock #(.highDuration(1), .lowDuration(1)) clock_2 (.out(clock_2_out));
  ReDirectControl redirectcontrol_1 (
    .halt(halt), .clk(CLK), .stall(redirectcontrol_1_stall), .instr(IF_ID_out_10),
    .ecall(\单周期硬布线控制器_1_ecall ), .alusrc(\单周期硬布线控制器_1_alu_src ), .ex_W_num(ID_EX_writereg_2), .jal(ex_j),
    .jalr(ex_i), .ex_regwrite(ID_EX_out_37), .branch(branchtaken), .mem_W_num(EX_MEM_out_26),
    .mem_regwrite(EX_MEM_out_19), .\无条件 (\无条件分支数 ), .\条件 (\条件分支成功数 ), .\气泡 (\插入气泡数 ),
    .r1_src(redirectcontrol_1_r1_src), .r2_src(redirectcontrol_1_r2_src), .ex_toreg(ID_EX_out_33),
    .loaduse(\LoadUse次数 ), .stype(\单周期硬布线控制器_1_s_type ));  // open: jal_2, jalr_2, branchtaken, flush2
  ID_EX ID_EX (
    .Beq(\单周期硬布线控制器_1_beq ), .Bne(\单周期硬布线控制器_1_bne ), .Bgeu(\单周期硬布线控制器_1_bgeu ),
    .MemToReg(\单周期硬布线控制器_1_memtoreg ), .MemWrite(\单周期硬布线控制器_1_memwrite ), .AluOP(\单周期硬布线控制器_1_alu_op ),
    .AluSrcB(\单周期硬布线控制器_1_alu_src ), .RegWrite(\单周期硬布线控制器_1_regwrite ), .LUI(\单周期硬布线控制器_1_lui ),
    .Sb(\单周期硬布线控制器_1_sb ), .CLK(CLK), .R1(regifile_1_r1), .R2(regifile_1_r2), .WriteReg(IF_ID_out_10[11:7]),
    .R1_2(ID_EX_r1_2), .R2_2(ID_EX_r2_2), .WriteReg_2(ID_EX_writereg_2), .out_30(ID_EX_out_30),
    .out_31(ID_EX_out_31), .out_32(ID_EX_out_32), .out_33(ID_EX_out_33), .out_36(ID_EX_out_36),
    .out_37(ID_EX_out_37), .out_38(ID_EX_out_38), .out_39(ID_EX_out_39), .out_34(ID_EX_out_34),
    .out_35(ID_EX_out_35), .pc(ID_PC), .pc_2(EX_PC), .EB(bit_extender_1_out), .EJ(bit_extender_2_out),
    .EU(bit_extender_3_out), .EB_2(ID_EX_eb_2), .EJ_2(ID_EX_ej_2), .EU_2(ID_EX_eu_2),
    .EI_S(bit_extender_4_out), .EI_S_2(ID_EX_ei_s_2), .out_40(ex_j), .jal(jal), .ir(ID_IR), .ir_2(EX_IR),
    .ecall(\单周期硬布线控制器_1_ecall ), .out_42(ecall), .run(run), .in_1(or_3_out), .jalr(jalr), .out_41(ex_i),
    .out_43(ID_EX_out_43), .r1src(redirectcontrol_1_r1_src), .out_45(ID_EX_out_45),
    .r2src(redirectcontrol_1_r2_src), .pred(IF_ID_out_11), .pred_2(pred_jump_ex));  // open: uret, uret_2
  nand nand_1 (nand_1_out, d_ff_1_q, comparator_2_eq);
  Counter #(.width(13), .max('h1fff), .ongoal("stay"), .trigger("rising"), .behavior("old")) counter_2 (
    .count(comparator_2_lt), .Q(CNT_num), .clk(clock_2_out));  // open: load, D, carry, clr, preset
  Shifter #(.width(32), .shift("ll")) shifter_1 (.in(ID_EX_eb_2), .\dist (5'b00001), .out(shifter_1_out));
  Shifter #(.width(32), .shift("ll")) shifter_2 (.in(ID_EX_ej_2), .\dist (5'b00001), .out(shifter_2_out));
  Shifter #(.width(32), .shift("ll")) shifter_3 (.in(ID_EX_eu_2), .\dist (5'b01100), .out(shifter_3_out));
  assign CLK = nand_1_out ? clock_2_out : 1'bz;  // Controlled_Buffer controlled_buffer_1
  or or_4 (ex_b, ID_EX_out_30, ID_EX_out_31, ID_EX_out_32);
  Multiplexer #(.select(2), .width(32), .disabled("Z"), .enable("false")) multiplexer_8 (
    .in0(ID_EX_r1_2), .in1(RDin), .in2(MEM_ALU), .out(R1), .sel(ID_EX_out_43));  // open: in3
  Multiplexer #(.select(2), .width(32), .disabled("Z"), .enable("false")) multiplexer_9 (
    .in0(ID_EX_r2_2), .in1(RDin), .in2(MEM_ALU), .out(R2), .sel(ID_EX_out_45));  // open: in3
  Adder #(.width(32)) adder_2 (.a(ID_EX_ei_s_2), .b(R1), .out({I_dest, adder_2_out[0]}));  // open: cin, cout
  Adder #(.width(32)) adder_3 (.a(EX_PC), .b(32'h4), .out(ex_pc_4));  // open: cin, cout
  Pull_Resistor #(.pull(1)) pull_resistor_1 (.node(CLK));
  or or_5 (branch, ID_EX_out_30, ID_EX_out_31, ID_EX_out_32, ex_j, ex_i);
  Multiplexer #(.select(1), .width(32), .disabled("Z"), .enable("false")) multiplexer_10 (
    .in0(R2), .in1(ID_EX_ei_s_2), .out(multiplexer_10_out), .sel(ID_EX_out_36));
  Adder #(.width(32)) adder_4 (.a(shifter_1_out), .b(EX_PC), .out(B_dest));  // open: cin, cout
  Adder #(.width(32)) adder_5 (.a(shifter_2_out), .b(EX_PC), .out(J_dest));  // open: cin, cout
  or or_6 (branchtaken, and_6_out, and_7_out, and_8_out);
  and and_6 (and_6_out, ID_EX_out_30, alu_1_equal);
  and and_7 (and_7_out, ID_EX_out_31, not_6_out);
  not not_6 (not_6_out, alu_1_equal);
  and and_8 (and_8_out, ID_EX_out_32, alu_1_out_4);
  ALU alu_1 (
    .X(R1), .Y(multiplexer_10_out), .AluOP(ID_EX_out_35), .Equal(alu_1_equal), .Result(alu_1_result),
    .out_4(alu_1_out_4));  // open: Result_2, out_6
  EX_MEM EX_MEM (
    .MemToReg(ID_EX_out_33), .MemWrite(ID_EX_out_34), .out_17(EX_MEM_out_17), .out_18(MemWrite),
    .RegWrite(ID_EX_out_37), .out_19(EX_MEM_out_19), .LUI(ID_EX_out_38), .out_20(EX_MEM_out_20),
    .Sb(ID_EX_out_39), .out_21(EX_MEM_out_21), .Alu(alu_1_result), .out_24({EX_MEM_out_24, \byte }), .R2(R2),
    .out_25(EX_MEM_out_25), .udata(shifter_3_out), .out_27(MEM_U), .pc(EX_PC), .out_28(M_PC), .ir(EX_IR),
    .out_29(MEM_IR), .CLK(CLK), .in_11(ID_EX_writereg_2), .out_26(EX_MEM_out_26), .run(run), .in_1(1'b0),
    .jal(ex_j), .out_22(EX_MEM_out_22), .jalr(ex_i), .out_23(EX_MEM_out_23));
  Multiplexer #(.select(1), .width(32), .disabled("Z"), .enable("false")) multiplexer_11 (
    .in0({EX_MEM_out_24, \byte }), .in1(MEM_U), .out(MEM_ALU), .sel(EX_MEM_out_20));
  Multiplexer #(.select(1), .width(32), .disabled("Z"), .enable("false")) multiplexer_12 (
    .in0(EX_MEM_out_25), .in1(sbdata), .out(MDin), .sel(EX_MEM_out_21));
  Decoder #(.select(2), .tristate("false"), .disabled("Z"), .enable("false")) decoder_1 (
    .out0(decoder_1_out0[0]), .out1(decoder_1_out0[1]), .out2(decoder_1_out0[2]), .out3(decoder_1_out0[3]),
    .sel(\byte ));
  assign bit_extender_5_out = {{24{1'b0}}, EX_MEM_out_25[7:0]};  // Bit_Extender bit_extender_5
  Multiplexer #(.select(1), .width(4), .disabled("Z"), .enable("false")) multiplexer_13 (
    .in0(4'b1111), .in1(decoder_1_out0), .out(multiplexer_13_out), .sel(EX_MEM_out_21));
  Shifter #(.width(32), .shift("ll")) shifter_4 (.in(bit_extender_5_out), .\dist (5'b01000), .out(shifter_4_out));
  Shifter #(.width(32), .shift("ll")) shifter_5 (.in(bit_extender_5_out), .\dist (5'b10000), .out(shifter_5_out));
  Shifter #(.width(32), .shift("ll")) shifter_6 (.in(bit_extender_5_out), .\dist (5'b11000), .out(shifter_6_out));
  Multiplexer #(.select(2), .width(32), .disabled("Z"), .enable("false")) multiplexer_14 (
    .in0(bit_extender_5_out), .in1(shifter_4_out), .in2(shifter_5_out), .in3(shifter_6_out), .out(sbdata),
    .sel(\byte ));
  // MIPS_RAM mips_ram_1: pin names not known; wires that end beside it: EX_MEM_out_24[11:2], MDin, MemWrite, multiplexer_13_out, CLK, mips_ram_1_p6
  MEM_WB MEM_WB (
    .in_2(EX_MEM_out_17), .out_15(MEM_WB_out_15), .in_3(EX_MEM_out_19), .out_16(RegWrite),
    .in_4(EX_MEM_out_20), .out_17(MEM_WB_out_17), .in_7({EX_MEM_out_24, \byte }), .out_20(MEM_WB_out_20),
    .in_8(mips_ram_1_p6), .out_21(MEM_WB_out_21), .in_10(MEM_U), .out_23(MEM_WB_out_23),
    .in_9(EX_MEM_out_26), .out_22(W_num), .in_11(M_PC), .out_24(WB_PC), .in_12(MEM_IR), .out_25(WB_IR),
    .CLK(CLK), .run(run), .in_1(1'b0), .in_5(EX_MEM_out_22), .out_18(MEM_WB_out_18), .in_6(EX_MEM_out_23),
    .out_19(MEM_WB_out_19));
  or or_7 (or_7_out, MEM_WB_out_18, MEM_WB_out_19);
  Adder #(.width(32)) adder_6 (.a(WB_PC), .b(32'h4), .out(adder_6_out));  // open: cin, cout
  Priority_Encoder #(.select(2), .disabled("Z")) priority_encoder_2 (
    .in0(1'b1), .in1(MEM_WB_out_15), .in2(or_7_out), .in3(MEM_WB_out_17), .out(priority_encoder_2_out));  // open: gs, en_out, en_in
  Multiplexer #(.select(2), .width(32), .disabled("Z"), .enable("false")) multiplexer_15 (
    .in0(MEM_WB_out_20), .in1(MEM_WB_out_21), .in2(adder_6_out), .in3(MEM_WB_out_23), .out(RDin),
    .sel(priority_encoder_2_out));

  // Other names for the same wires on the sheet: MEM_PC[31:0] = M_PC

  // Notes on the sheet:
  //   中断源
  //   时空图监测，可删除
  //   中断等待指示
  //   数码管输出
  //   contents of rom_1 (hex, n*v repeats v):
  //   100493 100006f 100493 200913 300993 100006f 100493 200913 300993 100006f 100493 200913 300993
  //   100006f 100493 200913 300993 29c000ef 100413 100493 1f49493 900533 2200893 73 24d493 48463 fedff06f
  //   900533 2200893 73 100493 249493 900533 2200893 73 48463 fedff06f 100493 1f49493 900533 2200893 73
  //   4034d493 900533 2200893 73 4044d493 900533 2200893 73 4044d493 900533 2200893 73 4044d493 900533
  //   2200893 73 4044d493 900533 2200893 73 4044d493 900533 2200893 73 4044d493 900533 2200893 73 4044d493
  //   900533 2200893 73 100413 1f41993 41f9d993 433 c00913 300b13 140413 f47413 800293 100313 499993
  //   89e9b3 1300533 2200893 73 406282b3 fe0294e3 140413 f00f93 1f47433 1c41413 800293 100313 49d993
  //   89e9b3 1300533 2200893 73 406282b3 fe0294e3 1c45413 406b0b33 b0463 f95ff06f 2b3 fff2c293 829293
  //   ff2e293 500533 2200893 73 fff00413 493 84a023 140413 448493 84a023 140413 448493 84a023 140413
  //   448493 84a023 140413 448493 84a023 140413 448493 84a023 140413 448493 84a023 140413 448493 84a023
  //   140413 448493 84a023 140413 448493 84a023 140413 448493 84a023 140413 448493 84a023 140413 448493
  //   84a023 140413 448493 84a023 140413 448493 84a023 140413 448493 84a023 140413 448493 140413 433
  //   3c00493 42983 4aa03 149a2b3 28663 134a023 1442023 ffc48493 fe9412e3 800533 2200893 73 440413 3c00493
  //   fc9416e3 a00893 73 413 140413 800533 2200893 73 240413 800533 2200893 73 340413 800533 2200893 73
  //   440413 800533 2200893 73 540413 800533 2200893 73 640413 800533 2200893 73 740413 800533 2200893 73
  //   840413 800533 2200893 2200893 73 8067
  //   I
  //   S
  //   Beq
  //   Bne
  //   Bgeu
  //   MemToReg
  //   MemWrite
  //   AluOP
  //   AluSrcB
  //   Regwrite
  //   Lui
  //   Sb
  //   Ecall
  //   B
  //   J
  //   控制位
  //   流水调试日志用
  //   暂停节拍，不能为0
  //   戳工具置1进入计数暂停模式，ctrl+k时钟自动运行到对应节拍暂停
  //   ctrl+k关闭时钟连续运行，将控制位置零，进入单步调试模式调试
  //   可计数暂停的时钟源
  //   为方便自动评测，需要输出流水线各段保存的PC值，注意是PC不是PC+4，另外ID段寄存器写入信息，Mem段内存写入信息也要输出
endmodule

module IF_ID (
  input  in_1,
  input  stall,
  input  run,
  input  [31:0] in_4,
  input  [31:0] in_5,
  input  in_6,
  input  [31:0] in_7,
  input  CLK,
  output [31:0] out_9,
  output [31:0] out_10,
  output out_11,
  output [31:0] out_12
);

  wire and_1_out, multiplexer_3_out, not_1_out, or_1_out;
  wire [31:0] multiplexer_1_out, multiplexer_2_out, multiplexer_4_out;

  Multiplexer #(.select(1), .width(32), .disabled("Z"), .enable("false")) multiplexer_1 (
    .in0(in_4), .in1({32{1'b0}}), .out(multiplexer_1_out), .sel(in_1));
  Multiplexer #(.select(1), .width(32), .disabled("Z"), .enable("false")) multiplexer_2 (
    .in0(in_5), .in1({32{1'b0}}), .out(multiplexer_2_out), .sel(in_1));
  Multiplexer #(.select(1), .width(1), .disabled("Z"), .enable("false")) multiplexer_3 (
    .in0(in_6), .in1(1'b0), .out(multiplexer_3_out), .sel(in_1));
  Multiplexer #(.select(1), .width(32), .disabled("Z"), .enable("false")) multiplexer_4 (
    .in0(in_7), .in1({32{1'b0}}), .out(multiplexer_4_out), .sel(in_1));
  not not_1 (not_1_out, stall);
  and and_1 (and_1_out, not_1_out, run);
  or or_1 (or_1_out, in_1, and_1_out);
  Register #(.width(32), .trigger("rising"), .Select("low")) register_1 (
    .D(multiplexer_1_out), .en(or_1_out), .Q(out_9), .clk(CLK));  // open: clr
  Register #(.width(32), .trigger("rising"), .Select("low")) register_2 (
    .D(multiplexer_2_out), .en(or_1_out), .Q(out_10), .clk(CLK));  // open: clr
  Register #(.width(1), .trigger("rising"), .Select("low")) register_3 (
    .D(multiplexer_3_out), .en(or_1_out), .Q(out_11), .clk(CLK));  // open: clr
  Register #(.width(32), .trigger("rising"), .Select("low")) register_4 (
    .D(multiplexer_4_out), .en(or_1_out), .Q(out_12), .clk(CLK));  // open: clr
endmodule
module ID_EX (
  input  in_1,
  input  Beq,
  input  Bne,
  input  Bgeu,
  input  MemToReg,
  input  MemWrite,
  input  [3:0] AluOP,
  input  AluSrcB,
  input  RegWrite,
  input  LUI,
  input  Sb,
  input  jal,
  input  jalr,
  input  ecall,
  input  [1:0] r1src,
  input  [31:0] R1,
  input  [1:0] r2src,
  input  [31:0] R2,
  input  [4:0] WriteReg,
  input  [31:0] EI_S,
  input  [31:0] EB,
  input  [31:0] EJ,
  input  [31:0] EU,
  input  uret,
  input  pred,
  input  [31:0] pc,
  input  [31:0] ir,
  input  run,
  input  CLK,
  output out_30,
  output out_31,
  output out_32,
  output out_33,
  output out_34,
  output [3:0] out_35,
  output out_36,
  output out_37,
  output out_38,
  output out_39,
  output out_40,
  output out_41,
  output out_42,
  output [1:0] out_43,
  output [31:0] R1_2,
  output [1:0] out_45,
  output [31:0] R2_2,
  output [4:0] WriteReg_2,
  output [31:0] EI_S_2,
  output [31:0] EB_2,
  output [31:0] EJ_2,
  output [31:0] EU_2,
  output uret_2,
  output pred_2,
  output [31:0] pc_2,
  output [31:0] ir_2
);

  wire multiplexer_1_out, multiplexer_2_out, multiplexer_3_out, multiplexer_4_out, multiplexer_5_out,
       multiplexer_7_out, multiplexer_8_out, multiplexer_9_out, multiplexer_10_out, multiplexer_11_out,
       multiplexer_12_out, multiplexer_13_out, multiplexer_23_out, multiplexer_24_out;
  wire [1:0] multiplexer_14_out, multiplexer_16_out;
  wire [3:0] multiplexer_6_out;
  wire [4:0] multiplexer_18_out;
  wire [31:0] multiplexer_15_out, multiplexer_17_out, multiplexer_19_out, multiplexer_20_out,
       multiplexer_21_out, multiplexer_22_out, multiplexer_25_out, multiplexer_26_out;

  Multiplexer #(.select(1), .width(1), .disabled("Z"), .enable("false")) multiplexer_1 (
    .in0(Beq), .in1(1'b0), .out(multiplexer_1_out), .sel(in_1));
  Multiplexer #(.select(1), .width(1), .disabled("Z"), .enable("false")) multiplexer_2 (
    .in0(Bne), .in1(1'b0), .out(multiplexer_2_out), .sel(in_1));
  Multiplexer #(.select(1), .width(1), .disabled("Z"), .enable("false")) multiplexer_3 (
    .in0(Bgeu), .in1(1'b0), .out(multiplexer_3_out), .sel(in_1));
  Multiplexer #(.select(1), .width(1), .disabled("Z"), .enable("false")) multiplexer_4 (
    .in0(MemToReg), .in1(1'b0), .out(multiplexer_4_out), .sel(in_1));
  Multiplexer #(.select(1), .width(1), .disabled("Z"), .enable("false")) multiplexer_5 (
    .in0(MemWrite), .in1(1'b0), .out(multiplexer_5_out), .sel(in_1));
  Multiplexer #(.select(1), .width(4), .disabled("Z"), .enable("false")) multiplexer_6 (
    .in0(AluOP), .in1(4'b0000), .out(multiplexer_6_out), .sel(in_1));
  Multiplexer #(.select(1), .width(1), .disabled("Z"), .enable("false")) multiplexer_7 (
    .in0(AluSrcB), .in1(1'b0), .out(multiplexer_7_out), .sel(in_1));
  Multiplexer #(.select(1), .width(1), .disabled("Z"), .enable("false")) multiplexer_8 (
    .in0(RegWrite), .in1(1'b0), .out(multiplexer_8_out), .sel(in_1));
  Multiplexer #(.select(1), .width(1), .disabled("Z"), .enable("false")) multiplexer_9 (
    .in0(LUI), .in1(1'b0), .out(multiplexer_9_out), .sel(in_1));
  Multiplexer #(.select(1), .width(1), .disabled("Z"), .enable("false")) multiplexer_10 (
    .in0(Sb), .in1(1'b0), .out(multiplexer_10_out), .sel(in_1));
  Multiplexer #(.select(1), .width(1), .disabled("Z"), .enable("false")) multiplexer_11 (
    .in0(jal), .in1(1'b0), .out(multiplexer_11_out), .sel(in_1));
  Multiplexer #(.select(1), .width(1), .disabled("Z"), .enable("false")) multiplexer_12 (
    .in0(jalr), .in1(1'b0), .out(multiplexer_12_out), .sel(in_1));
  Multiplexer #(.select(1), .width(1), .disabled("Z"), .enable("false")) multiplexer_13 (
    .in0(ecall), .in1(1'b0), .out(multiplexer_13_out), .sel(in_1));
  Multiplexer #(.select(1), .width(2), .disabled("Z"), .enable("false")) multiplexer_14 (
    .in0(r1src), .in1(2'b00), .out(multiplexer_14_out), .sel(in_1));
  Multiplexer #(.select(1), .width(32), .disabled("Z"), .enable("false")) multiplexer_15 (
    .in0(R1), .in1({32{1'b0}}), .out(multiplexer_15_out), .sel(in_1));
  Multiplexer #(.select(1), .width(2), .disabled("Z"), .enable("false")) multiplexer_16 (
    .in0(r2src), .in1(2'b00), .out(multiplexer_16_out), .sel(in_1));
  Multiplexer #(.select(1), .width(32), .disabled("Z"), .enable("false")) multiplexer_17 (
    .in0(R2), .in1({32{1'b0}}), .out(multiplexer_17_out), .sel(in_1));
  Multiplexer #(.select(1), .width(5), .disabled("Z"), .enable("false")) multiplexer_18 (
    .in0(WriteReg), .in1({5{1'b0}}), .out(multiplexer_18_out), .sel(in_1));
  Multiplexer #(.select(1), .width(32), .disabled("Z"), .enable("false")) multiplexer_19 (
    .in0(EI_S), .in1({32{1'b0}}), .out(multiplexer_19_out), .sel(in_1));
  Multiplexer #(.select(1), .width(32), .disabled("Z"), .enable("false")) multiplexer_20 (
    .in0(EB), .in1({32{1'b0}}), .out(multiplexer_20_out), .sel(in_1));
  Multiplexer #(.select(1), .width(32), .disabled("Z"), .enable("false")) multiplexer_21 (
    .in0(EJ), .in1({32{1'b0}}), .out(multiplexer_21_out), .sel(in_1));
  Multiplexer #(.select(1), .width(32), .disabled("Z"), .enable("false")) multiplexer_22 (
    .in0(EU), .in1({32{1'b0}}), .out(multiplexer_22_out), .sel(in_1));
  Multiplexer #(.select(1), .width(1), .disabled("Z"), .enable("false")) multiplexer_23 (
    .in0(uret), .in1(1'b0), .out(multiplexer_23_out), .sel(in_1));
  Multiplexer #(.select(1), .width(1), .disabled("Z"), .enable("false")) multiplexer_24 (
    .in0(pred), .in1(1'b0), .out(multiplexer_24_out), .sel(in_1));
  Multiplexer #(.select(1), .width(32), .disabled("Z"), .enable("false")) multiplexer_25 (
    .in0(pc), .in1({32{1'b0}}), .out(multiplexer_25_out), .sel(in_1));
  Multiplexer #(.select(1), .width(32), .disabled("Z"), .enable("false")) multiplexer_26 (
    .in0(ir), .in1({32{1'b0}}), .out(multiplexer_26_out), .sel(in_1));
  Register #(.width(1), .trigger("rising"), .Select("low")) register_1 (
    .D(multiplexer_1_out), .en(run), .Q(out_30), .clk(CLK));  // open: clr
  Register #(.width(1), .trigger("rising"), .Select("low")) register_2 (
    .D(multiplexer_2_out), .en(run), .Q(out_31), .clk(CLK));  // open: clr
  Register #(.width(1), .trigger("rising"), .Select("low")) register_3 (
    .D(multiplexer_3_out), .en(run), .Q(out_32), .clk(CLK));  // open: clr
  Register #(.width(1), .trigger("rising"), .Select("low")) register_4 (
    .D(multiplexer_4_out), .en(run), .Q(out_33), .clk(CLK));  // open: clr
  Register #(.width(1), .trigger("rising"), .Select("low")) register_5 (
    .D(multiplexer_5_out), .en(run), .Q(out_34), .clk(CLK));  // open: clr
  Register #(.width(4), .trigger("rising"), .Select("low")) register_6 (
    .D(multiplexer_6_out), .en(run), .Q(out_35), .clk(CLK));  // open: clr
  Register #(.width(1), .trigger("rising"), .Select("low")) register_7 (
    .D(multiplexer_7_out), .en(run), .Q(out_36), .clk(CLK));  // open: clr
  Register #(.width(1), .trigger("rising"), .Select("low")) register_8 (
    .D(multiplexer_8_out), .en(run), .Q(out_37), .clk(CLK));  // open: clr
  Register #(.width(1), .trigger("rising"), .Select("low")) register_9 (
    .D(multiplexer_9_out), .en(run), .Q(out_38), .clk(CLK));  // open: clr
  Register #(.width(1), .trigger("rising"), .Select("low")) register_10 (
    .D(multiplexer_10_out), .en(run), .Q(out_39), .clk(CLK));  // open: clr
  Register #(.width(1), .trigger("rising"), .Select("low")) register_11 (
    .D(multiplexer_11_out), .en(run), .Q(out_40), .clk(CLK));  // open: clr
  Register #(.width(1), .trigger("rising"), .Select("low")) register_12 (
    .D(multiplexer_12_out), .en(run), .Q(out_41), .clk(CLK));  // open: clr
  Register #(.width(1), .trigger("rising"), .Select("low")) register_13 (
    .D(multiplexer_13_out), .en(run), .Q(out_42), .clk(CLK));  // open: clr
  Register #(.width(2), .trigger("rising"), .Select("low")) register_14 (
    .D(multiplexer_14_out), .en(run), .Q(out_43), .clk(CLK));  // open: clr
  Register #(.width(32), .trigger("rising"), .Select("low")) register_15 (
    .D(multiplexer_15_out), .en(run), .Q(R1_2), .clk(CLK));  // open: clr
  Register #(.width(2), .trigger("rising"), .Select("low")) register_16 (
    .D(multiplexer_16_out), .en(run), .Q(out_45), .clk(CLK));  // open: clr
  Register #(.width(32), .trigger("rising"), .Select("low")) register_17 (
    .D(multiplexer_17_out), .en(run), .Q(R2_2), .clk(CLK));  // open: clr
  Register #(.width(5), .trigger("rising"), .Select("low")) register_18 (
    .D(multiplexer_18_out), .en(run), .Q(WriteReg_2), .clk(CLK));  // open: clr
  Register #(.width(32), .trigger("rising"), .Select("low")) register_19 (
    .D(multiplexer_19_out), .en(run), .Q(EI_S_2), .clk(CLK));  // open: clr
  Register #(.width(32), .trigger("rising"), .Select("low")) register_20 (
    .D(multiplexer_20_out), .en(run), .Q(EB_2), .clk(CLK));  // open: clr
  Register #(.width(32), .trigger("rising"), .Select("low")) register_21 (
    .D(multiplexer_21_out), .en(run), .Q(EJ_2), .clk(CLK));  // open: clr
  Register #(.width(32), .trigger("rising"), .Select("low")) register_22 (
    .D(multiplexer_22_out), .en(run), .Q(EU_2), .clk(CLK));  // open: clr
  Register #(.width(1), .trigger("rising"), .Select("low")) register_23 (
    .D(multiplexer_23_out), .en(run), .Q(uret_2), .clk(CLK));  // open: clr
  Register #(.width(1), .trigger("rising"), .Select("low")) register_24 (
    .D(multiplexer_24_out), .en(run), .Q(pred_2), .clk(CLK));  // open: clr
  Register #(.width(32), .trigger("rising"), .Select("low")) register_25 (
    .D(multiplexer_25_out), .en(run), .Q(pc_2), .clk(CLK));  // open: clr
  Register #(.width(32), .trigger("rising"), .Select("low")) register_26 (
    .D(multiplexer_26_out), .en(run), .Q(ir_2), .clk(CLK));  // open: clr
endmodule

module EX_MEM (
  input  in_1,
  input  MemToReg,
  input  MemWrite,
  input  RegWrite,
  input  LUI,
  input  Sb,
  input  jal,
  input  jalr,
  input  [31:0] Alu,
  input  [31:0] R2,
  input  [4:0] in_11,
  input  [31:0] udata,
  input  [31:0] pc,
  input  [31:0] ir,
  input  run,
  input  CLK,
  output out_17,
  output out_18,
  output out_19,
  output out_20,
  output out_21,
  output out_22,
  output out_23,
  output [31:0] out_24,
  output [31:0] out_25,
  output [4:0] out_26,
  output [31:0] out_27,
  output [31:0] out_28,
  output [31:0] out_29
);

  wire multiplexer_1_out, multiplexer_2_out, multiplexer_3_out, multiplexer_4_out, multiplexer_5_out,
       multiplexer_6_out, multiplexer_7_out;
  wire [4:0] multiplexer_10_out;
  wire [31:0] multiplexer_8_out, multiplexer_9_out, multiplexer_11_out, multiplexer_12_out,
       multiplexer_13_out;

  Multiplexer #(.select(1), .width(1), .disabled("Z"), .enable("false")) multiplexer_1 (
    .in0(MemToReg), .in1(1'b0), .out(multiplexer_1_out), .sel(in_1));
  Multiplexer #(.select(1), .width(1), .disabled("Z"), .enable("false")) multiplexer_2 (
    .in0(MemWrite), .in1(1'b0), .out(multiplexer_2_out), .sel(in_1));
  Multiplexer #(.select(1), .width(1), .disabled("Z"), .enable("false")) multiplexer_3 (
    .in0(RegWrite), .in1(1'b0), .out(multiplexer_3_out), .sel(in_1));
  Multiplexer #(.select(1), .width(1), .disabled("Z"), .enable("false")) multiplexer_4 (
    .in0(LUI), .in1(1'b0), .out(multiplexer_4_out), .sel(in_1));
  Multiplexer #(.select(1), .width(1), .disabled("Z"), .enable("false")) multiplexer_5 (
    .in0(Sb), .in1(1'b0), .out(multiplexer_5_out), .sel(in_1));
  Multiplexer #(.select(1), .width(1), .disabled("Z"), .enable("false")) multiplexer_6 (
    .in0(jal), .in1(1'b0), .out(multiplexer_6_out), .sel(in_1));
  Multiplexer #(.select(1), .width(1), .disabled("Z"), .enable("false")) multiplexer_7 (
    .in0(jalr), .in1(1'b0), .out(multiplexer_7_out), .sel(in_1));
  Multiplexer #(.select(1), .width(32), .disabled("Z"), .enable("false")) multiplexer_8 (
    .in0(Alu), .in1({32{1'b0}}), .out(multiplexer_8_out), .sel(in_1));
  Multiplexer #(.select(1), .width(32), .disabled("Z"), .enable("false")) multiplexer_9 (
    .in0(R2), .in1({32{1'b0}}), .out(multiplexer_9_out), .sel(in_1));
  Multiplexer #(.select(1), .width(5), .disabled("Z"), .enable("false")) multiplexer_10 (
    .in0(in_11), .in1({5{1'b0}}), .out(multiplexer_10_out), .sel(in_1));
  Multiplexer #(.select(1), .width(32), .disabled("Z"), .enable("false")) multiplexer_11 (
    .in0(udata), .in1({32{1'b0}}), .out(multiplexer_11_out), .sel(in_1));
  Multiplexer #(.select(1), .width(32), .disabled("Z"), .enable("false")) multiplexer_12 (
    .in0(pc), .in1({32{1'b0}}), .out(multiplexer_12_out), .sel(in_1));
  Multiplexer #(.select(1), .width(32), .disabled("Z"), .enable("false")) multiplexer_13 (
    .in0(ir), .in1({32{1'b0}}), .out(multiplexer_13_out), .sel(in_1));
  Register #(.width(1), .trigger("rising"), .Select("low")) register_1 (
    .D(multiplexer_1_out), .en(run), .Q(out_17), .clk(CLK));  // open: clr
  Register #(.width(1), .trigger("rising"), .Select("low")) register_2 (
    .D(multiplexer_2_out), .en(run), .Q(out_18), .clk(CLK));  // open: clr
  Register #(.width(1), .trigger("rising"), .Select("low")) register_3 (
    .D(multiplexer_3_out), .en(run), .Q(out_19), .clk(CLK));  // open: clr
  Register #(.width(1), .trigger("rising"), .Select("low")) register_4 (
    .D(multiplexer_4_out), .en(run), .Q(out_20), .clk(CLK));  // open: clr
  Register #(.width(1), .trigger("rising"), .Select("low")) register_5 (
    .D(multiplexer_5_out), .en(run), .Q(out_21), .clk(CLK));  // open: clr
  Register #(.width(1), .trigger("rising"), .Select("low")) register_6 (
    .D(multiplexer_6_out), .en(run), .Q(out_22), .clk(CLK));  // open: clr
  Register #(.width(1), .trigger("rising"), .Select("low")) register_7 (
    .D(multiplexer_7_out), .en(run), .Q(out_23), .clk(CLK));  // open: clr
  Register #(.width(32), .trigger("rising"), .Select("low")) register_8 (
    .D(multiplexer_8_out), .en(run), .Q(out_24), .clk(CLK));  // open: clr
  Register #(.width(32), .trigger("rising"), .Select("low")) register_9 (
    .D(multiplexer_9_out), .en(run), .Q(out_25), .clk(CLK));  // open: clr
  Register #(.width(5), .trigger("rising"), .Select("low")) register_10 (
    .D(multiplexer_10_out), .en(run), .Q(out_26), .clk(CLK));  // open: clr
  Register #(.width(32), .trigger("rising"), .Select("low")) register_11 (
    .D(multiplexer_11_out), .en(run), .Q(out_27), .clk(CLK));  // open: clr
  Register #(.width(32), .trigger("rising"), .Select("low")) register_12 (
    .D(multiplexer_12_out), .en(run), .Q(out_28), .clk(CLK));  // open: clr
  Register #(.width(32), .trigger("rising"), .Select("low")) register_13 (
    .D(multiplexer_13_out), .en(run), .Q(out_29), .clk(CLK));  // open: clr
endmodule

module MEM_WB (
  input  in_1,
  input  in_2,
  input  in_3,
  input  in_4,
  input  in_5,
  input  in_6,
  input  [31:0] in_7,
  input  [31:0] in_8,
  input  [4:0] in_9,
  input  [31:0] in_10,
  input  [31:0] in_11,
  input  [31:0] in_12,
  input  run,
  input  CLK,
  output out_15,
  output out_16,
  output out_17,
  output out_18,
  output out_19,
  output [31:0] out_20,
  output [31:0] out_21,
  output [4:0] out_22,
  output [31:0] out_23,
  output [31:0] out_24,
  output [31:0] out_25
);

  wire multiplexer_1_out, multiplexer_2_out, multiplexer_3_out, multiplexer_4_out, multiplexer_5_out;
  wire [4:0] multiplexer_8_out;
  wire [31:0] multiplexer_6_out, multiplexer_7_out, multiplexer_9_out, multiplexer_10_out, multiplexer_11_out;

  Multiplexer #(.select(1), .width(1), .disabled("Z"), .enable("false")) multiplexer_1 (
    .in0(in_2), .in1(1'b0), .out(multiplexer_1_out), .sel(in_1));
  Multiplexer #(.select(1), .width(1), .disabled("Z"), .enable("false")) multiplexer_2 (
    .in0(in_3), .in1(1'b0), .out(multiplexer_2_out), .sel(in_1));
  Multiplexer #(.select(1), .width(1), .disabled("Z"), .enable("false")) multiplexer_3 (
    .in0(in_4), .in1(1'b0), .out(multiplexer_3_out), .sel(in_1));
  Multiplexer #(.select(1), .width(1), .disabled("Z"), .enable("false")) multiplexer_4 (
    .in0(in_5), .in1(1'b0), .out(multiplexer_4_out), .sel(in_1));
  Multiplexer #(.select(1), .width(1), .disabled("Z"), .enable("false")) multiplexer_5 (
    .in0(in_6), .in1(1'b0), .out(multiplexer_5_out), .sel(in_1));
  Multiplexer #(.select(1), .width(32), .disabled("Z"), .enable("false")) multiplexer_6 (
    .in0(in_7), .in1({32{1'b0}}), .out(multiplexer_6_out), .sel(in_1));
  Multiplexer #(.select(1), .width(32), .disabled("Z"), .enable("false")) multiplexer_7 (
    .in0(in_8), .in1({32{1'b0}}), .out(multiplexer_7_out), .sel(in_1));
  Multiplexer #(.select(1), .width(5), .disabled("Z"), .enable("false")) multiplexer_8 (
    .in0(in_9), .in1({5{1'b0}}), .out(multiplexer_8_out), .sel(in_1));
  Multiplexer #(.select(1), .width(32), .disabled("Z"), .enable("false")) multiplexer_9 (
    .in0(in_10), .in1({32{1'b0}}), .out(multiplexer_9_out), .sel(in_1));
  Multiplexer #(.select(1), .width(32), .disabled("Z"), .enable("false")) multiplexer_10 (
    .in0(in_11), .in1({32{1'b0}}), .out(multiplexer_10_out), .sel(in_1));
  Multiplexer #(.select(1), .width(32), .disabled("Z"), .enable("false")) multiplexer_11 (
    .in0(in_12), .in1({32{1'b0}}), .out(multiplexer_11_out), .sel(in_1));
  Register #(.width(1), .trigger("rising"), .Select("low")) register_1 (
    .D(multiplexer_1_out), .en(run), .Q(out_15), .clk(CLK));  // open: clr
  Register #(.width(1), .trigger("rising"), .Select("low")) register_2 (
    .D(multiplexer_2_out), .en(run), .Q(out_16), .clk(CLK));  // open: clr
  Register #(.width(1), .trigger("rising"), .Select("low")) register_3 (
    .D(multiplexer_3_out), .en(run), .Q(out_17), .clk(CLK));  // open: clr
  Register #(.width(1), .trigger("rising"), .Select("low")) register_4 (
    .D(multiplexer_4_out), .en(run), .Q(out_18), .clk(CLK));  // open: clr
  Register #(.width(1), .trigger("rising"), .Select("low")) register_5 (
    .D(multiplexer_5_out), .en(run), .Q(out_19), .clk(CLK));  // open: clr
  Register #(.width(32), .trigger("rising"), .Select("low")) register_6 (
    .D(multiplexer_6_out), .en(run), .Q(out_20), .clk(CLK));  // open: clr
  Register #(.width(32), .trigger("rising"), .Select("low")) register_7 (
    .D(multiplexer_7_out), .en(run), .Q(out_21), .clk(CLK));  // open: clr
  Register #(.width(5), .trigger("rising"), .Select("low")) register_8 (
    .D(multiplexer_8_out), .en(run), .Q(out_22), .clk(CLK));  // open: clr
  Register #(.width(32), .trigger("rising"), .Select("low")) register_9 (
    .D(multiplexer_9_out), .en(run), .Q(out_23), .clk(CLK));  // open: clr
  Register #(.width(32), .trigger("rising"), .Select("low")) register_10 (
    .D(multiplexer_10_out), .en(run), .Q(out_24), .clk(CLK));  // open: clr
  Register #(.width(32), .trigger("rising"), .Select("low")) register_11 (
    .D(multiplexer_11_out), .en(run), .Q(out_25), .clk(CLK));  // open: clr
endmodule

module BubbleControl (
  input  halt,
  input  clk,
  input  jal,
  input  jalr,
  input  branch,
  input  [4:0] EXW_num,
  input  EXRW,
  input  in_8,
  input  ecall,
  input  [4:0] MEMW_num,
  input  [31:0] inst,
  input  MEMRW,
  output jal_2,
  output [15:0] \无条件分支 ,
  output jalr_2,
  output branchtaken,
  output [15:0] \条件分支 ,
  output EXflush,
  output stall,
  output [15:0] \气泡 
);

  wire and_1_out, and_2_out, and_3_out, and_4_out, and_5_out, and_6_out, and_8_out, and_9_out, and_10_out,
       comparator_1_eq, comparator_2_eq, comparator_3_eq, comparator_4_eq, comparator_5_eq, comparator_6_eq,
       comparator_7_eq, comparator_8_eq, not_1_out, not_2_out, not_3_out, not_4_out, not_5_out, not_6_out,
       not_7_out, or_1_out, or_2_out, or_4_out, or_5_out;
  wire [4:0] R1_num, R2_num;

  Comparator #(.width(5), .mode("unsigned")) comparator_1 (
    .a(R1_num), .b(EXW_num), .eq(comparator_1_eq));  // open: gt, lt
  Comparator #(.width(5), .mode("unsigned")) comparator_2 (
    .a(R1_num), .b({5{1'b0}}), .eq(comparator_2_eq));  // open: gt, lt
  not not_1 (not_1_out, comparator_2_eq);
  Comparator #(.width(5), .mode("unsigned")) comparator_3 (
    .a(R2_num), .b(EXW_num), .eq(comparator_3_eq));  // open: gt, lt
  not not_2 (not_2_out, comparator_4_eq);
  Comparator #(.width(5), .mode("unsigned")) comparator_4 (
    .a(R2_num), .b({5{1'b0}}), .eq(comparator_4_eq));  // open: gt, lt
  Comparator #(.width(5), .mode("unsigned")) comparator_5 (
    .a(R1_num), .b(MEMW_num), .eq(comparator_5_eq));  // open: gt, lt
  Comparator #(.width(5), .mode("unsigned")) comparator_6 (
    .a(R1_num), .b({5{1'b0}}), .eq(comparator_6_eq));  // open: gt, lt
  not not_3 (not_3_out, comparator_6_eq);
  Comparator #(.width(5), .mode("unsigned")) comparator_7 (
    .a(R2_num), .b(MEMW_num), .eq(comparator_7_eq));  // open: gt, lt
  Comparator #(.width(5), .mode("unsigned")) comparator_8 (
    .a(R2_num), .b({5{1'b0}}), .eq(comparator_8_eq));  // open: gt, lt
  not not_4 (not_4_out, comparator_8_eq);
  and and_1 (and_1_out, comparator_1_eq, not_1_out);
  and and_2 (and_2_out, comparator_3_eq, not_5_out, not_2_out);
  not not_5 (not_5_out, in_8);
  and and_3 (and_3_out, comparator_5_eq, not_3_out);
  and and_4 (and_4_out, comparator_7_eq, not_5_out, not_4_out);
  or or_1 (or_1_out, and_1_out, and_2_out);
  or or_2 (or_2_out, and_3_out, and_4_out);
  and and_5 (and_5_out, or_1_out, EXRW);
  and and_6 (and_6_out, or_2_out, MEMRW);
  or or_3 (branchtaken, jal, jalr, branch);
  or or_4 (or_4_out, and_5_out, and_6_out);
  not not_6 (not_6_out, branchtaken);
  or or_5 (or_5_out, jal, jalr);
  or or_6 (EXflush, branchtaken, or_4_out);
  and and_7 (stall, or_4_out, not_6_out);
  not not_7 (not_7_out, halt);
  and and_8 (and_8_out, or_5_out, not_7_out);
  Counter #(.width(16), .max('hffff), .ongoal("wrap"), .trigger("rising"), .behavior("new")) counter_1 (
    .count(and_8_out), .Q(\无条件分支 ), .clk(clk));  // open: load, D, carry, clr, preset, down
  and and_9 (and_9_out, branch, not_7_out);
  Counter #(.width(16), .max('hffff), .ongoal("wrap"), .trigger("rising"), .behavior("new")) counter_2 (
    .count(and_9_out), .Q(\条件分支 ), .clk(clk));  // open: load, D, carry, clr, preset, down
  and and_10 (and_10_out, or_4_out, not_7_out);
  Counter #(.width(16), .max('hffff), .ongoal("wrap"), .trigger("rising"), .behavior("new")) counter_3 (
    .count(and_10_out), .Q(\气泡 ), .clk(clk));  // open: load, D, carry, clr, preset, down
  Multiplexer #(.select(1), .width(5), .disabled("Z"), .enable("false")) multiplexer_1 (
    .in0(inst[19:15]), .in1(5'b01010), .out(R1_num), .sel(ecall));
  Multiplexer #(.select(1), .width(5), .disabled("Z"), .enable("false")) multiplexer_2 (
    .in0(inst[24:20]), .in1(5'b10001), .out(R2_num), .sel(ecall));

  assign jal_2 = jal;
  assign jalr_2 = jalr;
endmodule

module ReDirectControl (
  input  halt,
  input  ecall,
  input  clk,
  input  [31:0] instr,
  input  jal,
  input  jalr,
  input  branch,
  input  [4:0] mem_W_num,
  input  mem_regwrite,
  input  [4:0] ex_W_num,
  input  ex_regwrite,
  input  ex_toreg,
  input  stype,
  input  alusrc,
  output jal_2,
  output [15:0] \无条件 ,
  output jalr_2,
  output branchtaken,
  output [15:0] \条件 ,
  output [1:0] r1_src,
  output stall,
  output [15:0] \气泡 ,
  output flush2,
  output [15:0] loaduse,
  output [1:0] r2_src
);

  wire and_1_out, and_2_out, and_3_out, and_4_out, and_5_out, and_6_out, and_8_out, and_9_out, and_10_out,
       and_11_out, comparator_1_eq, comparator_2_eq, comparator_3_eq, comparator_4_eq, comparator_5_eq,
       comparator_6_eq, loaduse_t, not_1_out, not_2_out, not_3_out, not_4_out, not_5_out, or_1_out, or_2_out;
  wire [4:0] R1_num, R2_num;

  not not_1 (not_1_out, alusrc);
  or or_1 (or_1_out, stype, not_1_out);
  Multiplexer #(.select(1), .width(5), .disabled("Z"), .enable("false")) multiplexer_1 (
    .in0(instr[19:15]), .in1(5'b01010), .out(R1_num), .sel(ecall));
  Multiplexer #(.select(1), .width(5), .disabled("Z"), .enable("false")) multiplexer_2 (
    .in0(instr[24:20]), .in1(5'b10001), .out(R2_num), .sel(ecall));
  Comparator #(.width(5), .mode("unsigned")) comparator_1 (
    .a(mem_W_num), .b(R1_num), .eq(comparator_1_eq));  // open: gt, lt
  Comparator #(.width(5), .mode("unsigned")) comparator_2 (
    .a(R1_num), .b({5{1'b0}}), .eq(comparator_2_eq));  // open: gt, lt
  Comparator #(.width(5), .mode("unsigned")) comparator_3 (
    .a(R1_num), .b(ex_W_num), .eq(comparator_3_eq));  // open: gt, lt
  Comparator #(.width(5), .mode("unsigned")) comparator_4 (
    .a(R2_num), .b({5{1'b0}}), .eq(comparator_4_eq));  // open: gt, lt
  Comparator #(.width(5), .mode("unsigned")) comparator_5 (
    .a(R2_num), .b(ex_W_num), .eq(comparator_5_eq));  // open: gt, lt
  Comparator #(.width(5), .mode("unsigned")) comparator_6 (
    .a(R2_num), .b(mem_W_num), .eq(comparator_6_eq));  // open: gt, lt
  not not_2 (not_2_out, comparator_2_eq);
  not not_3 (not_3_out, comparator_4_eq);
  and and_1 (and_1_out, mem_regwrite, comparator_1_eq, not_2_out);
  and and_2 (and_2_out, not_2_out, comparator_3_eq, ex_regwrite);
  and and_3 (and_3_out, not_3_out, comparator_5_eq, or_1_out, ex_regwrite);
  and and_4 (and_4_out, not_3_out, or_1_out, mem_regwrite, comparator_6_eq);
  or or_2 (or_2_out, jal, jalr);
  Priority_Encoder #(.select(2), .disabled("Z")) priority_encoder_1 (
    .in0(1'b1), .in1(and_1_out), .in2(and_2_out), .out(r1_src));  // open: in3, gs, en_out, en_in
  and and_5 (and_5_out, not_2_out, comparator_3_eq, ex_toreg);
  and and_6 (and_6_out, not_3_out, comparator_5_eq, ex_toreg, or_1_out);
  Priority_Encoder #(.select(2), .disabled("Z")) priority_encoder_2 (
    .in0(1'b1), .in1(and_4_out), .in2(and_3_out), .out(r2_src));  // open: in3, gs, en_out, en_in
  or or_3 (branchtaken, or_2_out, branch);
  or or_4 (loaduse_t, and_5_out, and_6_out);
  not not_4 (not_4_out, branchtaken);
  and and_7 (stall, not_4_out, loaduse_t);
  or or_5 (flush2, branchtaken, loaduse_t);
  not not_5 (not_5_out, halt);
  and and_8 (and_8_out, or_2_out, not_5_out);
  and and_9 (and_9_out, branch, not_5_out);
  and and_10 (and_10_out, flush2, not_5_out);
  and and_11 (and_11_out, loaduse_t, not_5_out);
  Counter #(.width(16), .max('hffff), .ongoal("wrap"), .trigger("rising"), .behavior("new")) counter_1 (
    .count(and_8_out), .Q(\无条件 ), .clk(clk));  // open: load, D, carry, clr, preset, down
  Counter #(.width(16), .max('hffff), .ongoal("wrap"), .trigger("rising"), .behavior("new")) counter_2 (
    .count(and_9_out), .Q(\条件 ), .clk(clk));  // open: load, D, carry, clr, preset, down
  Counter #(.width(16), .max('hffff), .ongoal("wrap"), .trigger("rising"), .behavior("new")) counter_3 (
    .count(and_10_out), .Q(\气泡 ), .clk(clk));  // open: load, D, carry, clr, preset, down
  Counter #(.width(16), .max('hffff), .ongoal("wrap"), .trigger("rising"), .behavior("new")) counter_4 (
    .count(and_11_out), .Q(loaduse), .clk(clk));  // open: load, D, carry, clr, preset, down

  assign jal_2 = jal;
  assign jalr_2 = jalr;
endmodule

module BTB (
  input  [31:0] EX_PC,
  input  [31:0] EX_B_dest,
  input  EX_branch,
  input  [31:0] PC,
  input  CLK,
  input  EX_branchtaken,
  input  [1:0] init,
  output [31:0] jump_addr,
  output predict_jump
);

  wire and_19_out, and_20_out, and_21_out, and_22_out, comparator_1_eq, comparator_2_eq, comparator_3_eq,
       comparator_4_eq, comparator_5_eq, comparator_6_eq, comparator_7_eq, comparator_8_eq, comparator_9_eq,
       comparator_10_eq, comparator_11_eq, comparator_12_eq, comparator_13_eq, comparator_14_eq,
       comparator_15_eq, comparator_16_eq, d_ff_1_q, d_ff_2_q, d_ff_3_q, d_ff_4_q, d_ff_5_q, d_ff_6_q,
       d_ff_7_q, d_ff_8_q, decoder_1_out2, decoder_1_out3, decoder_2_out0, decoder_2_out1, decoder_2_out2,
       decoder_2_out3, decoder_2_out4, decoder_2_out5, decoder_2_out6, decoder_2_out7, init0, init1, init2,
       init3, init4, init5, init6, init7, missing, nor_1_out, not_1_out, not_2_out, not_3_out, not_4_out,
       not_5_out, not_6_out, not_7_out, not_8_out, not_9_out, not_10_out, not_11_out, not_12_out, not_13_out,
       or_1_out, or_2_out, or_3_out, or_4_out, or_5_out, or_6_out, or_7_out, or_8_out, or_9_out, or_10_out,
       or_11_out, or_12_out, or_13_out, or_14_out, or_15_out, or_16_out, or_17_out, or_18_out,
       priority_encoder_1_gs, read0, read1, read2, read3, read4, read5, read6, read7, v0, v1, v2, v3, v4, v5,
       v6, v7, write0, write1, write2, write3, write4, write5, write6, write7;
  wire [1:0] if_pred, multiplexer_1_out, pred_now, pred_nxt, register_25_q, register_26_q, register_27_q,
       register_28_q, register_29_q, register_30_q, register_31_q, register_32_q;
  wire [2:0] max3_1_max_num, max3_2_max_num, max3_3_max_num, max3_4_max_num, max3_5_max_num, max3_6_max_num,
       max3_7_max_num, multiplexer_2_out, priority_encoder_1_out, subtractor_1_out;
  wire [31:0] c0, c1, c2, c3, c4, c5, c6, c7, max3_1_max, max3_2_max, max3_3_max, max3_4_max, max3_5_max,
       max3_6_max, pc0, pc1, pc2, pc3, pc4, pc5, pc6, pc7, register_17_q, register_18_q, register_19_q,
       register_20_q, register_21_q, register_22_q, register_23_q, register_24_q;

  Register #(.width(1), .trigger("rising"), .Select("low")) register_1 (
    .D(1'b1), .en(init0), .Q(v0), .clk(CLK));  // open: clr
  Register #(.width(1), .trigger("rising"), .Select("low")) register_2 (
    .D(1'b1), .en(init1), .Q(v1), .clk(CLK));  // open: clr
  Register #(.width(1), .trigger("rising"), .Select("low")) register_3 (
    .D(1'b1), .en(init2), .Q(v2), .clk(CLK));  // open: clr
  Register #(.width(1), .trigger("rising"), .Select("low")) register_4 (
    .D(1'b1), .en(init3), .Q(v3), .clk(CLK));  // open: clr
  Register #(.width(1), .trigger("rising"), .Select("low")) register_5 (
    .D(1'b1), .en(init4), .Q(v4), .clk(CLK));  // open: clr
  Register #(.width(1), .trigger("rising"), .Select("low")) register_6 (
    .D(1'b1), .en(init5), .Q(v5), .clk(CLK));  // open: clr
  Register #(.width(1), .trigger("rising"), .Select("low")) register_7 (
    .D(1'b1), .en(init6), .Q(v6), .clk(CLK));  // open: clr
  Register #(.width(1), .trigger("rising"), .Select("low")) register_8 (
    .D(1'b1), .en(init7), .Q(v7), .clk(CLK));  // open: clr
  Register #(.width(32), .trigger("rising"), .Select("low")) register_9 (
    .D(EX_PC), .en(init0), .Q(pc0), .clk(CLK));  // open: clr
  Register #(.width(32), .trigger("rising"), .Select("low")) register_10 (
    .D(EX_PC), .en(init1), .Q(pc1), .clk(CLK));  // open: clr
  Register #(.width(32), .trigger("rising"), .Select("low")) register_11 (
    .D(EX_PC), .en(init2), .Q(pc2), .clk(CLK));  // open: clr
  Register #(.width(32), .trigger("rising"), .Select("low")) register_12 (
    .D(EX_PC), .en(init3), .Q(pc3), .clk(CLK));  // open: clr
  Register #(.width(32), .trigger("rising"), .Select("low")) register_13 (
    .D(EX_PC), .en(init4), .Q(pc4), .clk(CLK));  // open: clr
  Register #(.width(32), .trigger("rising"), .Select("low")) register_14 (
    .D(EX_PC), .en(init5), .Q(pc5), .clk(CLK));  // open: clr
  Register #(.width(32), .trigger("rising"), .Select("low")) register_15 (
    .D(EX_PC), .en(init6), .Q(pc6), .clk(CLK));  // open: clr
  Register #(.width(32), .trigger("rising"), .Select("low")) register_16 (
    .D(EX_PC), .en(init7), .Q(pc7), .clk(CLK));  // open: clr
  D_Flip_Flop #(.trigger("rising"), .Pre_Clr_Positions("LEGACY"), .NegatePresetClear("false"), .enable("true"), .NewFFLayout("false")) d_ff_1 (
    .clk(CLK), .D(or_1_out), .Q(d_ff_1_q));  // open: Qn, preset, en, reset
  or or_1 (or_1_out, init0, read0);
  D_Flip_Flop #(.trigger("rising"), .Pre_Clr_Positions("LEGACY"), .NegatePresetClear("false"), .enable("true"), .NewFFLayout("false")) d_ff_2 (
    .clk(CLK), .D(or_2_out), .Q(d_ff_2_q));  // open: Qn, preset, en, reset
  or or_2 (or_2_out, init1, read1);
  D_Flip_Flop #(.trigger("rising"), .Pre_Clr_Positions("LEGACY"), .NegatePresetClear("false"), .enable("true"), .NewFFLayout("false")) d_ff_3 (
    .clk(CLK), .D(or_3_out), .Q(d_ff_3_q));  // open: Qn, preset, en, reset
  or or_3 (or_3_out, CLK, init2);
  D_Flip_Flop #(.trigger("rising"), .Pre_Clr_Positions("LEGACY"), .NegatePresetClear("false"), .enable("true"), .NewFFLayout("false")) d_ff_4 (
    .clk(CLK), .D(or_4_out), .Q(d_ff_4_q));  // open: Qn, preset, en, reset
  or or_4 (or_4_out, CLK, init3);
  D_Flip_Flop #(.trigger("rising"), .Pre_Clr_Positions("LEGACY"), .NegatePresetClear("false"), .enable("true"), .NewFFLayout("false")) d_ff_5 (
    .clk(CLK), .D(or_5_out), .Q(d_ff_5_q));  // open: Qn, preset, en, reset
  or or_5 (or_5_out, CLK, init4);
  D_Flip_Flop #(.trigger("rising"), .Pre_Clr_Positions("LEGACY"), .NegatePresetClear("false"), .enable("true"), .NewFFLayout("false")) d_ff_6 (
    .clk(CLK), .D(or_6_out), .Q(d_ff_6_q));  // open: Qn, preset, en, reset
  or or_6 (or_6_out, CLK, init5);
  D_Flip_Flop #(.trigger("rising"), .Pre_Clr_Positions("LEGACY"), .NegatePresetClear("false"), .enable("true"), .NewFFLayout("false")) d_ff_7 (
    .clk(CLK), .D(or_7_out), .Q(d_ff_7_q));  // open: Qn, preset, en, reset
  or or_7 (or_7_out, CLK, init6);
  D_Flip_Flop #(.trigger("rising"), .Pre_Clr_Positions("LEGACY"), .NegatePresetClear("false"), .enable("true"), .NewFFLayout("false")) d_ff_8 (
    .clk(CLK), .D(or_8_out), .Q(d_ff_8_q));  // open: Qn, preset, en, reset
  or or_8 (or_8_out, CLK, init7);
  Counter #(.width(32), .max('hffffffff), .ongoal("wrap"), .trigger("rising"), .behavior("new")) counter_1 (
    .Q(c0), .clk(CLK), .clr(d_ff_1_q));  // open: load, D, count, carry, preset, down
  Counter #(.width(32), .max('hffffffff), .ongoal("wrap"), .trigger("rising"), .behavior("new")) counter_2 (
    .Q(c1), .clk(CLK), .clr(d_ff_2_q));  // open: load, D, count, carry, preset, down
  Counter #(.width(32), .max('hffffffff), .ongoal("wrap"), .trigger("rising"), .behavior("new")) counter_3 (
    .Q(c2), .clk(CLK), .clr(d_ff_3_q));  // open: load, D, count, carry, preset, down
  Counter #(.width(32), .max('hffffffff), .ongoal("wrap"), .trigger("rising"), .behavior("new")) counter_4 (
    .Q(c3), .clk(CLK), .clr(d_ff_4_q));  // open: load, D, count, carry, preset, down
  Counter #(.width(32), .max('hffffffff), .ongoal("wrap"), .trigger("rising"), .behavior("new")) counter_5 (
    .Q(c4), .clk(CLK), .clr(d_ff_5_q));  // open: load, D, count, carry, preset, down
  Counter #(.width(32), .max('hffffffff), .ongoal("wrap"), .trigger("rising"), .behavior("new")) counter_6 (
    .Q(c5), .clk(CLK), .clr(d_ff_6_q));  // open: load, D, count, carry, preset, down
  Counter #(.width(32), .max('hffffffff), .ongoal("wrap"), .trigger("rising"), .behavior("new")) counter_7 (
    .Q(c6), .clk(CLK), .clr(d_ff_7_q));  // open: load, D, count, carry, preset, down
  Counter #(.width(32), .max('hffffffff), .ongoal("wrap"), .trigger("rising"), .behavior("new")) counter_8 (
    .Q(c7), .clk(CLK), .clr(d_ff_8_q));  // open: load, D, count, carry, preset, down
  Register #(.width(32), .trigger("rising"), .Select("low")) register_17 (
    .D(EX_B_dest), .en(init0), .Q(register_17_q), .clk(CLK));  // open: clr
  assign jump_addr = read0 ? register_17_q : 32'bz;  // Controlled_Buffer controlled_buffer_1
  assign jump_addr = read1 ? register_18_q : 32'bz;  // Controlled_Buffer controlled_buffer_2
  Register #(.width(32), .trigger("rising"), .Select("low")) register_18 (
    .D(EX_B_dest), .en(init1), .Q(register_18_q), .clk(CLK));  // open: clr
  Register #(.width(32), .trigger("rising"), .Select("low")) register_19 (
    .D(EX_B_dest), .en(init2), .Q(register_19_q), .clk(CLK));  // open: clr
  assign jump_addr = read2 ? register_19_q : 32'bz;  // Controlled_Buffer controlled_buffer_3
  assign jump_addr = read3 ? register_20_q : 32'bz;  // Controlled_Buffer controlled_buffer_4
  Register #(.width(32), .trigger("rising"), .Select("low")) register_20 (
    .D(EX_B_dest), .en(init3), .Q(register_20_q), .clk(CLK));  // open: clr
  assign jump_addr = read4 ? register_21_q : 32'bz;  // Controlled_Buffer controlled_buffer_5
  Register #(.width(32), .trigger("rising"), .Select("low")) register_21 (
    .D(EX_B_dest), .en(init4), .Q(register_21_q), .clk(CLK));  // open: clr
  Register #(.width(32), .trigger("rising"), .Select("low")) register_22 (
    .D(EX_B_dest), .en(init5), .Q(register_22_q), .clk(CLK));  // open: clr
  assign jump_addr = read5 ? register_22_q : 32'bz;  // Controlled_Buffer controlled_buffer_6
  assign jump_addr = read6 ? register_23_q : 32'bz;  // Controlled_Buffer controlled_buffer_7
  Register #(.width(32), .trigger("rising"), .Select("low")) register_23 (
    .D(EX_B_dest), .en(init6), .Q(register_23_q), .clk(CLK));  // open: clr
  assign jump_addr = read7 ? register_24_q : 32'bz;  // Controlled_Buffer controlled_buffer_8
  Register #(.width(32), .trigger("rising"), .Select("low")) register_24 (
    .D(EX_B_dest), .en(init7), .Q(register_24_q), .clk(CLK));  // open: clr
  or or_9 (or_9_out, write0, init0);
  or or_10 (or_10_out, write1, init1);
  or or_11 (or_11_out, write2, init2);
  or or_12 (or_12_out, write3, init3);
  or or_13 (or_13_out, write4, init4);
  or or_14 (or_14_out, write5, init5);
  or or_15 (or_15_out, write6, init6);
  or or_16 (or_16_out, write7, init7);
  Register #(.width(2), .trigger("rising"), .Select("low")) register_25 (
    .D(pred_nxt), .en(or_9_out), .Q(register_25_q), .clk(CLK));  // open: clr
  Register #(.width(2), .trigger("rising"), .Select("low")) register_26 (
    .D(pred_nxt), .en(or_10_out), .Q(register_26_q), .clk(CLK));  // open: clr
  Register #(.width(2), .trigger("rising"), .Select("low")) register_27 (
    .D(pred_nxt), .en(or_11_out), .Q(register_27_q), .clk(CLK));  // open: clr
  Register #(.width(2), .trigger("rising"), .Select("low")) register_28 (
    .D(pred_nxt), .en(or_12_out), .Q(register_28_q), .clk(CLK));  // open: clr
  Register #(.width(2), .trigger("rising"), .Select("low")) register_29 (
    .D(pred_nxt), .en(or_13_out), .Q(register_29_q), .clk(CLK));  // open: clr
  Register #(.width(2), .trigger("rising"), .Select("low")) register_30 (
    .D(pred_nxt), .en(or_14_out), .Q(register_30_q), .clk(CLK));  // open: clr
  Register #(.width(2), .trigger("rising"), .Select("low")) register_31 (
    .D(pred_nxt), .en(or_15_out), .Q(register_31_q), .clk(CLK));  // open: clr
  Register #(.width(2), .trigger("rising"), .Select("low")) register_32 (
    .D(pred_nxt), .en(or_16_out), .Q(register_32_q), .clk(CLK));  // open: clr
  assign pred_now = write0 ? register_25_q : 2'bz;  // Controlled_Buffer controlled_buffer_9
  assign if_pred = read0 ? register_25_q : 2'bz;  // Controlled_Buffer controlled_buffer_10
  assign pred_now = write1 ? register_26_q : 2'bz;  // Controlled_Buffer controlled_buffer_11
  assign if_pred = read1 ? register_26_q : 2'bz;  // Controlled_Buffer controlled_buffer_12
  assign pred_now = write2 ? register_27_q : 2'bz;  // Controlled_Buffer controlled_buffer_13
  assign if_pred = read2 ? register_27_q : 2'bz;  // Controlled_Buffer controlled_buffer_14
  assign pred_now = write3 ? register_28_q : 2'bz;  // Controlled_Buffer controlled_buffer_15
  assign if_pred = read3 ? register_28_q : 2'bz;  // Controlled_Buffer controlled_buffer_16
  assign pred_now = write4 ? register_29_q : 2'bz;  // Controlled_Buffer controlled_buffer_17
  assign if_pred = read4 ? register_29_q : 2'bz;  // Controlled_Buffer controlled_buffer_18
  assign pred_now = write5 ? register_30_q : 2'bz;  // Controlled_Buffer controlled_buffer_19
  assign if_pred = read5 ? register_30_q : 2'bz;  // Controlled_Buffer controlled_buffer_20
  assign pred_now = write6 ? register_31_q : 2'bz;  // Controlled_Buffer controlled_buffer_21
  assign if_pred = read6 ? register_31_q : 2'bz;  // Controlled_Buffer controlled_buffer_22
  assign pred_now = write7 ? register_32_q : 2'bz;  // Controlled_Buffer controlled_buffer_23
  assign if_pred = read7 ? register_32_q : 2'bz;  // Controlled_Buffer controlled_buffer_24
  Comparator #(.width(32), .mode("unsigned")) comparator_1 (.a(PC), .b(pc0), .eq(comparator_1_eq));  // open: gt, lt
  Comparator #(.width(32), .mode("unsigned")) comparator_2 (.a(EX_PC), .b(pc0), .eq(comparator_2_eq));  // open: gt, lt
  Comparator #(.width(32), .mode("unsigned")) comparator_3 (.a(PC), .b(pc1), .eq(comparator_3_eq));  // open: gt, lt
  Comparator #(.width(32), .mode("unsigned")) comparator_4 (.a(EX_PC), .b(pc1), .eq(comparator_4_eq));  // open: gt, lt
  Comparator #(.width(32), .mode("unsigned")) comparator_5 (.a(PC), .b(pc2), .eq(comparator_5_eq));  // open: gt, lt
  Comparator #(.width(32), .mode("unsigned")) comparator_6 (.a(EX_PC), .b(pc2), .eq(comparator_6_eq));  // open: gt, lt
  Comparator #(.width(32), .mode("unsigned")) comparator_7 (.a(PC), .b(pc3), .eq(comparator_7_eq));  // open: gt, lt
  Comparator #(.width(32), .mode("unsigned")) comparator_8 (.a(EX_PC), .b(pc3), .eq(comparator_8_eq));  // open: gt, lt
  Comparator #(.width(32), .mode("unsigned")) comparator_9 (.a(PC), .b(pc4), .eq(comparator_9_eq));  // open: gt, lt
  Comparator #(.width(32), .mode("unsigned")) comparator_10 (
    .a(EX_PC), .b(pc4), .eq(comparator_10_eq));  // open: gt, lt
  Comparator #(.width(32), .mode("unsigned")) comparator_11 (.a(PC), .b(pc5), .eq(comparator_11_eq));  // open: gt, lt
  Comparator #(.width(32), .mode("unsigned")) comparator_12 (
    .a(EX_PC), .b(pc5), .eq(comparator_12_eq));  // open: gt, lt
  Comparator #(.width(32), .mode("unsigned")) comparator_13 (.a(PC), .b(pc6), .eq(comparator_13_eq));  // open: gt, lt
  Comparator #(.width(32), .mode("unsigned")) comparator_14 (
    .a(EX_PC), .b(pc6), .eq(comparator_14_eq));  // open: gt, lt
  Comparator #(.width(32), .mode("unsigned")) comparator_15 (.a(PC), .b(pc7), .eq(comparator_15_eq));  // open: gt, lt
  Comparator #(.width(32), .mode("unsigned")) comparator_16 (
    .a(EX_PC), .b(pc7), .eq(comparator_16_eq));  // open: gt, lt
  and and_1 (read0, comparator_1_eq, v0);
  and and_2 (write0, comparator_2_eq, EX_branch, v0);
  and and_3 (read1, comparator_3_eq, v1);
  and and_4 (write1, comparator_4_eq, EX_branch, v1);
  and and_5 (read2, comparator_5_eq, v2);
  and and_6 (write2, comparator_6_eq, EX_branch, v2);
  and and_7 (read3, comparator_7_eq, v3);
  and and_8 (write3, comparator_8_eq, EX_branch, v3);
  and and_9 (read4, comparator_9_eq, v4);
  and and_10 (write4, comparator_10_eq, EX_branch, v4);
  and and_11 (read5, comparator_11_eq, v5);
  and and_12 (write5, comparator_12_eq, EX_branch, v5);
  and and_13 (read6, comparator_13_eq, v6);
  and and_14 (write6, comparator_14_eq, EX_branch, v6);
  and and_15 (read7, comparator_15_eq, v7);
  and and_16 (write7, comparator_16_eq, EX_branch, v7);
  Decoder #(.select(2), .tristate("false"), .disabled("Z"), .enable("false")) decoder_1 (
    .out2(decoder_1_out2), .out3(decoder_1_out3), .sel(if_pred));  // open: out0, out1
  max3 max3_1 (.Y(c1), .X(c0), .Y_num(3'b001), .X_num(3'b000), .MAX(max3_1_max), .Max_num(max3_1_max_num));
  max3 max3_2 (.Y(c3), .X(c2), .Y_num(3'b011), .X_num(3'b010), .MAX(max3_2_max), .Max_num(max3_2_max_num));
  max3 max3_3 (.Y(c5), .X(c4), .Y_num(3'b101), .X_num(3'b100), .MAX(max3_3_max), .Max_num(max3_3_max_num));
  max3 max3_4 (.Y(c7), .X(c6), .Y_num(3'b111), .X_num(3'b110), .MAX(max3_4_max), .Max_num(max3_4_max_num));
  not not_1 (not_1_out, v7);
  not not_2 (not_2_out, v6);
  not not_3 (not_3_out, v5);
  not not_4 (not_4_out, v4);
  not not_5 (not_5_out, v3);
  not not_6 (not_6_out, v2);
  not not_7 (not_7_out, v1);
  not not_8 (not_8_out, v0);
  or or_17 (or_17_out, decoder_1_out2, decoder_1_out3);
  or or_18 (or_18_out, read0, read1, read2, read3, read4, read5, read6, read7);
  nor nor_1 (nor_1_out, write0, write1, write2, write3, write4, write5, write6, write7);
  max3 max3_5 (
    .Y(max3_2_max), .X(max3_1_max), .Y_num(max3_2_max_num), .X_num(max3_1_max_num), .MAX(max3_5_max),
    .Max_num(max3_5_max_num));
  max3 max3_6 (
    .Y(max3_4_max), .X(max3_3_max), .Y_num(max3_4_max_num), .X_num(max3_3_max_num), .MAX(max3_6_max),
    .Max_num(max3_6_max_num));
  Priority_Encoder #(.select(3), .disabled("Z")) priority_encoder_1 (
    .in0(not_1_out), .in1(not_2_out), .in2(not_3_out), .in3(not_4_out), .in4(not_5_out), .in5(not_6_out),
    .in6(not_7_out), .in7(not_8_out), .out(priority_encoder_1_out), .gs(priority_encoder_1_gs));  // open: en_out, en_in
  Multiplexer #(.select(1), .width(2), .disabled("Z"), .enable("false")) multiplexer_1 (
    .in0(pred_now), .in1(init), .out(multiplexer_1_out), .sel(missing));
  and and_17 (predict_jump, or_17_out, or_18_out);
  and and_18 (missing, EX_branch, nor_1_out);
  max3 max3_7 (
    .Y(max3_6_max), .X(max3_5_max), .Y_num(max3_6_max_num), .X_num(max3_5_max_num), .Max_num(max3_7_max_num));  // open: MAX
  Subtractor #(.width(3)) subtractor_1 (
    .a(3'b111), .b(priority_encoder_1_out), .out(subtractor_1_out));  // open: bin, bout
  and and_19 (and_19_out, EX_branchtaken, multiplexer_1_out[0]);
  not not_9 (not_9_out, multiplexer_1_out[0]);
  and and_20 (and_20_out, not_9_out, multiplexer_1_out[1]);
  not not_10 (not_10_out, multiplexer_1_out[0]);
  not not_11 (not_11_out, multiplexer_1_out[1]);
  and and_21 (and_21_out, not_10_out, not_11_out, EX_branchtaken);
  not not_12 (not_12_out, multiplexer_1_out[0]);
  and and_22 (and_22_out, not_12_out, multiplexer_1_out[1], not_13_out);
  not not_13 (not_13_out, EX_branchtaken);
  Decoder #(.select(3), .tristate("false"), .disabled("Z"), .enable("false")) decoder_2 (
    .out0(decoder_2_out0), .out1(decoder_2_out1), .out2(decoder_2_out2), .out3(decoder_2_out3),
    .out4(decoder_2_out4), .out5(decoder_2_out5), .out6(decoder_2_out6), .out7(decoder_2_out7),
    .sel(multiplexer_2_out));
  Multiplexer #(.select(1), .width(3), .disabled("Z"), .enable("false")) multiplexer_2 (
    .in0(max3_7_max_num), .in1(subtractor_1_out), .out(multiplexer_2_out), .sel(priority_encoder_1_gs));
  or or_19 (pred_nxt[1], and_19_out, and_20_out);
  or or_20 (pred_nxt[0], and_21_out, and_22_out);
  and and_23 (init0, decoder_2_out0, missing);
  and and_24 (init1, decoder_2_out1, missing);
  and and_25 (init2, decoder_2_out2, missing);
  and and_26 (init3, decoder_2_out3, missing);
  and and_27 (init4, decoder_2_out4, missing);
  and and_28 (init5, decoder_2_out5, missing);
  and and_29 (init6, decoder_2_out6, missing);
  and and_30 (init7, decoder_2_out7, missing);
endmodule

module max3 (
  input  [31:0] Y,
  input  [31:0] X,
  input  [2:0] Y_num,
  input  [2:0] X_num,
  output [31:0] MAX,
  output [2:0] Max_num
);

  wire comparator_1_eq, comparator_1_gt, or_1_out;

  Multiplexer #(.select(1), .width(32), .disabled("Z"), .enable("false")) multiplexer_1 (
    .in0(Y), .in1(X), .out(MAX), .sel(or_1_out));
  Comparator #(.width(32), .mode("unsigned")) comparator_1 (
    .a(X), .b(Y), .gt(comparator_1_gt), .eq(comparator_1_eq));  // open: lt
  or or_1 (or_1_out, comparator_1_gt, comparator_1_eq);
  Multiplexer #(.select(1), .width(3), .disabled("Z"), .enable("false")) multiplexer_2 (
    .in0(Y_num), .in1(X_num), .out(Max_num), .sel(or_1_out));

  // Notes on the sheet:
  //   输出两个输入中的较大值，并输出较大值的3位编号
endmodule

module error1 (
  input  clr,
  input  in,
  input  clk,
  output out
);

  wire d_ff_1_q;

  D_Flip_Flop #(.trigger("rising"), .Pre_Clr_Positions("ABOVE_BELOW"), .NegatePresetClear("false"), .enable("false"), .NewFFLayout("true")) d_ff_1 (
    .clk(clk), .D(clr), .Q(d_ff_1_q));  // open: Qn, preset, reset
  Register #(.width(1), .trigger("rising"), .Select("low")) register_1 (
    .D(in), .Q(out), .clk(clk), .clr(d_ff_1_q));  // open: en
endmodule
